// Logisim project G6A-Risc.circ as structural Verilog: 34 circuits, main circuit REG16Bit
module Main (
  input  RUN,
  output out_2,
  output out_3,
  output out_4,
  output out_5,
  output [15:0] out_6,
  output [15:0] out_7,
  output [15:0] out_8,
  output [15:0] out_9,
  output [15:0] A,
  output [15:0] B,
  output [15:0] out_12,
  output [15:0] out_13,
  output [15:0] out_14,
  output [15:0] out_15,
  output [15:0] out_16,
  output [15:0] out_17,
  output [15:0] out_18,
  output [15:0] Inc,
  output [10:0] out_20,
  output [15:0] PC,
  output [15:0] out_22,
  output [15:0] out_23
);

  wire A_ADD, A_AND, A_C, A_C1, A_D6_minus, A_D6_plus, A_LDA, A_LDB, A_OR, A_RSB, A_SELF, A_SELT, A_SUB,
       A_WiF, A_WiT, A_XOR, alu16bit_1_cout, alu16bit_1_nt_2, alu16bit_1_nw, alu16bit_1_nz, and_1_out,
       buffer1_1_out_2, buffer1_2_out_2, buffer1_3_out_2, buffer1_4_out_2, buffer_1_out, buffer_2_out,
       buffer_3_out, buffer_4_out, clock_1_out, CLR1, CLR2, HLT, IE_D, IE_LK, IE_MAR, IE_PFR, IE_R0, IE_R1,
       IE_R2, IE_R3, IE_R4, IE_R5, IE_R6, IE_R7, instfielddecoder_1_st, LDPM, not_1_out, OE_M, PH0, PH1, PH2,
       S_BUS, S_D, S_IMM, S_P, S_ROT, S_SL1, S_SL4, S_SR1, S_SR4, S_ZERO, SA_R0, SA_R1, SA_R2, SA_R3, SA_R4,
       SA_R5, SA_R6, SA_R7, SB_R0, SB_R1, SB_R2, SB_R3, SB_R4, SB_R5, SB_R6, SB_R7, shift_1_csh, shift_1_sh,
       SR_c_2, SR_nt_2, SR_nz_2, STEP_out, WE_M, WI_R, WI_SR;
  wire [1:0] instfielddecoder_1_fn, instfielddecoder_1_ty;
  wire [2:0] ALUR_nt_2, instfielddecoder_1_op, instfielddecoder_1_ri, instfielddecoder_1_rj,
       instfielddecoder_1_rk;
  wire [3:0] ALUR_rr_2, RR, RRsh;
  wire [7:0] A_CC;
  wire [10:0] Imm11;
  wire [15:0] alu16bit_1_o, ALUR_out, buffer16_1_out_2, buffer16_2_out_2, buffer16_3_out_2, IR_out, MAR_out,
       or16_1_q, R0_out, R1_out, R2_out, R3_out, R4_A0_out, R5_A1_out, R6_A2_out, R7_PC_out, S0_b, S4_b;

  Button STEP (.out(STEP_out));
  Buffer16 buffer16_1 (.in_1(R7_PC_out), .out_2(buffer16_1_out_2));
  REG16Bit R0 (.IE(IE_R0), .OE(1'b1), .In(ALUR_out), .Test(out_6), .CLR(CLR2), .Out(R0_out), .nWE(WI_R));
  REG16Bit R1 (.IE(IE_R1), .OE(1'b1), .In(ALUR_out), .Test(out_8), .CLR(CLR2), .Out(R1_out), .nWE(WI_R));
  REG16Bit R2 (.IE(IE_R2), .OE(1'b1), .In(ALUR_out), .Test(out_9), .CLR(CLR2), .Out(R2_out), .nWE(WI_R));
  REG16Bit R3 (.IE(IE_R3), .OE(1'b1), .In(ALUR_out), .Test(out_12), .CLR(CLR2), .Out(R3_out), .nWE(WI_R));
  REG16Bit R4_A0 (.IE(IE_R4), .OE(1'b1), .In(ALUR_out), .Test(out_13), .CLR(CLR2), .Out(R4_A0_out), .nWE(WI_R));
  REG16Bit R5_A1 (.IE(IE_R5), .OE(1'b1), .In(ALUR_out), .Test(out_16), .CLR(CLR2), .Out(R5_A1_out), .nWE(WI_R));
  REG_LINK R6_A2 (
    .IElk(IE_LK), .CLR(CLR2), .OE(1'b1), .InLK(Inc), .In(ALUR_out), .Out(R6_A2_out), .Test(out_17),
    .CLRlk(CLR1), .nWE(WI_R), .IE(IE_R6));
  REG_PC R7_PC (
    .OE(1'b1), .In(ALUR_out), .CLR1(CLR1), .Out(R7_PC_out), .Test(PC), .PH1(PH1), .PH(PH2), .nWE(WI_R),
    .IE(IE_R7), .CLR(CLR2), .Out_plus(Inc), .nWE1(LDPM));
  ROM #(.addrWidth(16), .dataWidth(16)) rom_1 (.addr(buffer16_1_out_2), .data(out_23), .sel(1'b1));
  Clock_part clock_1 (.out(clock_1_out));
  Sequencer sequencer_1 (
    .CLKIn(clock_1_out), .PH1(PH1), .CLR1(CLR1), .RUN(RUN), .Test(out_2), .Test_3(out_4), .Test_2(out_3),
    .Test_4(out_5), .PH2(PH2), .CLR2(CLR2), .PH0(PH0), .HLT(HLT), .Step(STEP_out));
  BusSelect S0 (.SA(SA_R0), .SB(SB_R0), .I1(R0_out), .A(A), .B(S0_b));
  BusSelect S1 (.SA(SA_R1), .SB(SB_R1), .I1(R1_out), .A(A), .B(S0_b));
  BusSelect S2 (.SA(SA_R2), .SB(SB_R2), .I1(R2_out), .A(A), .B(S0_b));
  BusSelect S3 (.SA(SA_R3), .SB(SB_R3), .I1(R3_out), .A(A), .B(S0_b));
  BusSelect S4 (.SA(SA_R4), .SB(SB_R4), .I1(R4_A0_out), .A(A), .B(S4_b));
  BusSelect S5 (.SA(SA_R5), .SB(SB_R5), .I1(R5_A1_out), .A(A), .B(S4_b));
  BusSelect S6 (.SA(SA_R6), .SB(SB_R6), .I1(R6_A2_out), .A(A), .B(S4_b));
  BusSelect S7 (.SA(SA_R7), .SB(SB_R7), .I1(R7_PC_out), .A(A), .B(S4_b));
  Transceiver transceiver_1 (.S0(S_P), .I0(out_23), .O0(S4_b));  // open: S1, I1, O1
  OR16 or16_1 (.I(S4_b), .Imm(out_18), .Q(or16_1_q));
  Buffer1 buffer1_1 (.in_1(WI_R), .out_2(buffer1_1_out_2));
  Buffer1 buffer1_2 (.in_1(WE_M), .out_2(buffer1_2_out_2));
  Buffer1 buffer1_3 (.in_1(CLR2), .out_2(buffer1_3_out_2));
  REG_STATUS SR (
    .IE(PH2), .CLR(CLR2), .OE(1'b1), .NZ(ALUR_nt_2[1]), .C(ALUR_nt_2[2]), .NT(ALUR_nt_2[0]), .NZ_2(SR_nz_2),
    .C_2(SR_c_2), .NT_2(SR_nt_2), .nWE(WI_SR), .RR(ALUR_rr_2), .RR_2(RR));
  SHIFT shift_1 (
    .SHR1(S_SR1), .SHL1(S_SL1), .B(S0_b), .RR(RR), .SHR4(S_SR4), .SHL4(S_SL4), .Csh(shift_1_csh), .O(B),
    .Sh(shift_1_sh), .ROT(S_ROT), .RR_2(RRsh));  // open: ZERO
  not not_1 (not_1_out, buffer1_1_out_2);
  REG_PFIX reg_pfix_1 (.IE(IE_PFR), .CLR(CLR2), .OE(1'b1), .In(Imm11), .Out(out_18[15:5]), .Test(out_20));
  REG16Bit IR (.IE(PH0), .OE(1'b1), .In(out_23), .Test(out_22), .CLR(CLR1), .Out(IR_out), .nWE(LDPM));
  InputSelect inputselect_1 (.EN1(S_BUS), .I1(S4_b), .I0(or16_1_q), .A(S0_b), .EN0(S_IMM));
  buf buffer_1 (buffer_1_out, buffer_2_out);
  buf buffer_2 (buffer_2_out, and_1_out);
  and and_1 (and_1_out, not_1_out, buffer1_2_out_2, buffer1_3_out_2);
  REG16Bit MAR (.IE(PH0), .OE(1'b1), .In(or16_1_q), .Test(out_14), .CLR(CLR1), .Out(MAR_out));  // open: nWE
  Buffer16 buffer16_2 (.in_1(MAR_out), .out_2(buffer16_2_out_2));
  buf buffer_3 (buffer_3_out, buffer_1_out);
  buf buffer_4 (buffer_4_out, buffer_3_out);
  InstFieldDecoder instfielddecoder_1 (
    .I(IR_out), .Op(instfielddecoder_1_op), .FN(instfielddecoder_1_fn), .Ri(instfielddecoder_1_ri),
    .imm5(out_18[4:0]), .pfix11(Imm11), .Ty(instfielddecoder_1_ty), .St(instfielddecoder_1_st),
    .Rj(instfielddecoder_1_rj), .Rk(instfielddecoder_1_rk));
  Buffer16 buffer16_3 (.in_1(ALUR_out), .out_2(buffer16_3_out_2));
  Buffer1 buffer1_4 (.in_1(OE_M), .out_2(buffer1_4_out_2));
  ALU16Bit alu16bit_1 (
    .And(A_AND), .Or(A_OR), .Xor(A_XOR), .Add(A_ADD), .Sub(A_SUB), .Rsb(A_RSB), .CIn(SR_c_2), .A(A), .B(B),
    .Cout(alu16bit_1_cout), .O(alu16bit_1_o), .LdA(A_LDA), .LdB(A_LDB), .NZIn(SR_nz_2), .CC_8(A_CC),
    .NT_2(alu16bit_1_nt_2), .NZ(alu16bit_1_nz), .NT(SR_nt_2), .SelT(A_SELT), .SH(shift_1_sh),
    .Csh(shift_1_csh), .SelF(A_SELF), .A_C(A_C), .A_C1(A_C1), .A_D6_plus(A_D6_plus), .A_D6_minus(A_D6_minus),
    .WiT(A_WiT), .WiF(A_WiF), .NW(alu16bit_1_nw));
  Transceiver transceiver_2 (.S0(IE_D), .S1(S_D), .I0(buffer16_3_out_2), .I1(out_15), .O0(out_15), .O1(S0_b));
  RAM #(.addrWidth(16), .dataWidth(16)) ram_1 (
    .addr(buffer16_2_out_2), .data(out_15), .sel(1'b1), .clk(buffer_4_out), .ld(buffer1_4_out_2));  // open: clr
  InstDecoder instdecoder_1 (
    .Op(instfielddecoder_1_op), .Fn_Ak(instfielddecoder_1_fn), .IE_R7(IE_R7), .IE_R6(IE_R6), .IE_R5(IE_R5),
    .IE_R4(IE_R4), .IE_R3(IE_R3), .IE_R2(IE_R2), .IE_R0(IE_R0), .SA_R7(SA_R7), .SA_R6(SA_R6), .SA_R5(SA_R5),
    .SA_R4(SA_R4), .SA_R3(SA_R3), .SA_R2(SA_R2), .SA_R1(SA_R1), .SA_R0(SA_R0), .IE_R1(IE_R1),
    .Rj(instfielddecoder_1_rj), .Rk(instfielddecoder_1_rk), .SB_R7(SB_R7), .SB_R6(SB_R6), .SB_R5(SB_R5),
    .SB_R4(SB_R4), .SB_R3(SB_R3), .SB_R2(SB_R2), .SB_R1(SB_R1), .SB_R0(SB_R0), .Ty(instfielddecoder_1_ty),
    .PH1(PH1), .PH2(PH2), .St(instfielddecoder_1_st), .IE_D(IE_D), .S_IMM(S_IMM), .IE_MAR(IE_MAR),
    .WE_M(WE_M), .OE_M(OE_M), .S_BUS(S_BUS), .WI_SR(WI_SR), .A_C(A_C), .A_C1(A_C1), .A_D6_plus(A_D6_plus),
    .A_D6_minus(A_D6_minus), .S_ZERO(S_ZERO), .A_LDB(A_LDB), .A_SELT(A_SELT), .A_SELF(A_SELF), .A_ADD(A_ADD),
    .A_SUB(A_SUB), .A_RSB(A_RSB), .A_AND(A_AND), .A_OR(A_OR), .A_XOR(A_XOR), .S_SR1(S_SR1), .S_SR4(S_SR4),
    .S_SL1(S_SL1), .S_SL4(S_SL4), .S_ROT(S_ROT), .IE_PFR(IE_PFR), .A_CC(A_CC), .IE_LK(IE_LK), .A_WIT(A_WiT),
    .A_WIF(A_WiF), .HLT(HLT), .Ri_CC(instfielddecoder_1_ri), .A_LDA(A_LDA), .S_D(S_D), .CLR1(CLR1),
    .CLR2(CLR2), .S_P(S_P), .LPDM(LDPM), .PH0(PH0));
  REG_ALU ALUR (
    .IE(PH1), .CLR(CLR1), .OE(1'b1), .NZ(alu16bit_1_nz), .C(alu16bit_1_cout), .NT(alu16bit_1_nt_2),
    .In(alu16bit_1_o), .NZ_2(ALUR_nt_2[1]), .C_2(ALUR_nt_2[2]), .Out(ALUR_out), .Test(out_7),
    .NW(alu16bit_1_nw), .NW_2(WI_R), .NT_2(ALUR_nt_2[0]), .RR(RRsh), .RR_2(ALUR_rr_2));

  // Other names for the same wires on the sheet: Imm5[4:0] = out_18[4:0]; IMM16_D[15:0] = out_18

  // Notes on the sheet:
  //   contents of rom_1 (hex, n*v repeats v):
  //   3 df08 5e28 5e00 18c0 19c1 1ac2 1ec3 fe90 e784 8880 89c1 8ac2 b300 bc09 bd12 b31b bc24 bd2d b318
  //   bc21 bd2a d800 d900 8 da00 5830 5931 5a32 2 da10 582c 592d 5a2e de0b b358 bc61 bd6a ef88 7010 7911
  //   7a12 b358 bc61 bd6a e7c6 e641 e795 b318 bc21 bd2a 704c 794d 7a4e 40ae 40ed 40ec 700c 790d 7a0e 40b2
  //   40f1 40f0 8b83 8cc4 8dc5 1 e740 5e00 18e0 19e1 1ae2 18c3 8080 b100 b109 b108 8181 f141 8981 19e3
  //   5f08 5c00 e404 5804 1860 5805 1861 5806 1862 5807 1863 5c20 df42 5c00 1840 5838 1841 5839 1842 583a
  //   1843 583b 800 3 d815 dc00 d908 900c e786 1b00 1b60 e001 e401 e746 2 df12 18 260 4*0 20
endmodule

module Clock (
  input  Reset,
  input  Fast_Slow,
  input  Osc_Man,
  input  Tick,
  output CLK_PH
);

  wire and_1_out, and_2_out, buffer_1_out, buffer_2_out, clock_1_out, clock_2_out, d_ff_1_q, d_ff_1_qn,
       d_ff_2_q, d_ff_2_qn, d_ff_3_q, d_ff_4_q, d_ff_5_qn, d_ff_6_qn, nand_1_out, not_1_out, not_2_out,
       not_3_out, or_1_out, or_2_out, or_3_out;

  Button u_Reset (.out(Reset));
  Button button_1 ();  // open: out
  Clock_part clock_1 (.out(clock_1_out));
  Button button_2 ();  // open: out
  Clock_part #(.highDuration(3), .lowDuration(3)) clock_2 (.out(clock_2_out));
  Button u_Tick ();  // open: out
  buf buffer_1 (buffer_1_out, Fast_Slow);
  not not_1 (not_1_out, Fast_Slow);
  buf buffer_2 (buffer_2_out, Osc_Man);
  not not_2 (not_2_out, Osc_Man);
  not not_3 (not_3_out, Tick);
  D_Flip_Flop d_ff_1 (.clk(clock_1_out), .D(d_ff_1_qn), .Q(d_ff_1_q), .Qn(d_ff_1_qn));  // open: preset, en, reset
  D_Flip_Flop d_ff_2 (.clk(clock_2_out), .D(d_ff_2_qn), .Q(d_ff_2_q), .Qn(d_ff_2_qn));  // open: preset, en, reset
  and and_1 (and_1_out, buffer_1_out, buffer_2_out, d_ff_6_qn);
  and and_2 (and_2_out, not_1_out, buffer_2_out, d_ff_5_qn);
  nand nand_1 (nand_1_out, d_ff_5_qn, d_ff_6_qn, not_2_out);
  D_Flip_Flop d_ff_3 (.clk(d_ff_1_q), .D(and_1_out), .Q(d_ff_3_q));  // open: Qn, preset, en, reset
  D_Flip_Flop d_ff_4 (.clk(d_ff_2_q), .D(and_2_out), .Q(d_ff_4_q));  // open: Qn, preset, en, reset
  D_Flip_Flop d_ff_5 (.clk(d_ff_1_qn), .D(d_ff_3_q), .Qn(d_ff_5_qn), .reset(Reset));  // open: Q, preset, en
  D_Flip_Flop d_ff_6 (.clk(d_ff_2_qn), .D(d_ff_4_q), .Qn(d_ff_6_qn), .reset(Reset));  // open: Q, preset, en
  or or_1 (or_1_out, d_ff_5_qn, d_ff_1_qn);
  or or_2 (or_2_out, d_ff_6_qn, d_ff_2_qn);
  or or_3 (or_3_out, nand_1_out, not_3_out);
  nand nand_2 (CLK_PH, or_1_out, or_2_out, or_3_out);

  // Other names for the same wires on the sheet: RST = Reset
endmodule

// SEQ
module Sequencer (
  input  CLKIn,
  input  HLT,
  input  Step,
  input  RUN,
  output PH0,
  output PH1,
  output CLR1,
  output PH2,
  output CLR2,
  output Test,
  output Test_2,
  output Test_3,
  output Test_4
);

  wire buffer_1_out, buffer_2_out, buffer_6_out, buffer_7_out, buffer_9_out, buffer_11_out, buffer_12_out,
       buffer_14_out, buffer_15_out, buffer_16_out, buffer_17_out, buffer_20_out, buffer_21_out,
       buffer_22_out, CLK, dpdt_1_com_2, dpdth_1_com_2, dpdth_2_com_2, dpdth_3_com, dpdth_3_com_2,
       dpdth_4_com_2, dpdth_6_com, dpdth_6_com_2, dpdth_7_com_2, dpdth_8_com, dpdth_8_com_2, dpdth_9_com_2,
       dpdth_10_com, dpdth_10_com_2, dpdth_11_com_2, dpdtr_1_nc_2, dpdtr_1_no, dpdtr_3_nc_2, dpdtr_3_no,
       dpdtr_3_no_2, dpdtr_4_nc_2, dpdtr_4_no, dpdtr_5_nc_2, dpdtr_6_nc_2, dpdtr_6_no, dpdtr_7_nc_2,
       dpdtr_7_no, dpdtr_7_no_2, dpdtr_8_nc_2, dpdtr_9_nc_2, nCLK, not_1_out, SEQRun;

  buf buffer_1 (buffer_1_out, dpdth_11_com_2);
  not not_1 (not_1_out, Step);
  buf buffer_2 (buffer_2_out, Step);
  buf buffer_3 (buffer_2_out, RUN);
  buf buffer_4 (CLR1, dpdtr_1_no);
  buf buffer_5 (PH0, dpdtr_1_no);
  DPDTr dpdtr_1 (.coil(Test), .com(1'b1), .com_2(1'b1), .NO(dpdtr_1_no), .NC_2(dpdtr_1_nc_2));  // open: NC, NO_2
  DPDTh dpdth_1 (
    .coil(buffer_1_out), .NO(dpdtr_4_nc_2), .NO_2(nCLK), .com(Test), .com_2(dpdth_1_com_2));  // open: NC, NC_2
  buf buffer_6 (buffer_6_out, CLKIn);
  buf buffer_7 (buffer_7_out, dpdth_1_com_2);
  DPDTr dpdtr_2 (.coil(buffer_6_out), .com(1'b1), .NC(nCLK), .NO(CLK));  // open: com_2, NC_2, NO_2
  DPDTh dpdth_2 (.coil(HLT), .NO(not_1_out), .NC_2(buffer_2_out), .com_2(dpdth_2_com_2));  // open: NC, NO_2, com
  buf buffer_8 (PH0, dpdtr_3_no);
  DPDTr dpdtr_3 (
    .coil(dpdth_3_com), .com(1'b1), .com_2(1'b1), .NO(dpdtr_3_no), .NC_2(dpdtr_3_nc_2), .NO_2(dpdtr_3_no_2));  // open: NC
  DPDTh dpdth_3 (
    .coil(buffer_7_out), .NO(dpdtr_5_nc_2), .NO_2(CLK), .com(dpdth_3_com), .com_2(dpdth_3_com_2));  // open: NC, NC_2
  buf buffer_9 (buffer_9_out, dpdtr_3_no);
  buf buffer_10 (PH1, dpdtr_3_no);
  buf buffer_11 (buffer_11_out, dpdth_3_com_2);
  DPDT dpdt_1 (.coil(dpdth_2_com_2), .com_2(dpdt_1_com_2), .NO_2(nCLK));  // open: NC, com, NO, NC_2
  DPDTr dpdtr_4 (.coil(Test_2), .com(1'b1), .com_2(1'b1), .NO(dpdtr_4_no), .NC_2(dpdtr_4_nc_2));  // open: NC, NO_2
  DPDTh dpdth_4 (
    .coil(buffer_11_out), .NO(dpdtr_6_nc_2), .NO_2(nCLK), .com(Test_2), .com_2(dpdth_4_com_2));  // open: NC, NC_2
  buf buffer_12 (buffer_12_out, dpdt_1_com_2);
  buf buffer_13 (PH0, dpdtr_4_no);
  buf buffer_14 (buffer_14_out, dpdtr_4_no);
  buf buffer_15 (buffer_15_out, dpdth_4_com_2);
  DPDTh dpdth_5 (.coil(buffer_12_out), .NO(dpdth_2_com_2), .NO_2(CLK), .com_2(SEQRun));  // open: NC, NC_2, com
  DPDTr dpdtr_5 (.coil(dpdth_6_com), .com_2(1'b1), .NC_2(dpdtr_5_nc_2));  // open: com, NC, NO, NO_2
  DPDTh dpdth_6 (
    .coil(buffer_15_out), .NO(dpdtr_7_nc_2), .NO_2(CLK), .com(dpdth_6_com), .com_2(dpdth_6_com_2));  // open: NC, NC_2
  buf buffer_16 (buffer_16_out, dpdth_6_com_2);
  DPDTr dpdtr_6 (.coil(Test_3), .com(1'b1), .com_2(1'b1), .NO(dpdtr_6_no), .NC_2(dpdtr_6_nc_2));  // open: NC, NO_2
  buf buffer_17 (buffer_17_out, dpdth_7_com_2);
  DPDTh dpdth_7 (
    .coil(buffer_16_out), .NO(dpdtr_8_nc_2), .NO_2(nCLK), .com(Test_3), .com_2(dpdth_7_com_2));  // open: NC, NC_2
  buf buffer_18 (CLR2, dpdtr_7_no);
  DPDTr dpdtr_7 (
    .coil(dpdth_8_com), .com(dpdtr_6_no), .com_2(1'b1), .NO(dpdtr_7_no), .NC_2(dpdtr_7_nc_2),
    .NO_2(dpdtr_7_no_2));  // open: NC
  DPDTh dpdth_8 (
    .coil(buffer_17_out), .NO(dpdtr_9_nc_2), .NO_2(CLK), .com(dpdth_8_com), .com_2(dpdth_8_com_2));  // open: NC, NC_2
  buf buffer_19 (PH2, dpdtr_7_no_2);
  buf buffer_20 (buffer_20_out, dpdth_8_com_2);
  DPDTr dpdtr_8 (.coil(Test_4), .com_2(1'b1), .NC_2(dpdtr_8_nc_2));  // open: com, NC, NO, NO_2
  DPDTh dpdth_9 (
    .coil(buffer_20_out), .NO(dpdtr_1_nc_2), .NO_2(nCLK), .com(Test_4), .com_2(dpdth_9_com_2));  // open: NC, NC_2
  buf buffer_21 (buffer_21_out, dpdth_9_com_2);
  DPDTr dpdtr_9 (.coil(dpdth_10_com), .com_2(1'b1), .NC_2(dpdtr_9_nc_2));  // open: com, NC, NO, NO_2
  DPDTh dpdth_10 (
    .coil(buffer_21_out), .NO(dpdtr_3_nc_2), .NC_2(1'b1), .NO_2(CLK), .com(dpdth_10_com),
    .com_2(dpdth_10_com_2));  // open: NC
  buf buffer_22 (buffer_22_out, dpdth_10_com_2);
  DPDTh dpdth_11 (
    .coil(dpdtr_3_no_2), .NO(buffer_22_out), .NC_2(SEQRun), .com_2(dpdth_11_com_2));  // open: NC, NO_2, com

  // Notes on the sheet:
  //   buffer_1 drives only 1 and floats otherwise
  //   buffer_2 drives only 1 and floats otherwise
  //   buffer_3 drives only 1 and floats otherwise
  //   buffer_4 drives only 1 and floats otherwise
  //   buffer_5 drives only 1 and floats otherwise
  //   buffer_6 drives only 1 and floats otherwise
  //   buffer_7 drives only 1 and floats otherwise
  //   buffer_8 drives only 1 and floats otherwise
  //   buffer_9 drives only 1 and floats otherwise
  //   buffer_10 drives only 1 and floats otherwise
  //   buffer_11 drives only 1 and floats otherwise
  //   buffer_12 drives only 1 and floats otherwise
  //   buffer_13 drives only 1 and floats otherwise
  //   buffer_14 drives only 1 and floats otherwise
  //   buffer_15 drives only 1 and floats otherwise
  //   buffer_16 drives only 1 and floats otherwise
  //   buffer_17 drives only 1 and floats otherwise
  //   buffer_18 drives only 1 and floats otherwise
  //   buffer_19 drives only 1 and floats otherwise
  //   buffer_20 drives only 1 and floats otherwise
  //   buffer_21 drives only 1 and floats otherwise
  //   buffer_22 drives only 1 and floats otherwise
endmodule

// REG
module REG16Bit (
  input  nWE,
  input  IE,
  input  CLR,
  input  OE,
  input  [15:0] In,
  output [15:0] Out,
  output [15:0] Test
);

  wire buffer_1_out, buffer_2_out, buffer_3_out, IE_no, nH_nc_2, nWE_nc;

  buf buffer_1 (buffer_1_out, IE);
  DPDTr u_nWE (.coil(nWE), .com(buffer_1_out), .NC(nWE_nc));  // open: com_2, NO, NC_2, NO_2
  buf buffer_2 (buffer_2_out, CLR);
  buf buffer_3 (buffer_3_out, OE);
  DPDTr u_IE (.coil(nWE_nc), .com(buffer_2_out), .NO(IE_no));  // open: com_2, NC, NC_2, NO_2
  DPDTr nH (.coil(IE_no), .com_2(1'b1), .NC_2(nH_nc_2));  // open: com, NC, NO, NO_2
  REGBase16Bit regbase16bit_1 (.Hold(nH_nc_2), .IE(nWE_nc), .OE(buffer_3_out), .R(Test), .A(Out), .I0(In));

  // Notes on the sheet:
  //   buffer_1 drives only 1 and floats otherwise
  //   buffer_2 drives only 1 and floats otherwise
  //   buffer_3 drives only 1 and floats otherwise
endmodule

// PC
module REG_PC (
  input  nWE,
  input  IE,
  input  PH,
  input  CLR,
  input  OE,
  input  [15:0] In,
  input  nWE1,
  input  PH1,
  input  CLR1,
  output [15:0] Out,
  output [15:0] Out_plus,
  output [15:0] Test
);

  wire buffer_1_out, buffer_2_out, buffer_3_out, buffer_4_out, buffer_5_out, buffer_6_out, buffer_7_out,
       buffer_9_out, IE1_no, IE_no, nH1_nc_2, nH_nc_2, nWE1_nc, nWE_nc;
  wire [15:0] inputswitch_1_o;

  buf buffer_1 (buffer_1_out, IE);
  buf buffer_2 (buffer_2_out, PH);
  buf buffer_3 (buffer_3_out, CLR);
  buf buffer_4 (buffer_4_out, OE);
  DPDTr u_nWE (.coil(nWE), .com(buffer_1_out), .NC(nWE_nc));  // open: com_2, NO, NC_2, NO_2
  buf buffer_5 (buffer_5_out, PH1);
  buf buffer_6 (buffer_6_out, CLR1);
  buf buffer_7 (buffer_7_out, nWE_nc);
  buf buffer_8 (buffer_7_out, buffer_2_out);
  buf buffer_9 (buffer_9_out, nWE_nc);
  buf buffer_10 (buffer_9_out, buffer_2_out);
  DPDTr u_nWE1 (.coil(nWE1), .com(buffer_5_out), .NC(nWE1_nc));  // open: com_2, NO, NC_2, NO_2
  DPDTr u_IE (.coil(buffer_7_out), .com(buffer_3_out), .NO(IE_no));  // open: com_2, NC, NC_2, NO_2
  DPDTr IE1 (.coil(nWE1_nc), .com(buffer_6_out), .NO(IE1_no));  // open: com_2, NC, NC_2, NO_2
  DPDTr nH (.coil(IE_no), .com_2(1'b1), .NC_2(nH_nc_2));  // open: com, NC, NO, NO_2
  InputSwitch inputswitch_1 (.S1(nWE_nc), .I0(Out_plus), .I1(In), .O(inputswitch_1_o));
  DPDTr nH1 (.coil(IE1_no), .com_2(1'b1), .NC_2(nH1_nc_2));  // open: com, NC, NO, NO_2
  REGBase16Bit PC (.Hold(nH_nc_2), .IE(buffer_9_out), .OE(buffer_4_out), .R(Test), .A(Out), .I0(inputswitch_1_o));
  INCrementer INC_R (.Hold(nH1_nc_2), .OE(1'b1), .I0(Test), .B(Out_plus), .IE(nWE1_nc));  // open: COut, R

  // Notes on the sheet:
  //   buffer_1 drives only 1 and floats otherwise
  //   buffer_2 drives only 1 and floats otherwise
  //   buffer_3 drives only 1 and floats otherwise
  //   buffer_4 drives only 1 and floats otherwise
  //   buffer_5 drives only 1 and floats otherwise
  //   buffer_6 drives only 1 and floats otherwise
  //   buffer_7 drives only 1 and floats otherwise
  //   buffer_8 drives only 1 and floats otherwise
  //   buffer_9 drives only 1 and floats otherwise
  //   buffer_10 drives only 1 and floats otherwise
endmodule

// REG_LNK
module REG_LINK (
  input  nWE,
  input  IE,
  input  CLR,
  input  IElk,
  input  CLRlk,
  input  OE,
  input  [15:0] In,
  input  [15:0] InLK,
  output [15:0] Out,
  output [15:0] Test
);

  wire buffer_1_out, buffer_2_out, buffer_3_out, buffer_5_out, buffer_6_out, dpdtr_1_no, nH_nc_2, nWE_nc;

  DPDTr u_nWE (.coil(nWE), .com(buffer_1_out), .NC(nWE_nc));  // open: com_2, NO, NC_2, NO_2
  buf buffer_1 (buffer_1_out, IE);
  buf buffer_2 (buffer_2_out, CLR);
  buf buffer_3 (buffer_3_out, IElk);
  buf buffer_4 (buffer_2_out, CLRlk);
  buf buffer_5 (buffer_5_out, OE);
  buf buffer_6 (buffer_6_out, nWE_nc);
  buf buffer_7 (buffer_6_out, buffer_3_out);
  DPDTr dpdtr_1 (.coil(buffer_6_out), .com(buffer_2_out), .NO(dpdtr_1_no));  // open: com_2, NC, NC_2, NO_2
  DPDTr nH (.coil(dpdtr_1_no), .com_2(1'b1), .NC_2(nH_nc_2));  // open: com, NC, NO, NO_2
  REGBase16Bit_2 regbase16bit_2_1 (
    .Hold(nH_nc_2), .IE0(nWE_nc), .IE1(buffer_3_out), .OE(buffer_5_out), .I0(In), .I1(InLK), .R(Test), .A(Out));

  // Notes on the sheet:
  //   buffer_1 drives only 1 and floats otherwise
  //   buffer_2 drives only 1 and floats otherwise
  //   buffer_3 drives only 1 and floats otherwise
  //   buffer_4 drives only 1 and floats otherwise
  //   buffer_5 drives only 1 and floats otherwise
  //   buffer_6 drives only 1 and floats otherwise
  //   buffer_7 drives only 1 and floats otherwise
endmodule

// STATUS REG
module REG_STATUS (
  input  nWE,
  input  IE,
  input  CLR,
  input  OE,
  input  NZ,
  input  C,
  input  NT,
  input  [3:0] RR,
  output NZ_2,
  output C_2,
  output NT_2,
  output [3:0] RR_2
);

  wire buffer_1_out, buffer_2_out, buffer_3_out, buffer_4_out, buffer_5_out, buffer_6_out, buffer_7_out,
       buffer_8_out, buffer_9_out, buffer_10_out, IE_2_com, IE_2_com_2, IE_3_com, IE_4_com, IE_4_com_2,
       IE_5_com, IE_5_com_2, IE_no, nH_nc_2, nWE_nc;

  buf buffer_1 (buffer_1_out, IE);
  buf buffer_2 (buffer_2_out, CLR);
  buf buffer_3 (buffer_3_out, OE);
  DPDTr u_nWE (.coil(nWE), .com(buffer_1_out), .NC(nWE_nc));  // open: com_2, NO, NC_2, NO_2
  DPDTr u_IE (.coil(nWE_nc), .com(buffer_2_out), .NO(IE_no));  // open: com_2, NC, NC_2, NO_2
  DPDT IE_2 (.coil(nWE_nc), .com(IE_2_com), .NO(NZ), .com_2(IE_2_com_2), .NO_2(C));  // open: NC, NC_2
  buf buffer_4 (buffer_4_out, IE_2_com);
  buf buffer_5 (buffer_5_out, IE_2_com_2);
  DPDT IE_3 (.coil(nWE_nc), .com(IE_3_com), .NO(NT));  // open: NC, NC_2, com_2, NO_2
  buf buffer_6 (buffer_6_out, IE_3_com);
  buf buffer_7 (buffer_7_out, IE_4_com);
  DPDT IE_4 (.coil(nWE_nc), .com(IE_4_com), .NO(RR[0]), .com_2(IE_4_com_2), .NO_2(RR[1]));  // open: NC, NC_2
  buf buffer_8 (buffer_8_out, IE_4_com_2);
  buf buffer_9 (buffer_9_out, IE_5_com);
  DPDT IE_5 (.coil(nWE_nc), .com(IE_5_com), .NO(RR[2]), .com_2(IE_5_com_2), .NO_2(RR[3]));  // open: NC, NC_2
  buf buffer_10 (buffer_10_out, IE_5_com_2);
  DPDTr nH (.coil(IE_no), .com_2(1'b1), .NC_2(nH_nc_2));  // open: com, NC, NO, NO_2
  DPDTh u_C (.coil(buffer_5_out), .NO(nH_nc_2), .NO_2(buffer_3_out), .com_2(C_2));  // open: NC, NC_2, com
  DPDTh RR1 (.coil(buffer_8_out), .NO(nH_nc_2), .NO_2(buffer_3_out), .com_2(RR_2[1]));  // open: NC, NC_2, com
  DPDTh RR3 (.coil(buffer_10_out), .NO(nH_nc_2), .NO_2(buffer_3_out), .com_2(RR_2[3]));  // open: NC, NC_2, com
  DPDTh u_NZ (.coil(buffer_4_out), .NO(nH_nc_2), .NO_2(buffer_3_out), .com_2(NZ_2));  // open: NC, NC_2, com
  DPDTh T (.coil(buffer_6_out), .NO(nH_nc_2), .NO_2(buffer_3_out), .com_2(NT_2));  // open: NC, NC_2, com
  DPDTh RR0 (.coil(buffer_7_out), .NO(nH_nc_2), .NO_2(buffer_3_out), .com_2(RR_2[0]));  // open: NC, NC_2, com
  DPDTh RR2 (.coil(buffer_9_out), .NO(nH_nc_2), .NO_2(buffer_3_out), .com_2(RR_2[2]));  // open: NC, NC_2, com

  // Notes on the sheet:
  //   buffer_1 drives only 1 and floats otherwise
  //   buffer_2 drives only 1 and floats otherwise
  //   buffer_3 drives only 1 and floats otherwise
  //   buffer_4 drives only 1 and floats otherwise
  //   buffer_5 drives only 1 and floats otherwise
  //   buffer_6 drives only 1 and floats otherwise
  //   buffer_7 drives only 1 and floats otherwise
  //   buffer_8 drives only 1 and floats otherwise
  //   buffer_9 drives only 1 and floats otherwise
  //   buffer_10 drives only 1 and floats otherwise
endmodule

// PREFIX
module REG_PFIX (
  input  IE,
  input  CLR,
  input  OE,
  input  [10:0] In,
  output [10:0] Out,
  output [10:0] Test
);

  wire buffer_1_out, buffer_2_out, buffer_3_out, CLR_nc_2;
  wire [15:11] regbase16bit_1_a, regbase16bit_1_r, undriven;

  buf buffer_1 (buffer_1_out, IE);
  buf buffer_2 (buffer_2_out, CLR);
  buf buffer_3 (buffer_3_out, OE);
  DPDTr u_CLR (.coil(buffer_2_out), .com_2(1'b1), .NC_2(CLR_nc_2));  // open: com, NC, NO, NO_2
  REGBase16Bit regbase16bit_1 (
    .Hold(CLR_nc_2), .IE(buffer_1_out), .OE(buffer_3_out), .R({regbase16bit_1_r, Test}),
    .A({regbase16bit_1_a, Out}), .I0({undriven, In}));

  // Notes on the sheet:
  //   buffer_1 drives only 1 and floats otherwise
  //   buffer_2 drives only 1 and floats otherwise
  //   buffer_3 drives only 1 and floats otherwise
endmodule

// ALU REG
module REG_ALU (
  input  IE,
  input  CLR,
  input  OE,
  input  NT,
  input  NZ,
  input  C,
  input  NW,
  input  [3:0] RR,
  input  [15:0] In,
  output NT_2,
  output NZ_2,
  output C_2,
  output NW_2,
  output [3:0] RR_2,
  output [15:0] Out,
  output [15:0] Test
);

  wire buffer_1_out, buffer_2_out, buffer_3_out, buffer_4_out, buffer_5_out, buffer_6_out, buffer_7_out,
       buffer_8_out, buffer_9_out, buffer_10_out, buffer_11_out, IE_2_com, IE_2_com_2, IE_3_com, IE_3_com_2,
       IE_4_com, IE_4_com_2, IE_5_com, IE_5_com_2, IE_no, nH_nc_2;

  buf buffer_1 (buffer_1_out, IE);
  buf buffer_2 (buffer_2_out, CLR);
  buf buffer_3 (buffer_3_out, OE);
  DPDTr u_IE (.coil(buffer_1_out), .com(buffer_2_out), .NO(IE_no));  // open: com_2, NC, NC_2, NO_2
  DPDT IE_2 (.coil(buffer_1_out), .com(IE_2_com), .NO(NT), .com_2(IE_2_com_2), .NO_2(NZ));  // open: NC, NC_2
  DPDT IE_3 (.coil(buffer_1_out), .com(IE_3_com), .NO(C), .com_2(IE_3_com_2), .NO_2(NW));  // open: NC, NC_2
  DPDT IE_4 (.coil(buffer_1_out), .com(IE_4_com), .NO(RR[0]), .com_2(IE_4_com_2), .NO_2(RR[1]));  // open: NC, NC_2
  DPDT IE_5 (.NC(RR[2]), .com(IE_5_com), .NO(buffer_1_out), .com_2(IE_5_com_2), .NO_2(RR[3]));  // open: coil, NC_2
  buf buffer_4 (buffer_4_out, IE_2_com);
  buf buffer_5 (buffer_5_out, IE_2_com_2);
  buf buffer_6 (buffer_6_out, IE_3_com);
  buf buffer_7 (buffer_7_out, IE_3_com_2);
  buf buffer_8 (buffer_8_out, IE_4_com);
  buf buffer_9 (buffer_9_out, IE_4_com_2);
  buf buffer_10 (buffer_10_out, IE_5_com);
  buf buffer_11 (buffer_11_out, IE_5_com_2);
  DPDTr nH (.coil(IE_no), .com_2(1'b1), .NC_2(nH_nc_2));  // open: com, NC, NO, NO_2
  DPDTh u_NZ (.coil(buffer_5_out), .NO(nH_nc_2), .NO_2(buffer_3_out), .com_2(NZ_2));  // open: NC, NC_2, com
  DPDTh u_NW (.coil(buffer_7_out), .NO(nH_nc_2), .NO_2(buffer_3_out), .com_2(NW_2));  // open: NC, NC_2, com
  DPDTh RR1 (.coil(buffer_9_out), .NO(nH_nc_2), .NO_2(buffer_3_out), .com_2(RR_2[1]));  // open: NC, NC_2, com
  DPDTh RR3 (.coil(buffer_11_out), .NO(nH_nc_2), .NO_2(buffer_3_out), .com_2(RR_2[3]));  // open: NC, NC_2, com
  REGBase16Bit regbase16bit_1 (.Hold(nH_nc_2), .IE(buffer_1_out), .OE(buffer_3_out), .R(Test), .A(Out), .I0(In));
  DPDTh u_NT (.coil(buffer_4_out), .NO(nH_nc_2), .NO_2(buffer_3_out), .com_2(NT_2));  // open: NC, NC_2, com
  DPDTh u_C (.coil(buffer_6_out), .NO(nH_nc_2), .NO_2(buffer_3_out), .com_2(C_2));  // open: NC, NC_2, com
  DPDTh RR0 (.coil(buffer_8_out), .NO(nH_nc_2), .NO_2(buffer_3_out), .com_2(RR_2[0]));  // open: NC, NC_2, com
  DPDTh RR2 (.coil(buffer_10_out), .NO(nH_nc_2), .NO_2(buffer_3_out), .com_2(RR_2[2]));  // open: NC, NC_2, com

  // Notes on the sheet:
  //   buffer_1 drives only 1 and floats otherwise
  //   buffer_2 drives only 1 and floats otherwise
  //   buffer_3 drives only 1 and floats otherwise
  //   buffer_4 drives only 1 and floats otherwise
  //   buffer_5 drives only 1 and floats otherwise
  //   buffer_6 drives only 1 and floats otherwise
  //   buffer_7 drives only 1 and floats otherwise
  //   buffer_8 drives only 1 and floats otherwise
  //   buffer_9 drives only 1 and floats otherwise
  //   buffer_10 drives only 1 and floats otherwise
  //   buffer_11 drives only 1 and floats otherwise
endmodule

// REG BASE
module REGBase16Bit (
  input  [15:0] I0,
  input  Hold,
  input  IE,
  input  OE,
  output [15:0] R,
  output [15:0] A
);

  wire buffer_1_out, buffer_2_out, buffer_3_out, buffer_4_out, buffer_5_out, buffer_6_out, buffer_7_out,
       buffer_8_out, buffer_9_out, buffer_10_out, buffer_11_out, buffer_12_out, buffer_13_out, buffer_14_out,
       buffer_15_out, buffer_16_out, IE_2_com, IE_2_com_2, IE_3_com, IE_3_com_2, IE_4_com, IE_4_com_2,
       IE_5_com, IE_5_com_2, IE_6_com, IE_6_com_2, IE_7_com, IE_7_com_2, IE_8_com, IE_8_com_2, IE_com,
       IE_com_2;

  DPDT u_IE (.coil(IE), .com(IE_com), .NO(I0[0]), .com_2(IE_com_2), .NO_2(I0[1]));  // open: NC, NC_2
  DPDT IE_2 (.coil(IE), .com(IE_2_com), .NO(I0[2]), .com_2(IE_2_com_2), .NO_2(I0[3]));  // open: NC, NC_2
  DPDT IE_3 (.coil(IE), .com(IE_3_com), .NO(I0[4]), .com_2(IE_3_com_2), .NO_2(I0[5]));  // open: NC, NC_2
  DPDT IE_4 (.coil(IE), .com(IE_4_com), .NO(I0[6]), .com_2(IE_4_com_2), .NO_2(I0[7]));  // open: NC, NC_2
  DPDT IE_5 (.coil(IE), .com(IE_5_com), .NO(I0[8]), .com_2(IE_5_com_2), .NO_2(I0[9]));  // open: NC, NC_2
  DPDT IE_6 (.coil(IE), .com(IE_6_com), .NO(I0[10]), .com_2(IE_6_com_2), .NO_2(I0[11]));  // open: NC, NC_2
  DPDT IE_7 (.coil(IE), .com(IE_7_com), .NO(I0[12]), .com_2(IE_7_com_2), .NO_2(I0[13]));  // open: NC, NC_2
  DPDT IE_8 (.coil(IE), .com(IE_8_com), .NO(I0[14]), .com_2(IE_8_com_2), .NO_2(I0[15]));  // open: NC, NC_2
  buf buffer_1 (buffer_1_out, IE_com);
  buf buffer_2 (buffer_2_out, IE_com_2);
  buf buffer_3 (buffer_3_out, IE_2_com);
  buf buffer_4 (buffer_4_out, IE_2_com_2);
  buf buffer_5 (buffer_5_out, IE_3_com);
  buf buffer_6 (buffer_6_out, IE_3_com_2);
  buf buffer_7 (buffer_7_out, IE_4_com);
  buf buffer_8 (buffer_8_out, IE_4_com_2);
  buf buffer_9 (buffer_9_out, IE_5_com);
  buf buffer_10 (buffer_10_out, IE_5_com_2);
  buf buffer_11 (buffer_11_out, IE_6_com);
  buf buffer_12 (buffer_12_out, IE_6_com_2);
  buf buffer_13 (buffer_13_out, IE_7_com);
  buf buffer_14 (buffer_14_out, IE_7_com_2);
  buf buffer_15 (buffer_15_out, IE_8_com);
  buf buffer_16 (buffer_16_out, IE_8_com_2);
  DPDTh dpdth_1 (.coil(buffer_2_out), .NO(Hold), .NO_2(OE), .com(R[1]), .com_2(A[1]));  // open: NC, NC_2
  DPDTh dpdth_2 (.coil(buffer_4_out), .NO(Hold), .NO_2(OE), .com(R[3]), .com_2(A[3]));  // open: NC, NC_2
  DPDTh dpdth_3 (.coil(buffer_6_out), .NO(Hold), .NO_2(OE), .com(R[5]), .com_2(A[5]));  // open: NC, NC_2
  DPDTh dpdth_4 (.coil(buffer_8_out), .NO(Hold), .NO_2(OE), .com(R[7]), .com_2(A[7]));  // open: NC, NC_2
  DPDTh dpdth_5 (.coil(buffer_10_out), .NO(Hold), .NO_2(OE), .com(R[9]), .com_2(A[9]));  // open: NC, NC_2
  DPDTh dpdth_6 (.coil(buffer_12_out), .NO(Hold), .NO_2(OE), .com(R[11]), .com_2(A[11]));  // open: NC, NC_2
  DPDTh dpdth_7 (.coil(buffer_14_out), .NO(Hold), .NO_2(OE), .com(R[13]), .com_2(A[13]));  // open: NC, NC_2
  DPDTh dpdth_8 (.coil(buffer_16_out), .NO(Hold), .NO_2(OE), .com(R[15]), .com_2(A[15]));  // open: NC, NC_2
  DPDTh dpdth_9 (.coil(buffer_1_out), .NO(Hold), .NO_2(OE), .com(R[0]), .com_2(A[0]));  // open: NC, NC_2
  DPDTh dpdth_10 (.coil(buffer_3_out), .NO(Hold), .NO_2(OE), .com(R[2]), .com_2(A[2]));  // open: NC, NC_2
  DPDTh dpdth_11 (.coil(buffer_5_out), .NO(Hold), .NO_2(OE), .com(R[4]), .com_2(A[4]));  // open: NC, NC_2
  DPDTh dpdth_12 (.coil(buffer_7_out), .NO(Hold), .NO_2(OE), .com(R[6]), .com_2(A[6]));  // open: NC, NC_2
  DPDTh dpdth_13 (.coil(buffer_9_out), .NO(Hold), .NO_2(OE), .com(R[8]), .com_2(A[8]));  // open: NC, NC_2
  DPDTh dpdth_14 (.coil(buffer_11_out), .NO(Hold), .NO_2(OE), .com(R[10]), .com_2(A[10]));  // open: NC, NC_2
  DPDTh dpdth_15 (.coil(buffer_13_out), .NO(Hold), .NO_2(OE), .com(R[12]), .com_2(A[12]));  // open: NC, NC_2
  DPDTh dpdth_16 (.coil(buffer_15_out), .NO(Hold), .NO_2(OE), .com(R[14]), .com_2(A[14]));  // open: NC, NC_2

  // Notes on the sheet:
  //   buffer_1 drives only 1 and floats otherwise
  //   buffer_2 drives only 1 and floats otherwise
  //   buffer_3 drives only 1 and floats otherwise
  //   buffer_4 drives only 1 and floats otherwise
  //   buffer_5 drives only 1 and floats otherwise
  //   buffer_6 drives only 1 and floats otherwise
  //   buffer_7 drives only 1 and floats otherwise
  //   buffer_8 drives only 1 and floats otherwise
  //   buffer_9 drives only 1 and floats otherwise
  //   buffer_10 drives only 1 and floats otherwise
  //   buffer_11 drives only 1 and floats otherwise
  //   buffer_12 drives only 1 and floats otherwise
  //   buffer_13 drives only 1 and floats otherwise
  //   buffer_14 drives only 1 and floats otherwise
  //   buffer_15 drives only 1 and floats otherwise
  //   buffer_16 drives only 1 and floats otherwise
endmodule

// REGBASE_2
module REGBase16Bit_2 (
  input  [15:0] I0,
  input  [15:0] I1,
  input  Hold,
  input  IE0,
  input  IE1,
  input  OE,
  output [15:0] R,
  output [15:0] A
);

  wire buffer_1_out, buffer_2_out, buffer_3_out, buffer_4_out, buffer_5_out, buffer_6_out, buffer_7_out,
       buffer_8_out, buffer_9_out, buffer_10_out, buffer_11_out, buffer_12_out, buffer_13_out, buffer_14_out,
       buffer_15_out, buffer_16_out, IE0_2_com, IE0_2_com_2, IE0_3_com, IE0_3_com_2, IE0_4_com, IE0_4_com_2,
       IE0_5_com, IE0_5_com_2, IE0_6_com, IE0_6_com_2, IE0_7_com, IE0_7_com_2, IE0_8_com, IE0_8_com_2,
       IE0_com, IE0_com_2, IE1_2_com, IE1_2_com_2, IE1_3_com, IE1_3_com_2, IE1_4_com, IE1_4_com_2, IE1_5_com,
       IE1_5_com_2, IE1_6_com, IE1_6_com_2, IE1_7_com, IE1_7_com_2, IE1_8_com, IE1_8_com_2, IE1_com,
       IE1_com_2;

  DPDT u_IE1 (.coil(IE1), .com(IE1_com), .NO(I1[0]), .com_2(IE1_com_2), .NO_2(I1[1]));  // open: NC, NC_2
  DPDT IE1_2 (.coil(IE1), .com(IE1_2_com), .NO(I1[2]), .com_2(IE1_2_com_2), .NO_2(I1[3]));  // open: NC, NC_2
  DPDT IE1_3 (.coil(IE1), .com(IE1_3_com), .NO(I1[4]), .com_2(IE1_3_com_2), .NO_2(I1[5]));  // open: NC, NC_2
  DPDT IE1_4 (.coil(IE1), .com(IE1_4_com), .NO(I1[6]), .com_2(IE1_4_com_2), .NO_2(I1[7]));  // open: NC, NC_2
  DPDT IE1_5 (.coil(IE1), .com(IE1_5_com), .NO(I1[8]), .com_2(IE1_5_com_2), .NO_2(I1[9]));  // open: NC, NC_2
  DPDT IE1_6 (.coil(IE1), .com(IE1_6_com), .NO(I1[10]), .com_2(IE1_6_com_2), .NO_2(I1[11]));  // open: NC, NC_2
  DPDT IE1_7 (.coil(IE1), .com(IE1_7_com), .NO(I1[12]), .com_2(IE1_7_com_2), .NO_2(I1[13]));  // open: NC, NC_2
  DPDT IE1_8 (.coil(IE1), .com(IE1_8_com), .NO(I1[14]), .com_2(IE1_8_com_2), .NO_2(I1[15]));  // open: NC, NC_2
  buf buffer_1 (buffer_1_out, IE1_com);
  buf buffer_2 (buffer_2_out, IE1_com_2);
  buf buffer_3 (buffer_3_out, IE1_2_com);
  buf buffer_4 (buffer_4_out, IE1_2_com_2);
  buf buffer_5 (buffer_5_out, IE1_3_com);
  buf buffer_6 (buffer_6_out, IE1_3_com_2);
  buf buffer_7 (buffer_7_out, IE1_4_com);
  buf buffer_8 (buffer_8_out, IE1_4_com_2);
  buf buffer_9 (buffer_9_out, IE1_5_com);
  buf buffer_10 (buffer_10_out, IE1_5_com_2);
  buf buffer_11 (buffer_11_out, IE1_6_com);
  buf buffer_12 (buffer_12_out, IE1_6_com_2);
  buf buffer_13 (buffer_13_out, IE1_7_com);
  buf buffer_14 (buffer_14_out, IE1_7_com_2);
  buf buffer_15 (buffer_15_out, IE1_8_com);
  buf buffer_16 (buffer_16_out, IE1_8_com_2);
  DPDT u_IE0 (.coil(IE0), .com(IE0_com), .NO(I0[0]), .com_2(IE0_com_2), .NO_2(I0[1]));  // open: NC, NC_2
  buf buffer_17 (buffer_1_out, IE0_com);
  buf buffer_18 (buffer_2_out, IE0_com_2);
  buf buffer_19 (buffer_3_out, IE0_2_com);
  DPDT IE0_2 (.coil(IE0), .com(IE0_2_com), .NO(I0[2]), .com_2(IE0_2_com_2), .NO_2(I0[3]));  // open: NC, NC_2
  buf buffer_20 (buffer_4_out, IE0_2_com_2);
  DPDT IE0_3 (.coil(IE0), .com(IE0_3_com), .NO(I0[4]), .com_2(IE0_3_com_2), .NO_2(I0[5]));  // open: NC, NC_2
  buf buffer_21 (buffer_5_out, IE0_3_com);
  buf buffer_22 (buffer_6_out, IE0_3_com_2);
  buf buffer_23 (buffer_7_out, IE0_4_com);
  DPDT IE0_4 (.coil(IE0), .com(IE0_4_com), .NO(I0[6]), .com_2(IE0_4_com_2), .NO_2(I0[7]));  // open: NC, NC_2
  buf buffer_24 (buffer_8_out, IE0_4_com_2);
  DPDT IE0_5 (.coil(IE0), .com(IE0_5_com), .NO(I0[8]), .com_2(IE0_5_com_2), .NO_2(I0[9]));  // open: NC, NC_2
  buf buffer_25 (buffer_9_out, IE0_5_com);
  buf buffer_26 (buffer_10_out, IE0_5_com_2);
  DPDT IE0_6 (.coil(IE0), .com(IE0_6_com), .NO(I0[10]), .com_2(IE0_6_com_2), .NO_2(I0[11]));  // open: NC, NC_2
  buf buffer_27 (buffer_11_out, IE0_6_com);
  buf buffer_28 (buffer_12_out, IE0_6_com_2);
  buf buffer_29 (buffer_13_out, IE0_7_com);
  DPDT IE0_7 (.coil(IE0), .com(IE0_7_com), .NO(I0[12]), .com_2(IE0_7_com_2), .NO_2(I0[13]));  // open: NC, NC_2
  buf buffer_30 (buffer_14_out, IE0_7_com_2);
  buf buffer_31 (buffer_15_out, IE0_8_com);
  DPDT IE0_8 (.coil(IE0), .com(IE0_8_com), .NO(I0[14]), .com_2(IE0_8_com_2), .NO_2(I0[15]));  // open: NC, NC_2
  buf buffer_32 (buffer_16_out, IE0_8_com_2);
  DPDTh dpdth_1 (.coil(buffer_2_out), .NO(Hold), .NO_2(OE), .com(R[1]), .com_2(A[1]));  // open: NC, NC_2
  DPDTh dpdth_2 (.coil(buffer_4_out), .NO(Hold), .NO_2(OE), .com(R[3]), .com_2(A[3]));  // open: NC, NC_2
  DPDTh dpdth_3 (.coil(buffer_6_out), .NO(Hold), .NO_2(OE), .com(R[5]), .com_2(A[5]));  // open: NC, NC_2
  DPDTh dpdth_4 (.coil(buffer_8_out), .NO(Hold), .NO_2(OE), .com(R[7]), .com_2(A[7]));  // open: NC, NC_2
  DPDTh dpdth_5 (.coil(buffer_10_out), .NO(Hold), .NO_2(OE), .com(R[9]), .com_2(A[9]));  // open: NC, NC_2
  DPDTh dpdth_6 (.coil(buffer_12_out), .NO(Hold), .NO_2(OE), .com(R[11]), .com_2(A[11]));  // open: NC, NC_2
  DPDTh dpdth_7 (.coil(buffer_14_out), .NO(Hold), .NO_2(OE), .com(R[13]), .com_2(A[13]));  // open: NC, NC_2
  DPDTh dpdth_8 (.coil(buffer_16_out), .NO(Hold), .NO_2(OE), .com(R[15]), .com_2(A[15]));  // open: NC, NC_2
  DPDTh dpdth_9 (.coil(buffer_1_out), .NO(Hold), .NO_2(OE), .com(R[0]), .com_2(A[0]));  // open: NC, NC_2
  DPDTh dpdth_10 (.coil(buffer_3_out), .NO(Hold), .NO_2(OE), .com(R[2]), .com_2(A[2]));  // open: NC, NC_2
  DPDTh dpdth_11 (.coil(buffer_5_out), .NO(Hold), .NO_2(OE), .com(R[4]), .com_2(A[4]));  // open: NC, NC_2
  DPDTh dpdth_12 (.coil(buffer_7_out), .NO(Hold), .NO_2(OE), .com(R[6]), .com_2(A[6]));  // open: NC, NC_2
  DPDTh dpdth_13 (.coil(buffer_9_out), .NO(Hold), .NO_2(OE), .com(R[8]), .com_2(A[8]));  // open: NC, NC_2
  DPDTh dpdth_14 (.coil(buffer_11_out), .NO(Hold), .NO_2(OE), .com(R[10]), .com_2(A[10]));  // open: NC, NC_2
  DPDTh dpdth_15 (.coil(buffer_13_out), .NO(Hold), .NO_2(OE), .com(R[12]), .com_2(A[12]));  // open: NC, NC_2
  DPDTh dpdth_16 (.coil(buffer_15_out), .NO(Hold), .NO_2(OE), .com(R[14]), .com_2(A[14]));  // open: NC, NC_2

  // Notes on the sheet:
  //   buffer_1 drives only 1 and floats otherwise
  //   buffer_2 drives only 1 and floats otherwise
  //   buffer_3 drives only 1 and floats otherwise
  //   buffer_4 drives only 1 and floats otherwise
  //   buffer_5 drives only 1 and floats otherwise
  //   buffer_6 drives only 1 and floats otherwise
  //   buffer_7 drives only 1 and floats otherwise
  //   buffer_8 drives only 1 and floats otherwise
  //   buffer_9 drives only 1 and floats otherwise
  //   buffer_10 drives only 1 and floats otherwise
  //   buffer_11 drives only 1 and floats otherwise
  //   buffer_12 drives only 1 and floats otherwise
  //   buffer_13 drives only 1 and floats otherwise
  //   buffer_14 drives only 1 and floats otherwise
  //   buffer_15 drives only 1 and floats otherwise
  //   buffer_16 drives only 1 and floats otherwise
  //   buffer_17 drives only 1 and floats otherwise
  //   buffer_18 drives only 1 and floats otherwise
  //   buffer_19 drives only 1 and floats otherwise
  //   buffer_20 drives only 1 and floats otherwise
  //   buffer_21 drives only 1 and floats otherwise
  //   buffer_22 drives only 1 and floats otherwise
  //   buffer_23 drives only 1 and floats otherwise
  //   buffer_24 drives only 1 and floats otherwise
  //   buffer_25 drives only 1 and floats otherwise
  //   buffer_26 drives only 1 and floats otherwise
  //   buffer_27 drives only 1 and floats otherwise
  //   buffer_28 drives only 1 and floats otherwise
  //   buffer_29 drives only 1 and floats otherwise
  //   buffer_30 drives only 1 and floats otherwise
  //   buffer_31 drives only 1 and floats otherwise
  //   buffer_32 drives only 1 and floats otherwise
endmodule

// ALU-CTRL
module ALUController (
  input  Ld_A,
  input  Ld_B,
  input  And,
  input  Or,
  input  Xor,
  input  Add,
  input  Sub,
  input  Rsb,
  output [7:0] out_9
);

  buf buffer_1 (out_9[7], Add);
  buf buffer_2 (out_9[6], Rsb);
  buf buffer_3 (out_9[5], Sub);
  buf buffer_4 (out_9[3], Ld_A);
  buf buffer_5 (out_9[2], Ld_B);
  buf buffer_6 (out_9[3], Ld_B);
  buf buffer_7 (out_9[3], And);
  buf buffer_8 (out_9[3], Or);
  buf buffer_9 (out_9[2], Or);
  buf buffer_10 (out_9[2], Xor);
  buf buffer_11 (out_9[2], Add);
  buf buffer_12 (out_9[3], Sub);
  buf buffer_13 (out_9[3], Rsb);
  buf buffer_14 (out_9[1], Ld_A);
  buf buffer_15 (out_9[1], Or);
  buf buffer_16 (out_9[1], Xor);
  buf buffer_17 (out_9[1], Add);
  buf buffer_18 (out_9[0], Sub);
  buf buffer_19 (out_9[0], Rsb);

  // Notes on the sheet:
  //   buffer_1 drives only 1 and floats otherwise
  //   buffer_2 drives only 1 and floats otherwise
  //   buffer_3 drives only 1 and floats otherwise
  //   buffer_4 drives only 1 and floats otherwise
  //   buffer_5 drives only 1 and floats otherwise
  //   buffer_6 drives only 1 and floats otherwise
  //   buffer_7 drives only 1 and floats otherwise
  //   buffer_8 drives only 1 and floats otherwise
  //   buffer_9 drives only 1 and floats otherwise
  //   buffer_10 drives only 1 and floats otherwise
  //   buffer_11 drives only 1 and floats otherwise
  //   buffer_12 drives only 1 and floats otherwise
  //   buffer_13 drives only 1 and floats otherwise
  //   buffer_14 drives only 1 and floats otherwise
  //   buffer_15 drives only 1 and floats otherwise
  //   buffer_16 drives only 1 and floats otherwise
  //   buffer_17 drives only 1 and floats otherwise
  //   buffer_18 drives only 1 and floats otherwise
  //   buffer_19 drives only 1 and floats otherwise
endmodule

// ALU
module ALU16Bit (
  input  LdA,
  input  LdB,
  input  And,
  input  Or,
  input  Xor,
  input  Add,
  input  Sub,
  input  Rsb,
  input  SelT,
  input  SelF,
  input  WiT,
  input  WiF,
  input  A_D6_plus,
  input  A_D6_minus,
  input  A_C1,
  input  A_C,
  input  NT,
  input  CIn,
  input  NZIn,
  input  [15:0] A,
  input  [15:0] B,
  input  Csh,
  input  SH,
  input  [7:0] CC_8,
  output NW,
  output Cout,
  output [15:0] O,
  output NZ,
  output NT_2
);

  wire alubase4bit_1_cout, alubase4bit_2_cout, alubase4bit_3_cout, alubase4bit_4_cx, buffer_3_out,
       buffer_4_out, buffer_11_out, buffer_30_out, CIn_no, NT_2_nc, NT_2_no_2, NT_nc, NT_nc_2, NT_no,
       NT_no_2, NZIn_no;
  wire [7:0] alucontroller_1_out_9;

  buf buffer_1 (CC_8[2], SH);
  buf buffer_2 (CC_8[2], A_D6_minus);
  DPDTr u_NT (.coil(NT), .com(SelT), .com_2(SelF), .NC(NT_nc), .NO(NT_no), .NC_2(NT_nc_2), .NO_2(NT_no_2));
  DPDTr u_NT_2 (.coil(NT), .com(WiT), .com_2(WiF), .NC(NT_2_nc), .NO_2(NT_2_no_2));  // open: NO, NC_2
  DPDTr u_CIn (.coil(CIn), .com(A_C), .NO(CIn_no));  // open: com_2, NC, NC_2, NO_2
  DPDTr u_NZIn (.coil(NZIn), .com(A_C), .NO(NZIn_no));  // open: com_2, NC, NC_2, NO_2
  buf buffer_3 (buffer_3_out, LdA);
  buf buffer_4 (buffer_4_out, LdB);
  buf buffer_5 (buffer_3_out, NT_no);
  buf buffer_6 (buffer_4_out, NT_nc);
  buf buffer_7 (buffer_4_out, NT_no_2);
  buf buffer_8 (buffer_3_out, NT_nc_2);
  buf buffer_9 (NW, NT_2_nc);
  buf buffer_10 (NW, NT_2_no_2);
  buf buffer_11 (buffer_11_out, A_C1);
  buf buffer_12 (buffer_11_out, CIn_no);
  ALUController alucontroller_1 (
    .And(And), .Or(Or), .Xor(Xor), .Add(Add), .Sub(Sub), .out_9(alucontroller_1_out_9), .Rsb(Rsb),
    .Ld_A(buffer_3_out), .Ld_B(buffer_4_out));
  buf buffer_13 (NZ, NZIn_no);
  ALUBase4Bit alubase4bit_1 (
    .Op(alucontroller_1_out_9), .A(A[3:0]), .B(B[3:0]), .Cin(buffer_11_out), .minus_6(A_D6_minus),
    .Q(O[3:0]), .Cout(alubase4bit_1_cout), .plus_6(A_D6_plus));  // open: Cx
  buf buffer_14 (NZ, O[2]);
  buf buffer_15 (NZ, O[0]);
  buf buffer_16 (NZ, O[6]);
  buf buffer_17 (NZ, O[4]);
  buf buffer_18 (NZ, O[7]);
  buf buffer_19 (NZ, O[5]);
  buf buffer_20 (NZ, O[3]);
  buf buffer_21 (NZ, O[1]);
  buf buffer_22 (NZ, O[10]);
  buf buffer_23 (NZ, O[8]);
  buf buffer_24 (NZ, O[14]);
  buf buffer_25 (NZ, O[12]);
  buf buffer_26 (NZ, O[13]);
  buf buffer_27 (NZ, O[15]);
  buf buffer_28 (NZ, O[11]);
  buf buffer_29 (NZ, O[9]);
  ALUBase4Bit alubase4bit_2 (
    .Op(alucontroller_1_out_9), .A(A[7:4]), .B(B[7:4]), .Cin(alubase4bit_1_cout), .minus_6(A_D6_minus),
    .Q(O[7:4]), .Cout(alubase4bit_2_cout), .plus_6(A_D6_plus));  // open: Cx
  buf buffer_30 (buffer_30_out, Csh);
  ALUBase4Bit alubase4bit_3 (
    .Op(alucontroller_1_out_9), .A(A[11:8]), .B(B[11:8]), .Cin(alubase4bit_2_cout), .minus_6(A_D6_minus),
    .Q(O[11:8]), .Cout(alubase4bit_3_cout), .plus_6(A_D6_plus));  // open: Cx
  buf buffer_31 (buffer_30_out, Cout);
  ALUBase4Bit alubase4bit_4 (
    .Op(alucontroller_1_out_9), .A(A[15:12]), .B(B[15:12]), .Cin(alubase4bit_3_cout), .minus_6(A_D6_minus),
    .Q(O[15:12]), .Cout(Cout), .Cx(alubase4bit_4_cx), .plus_6(A_D6_plus));
  ALUFlags aluflags_1 (.NT(NT_2), .Cx(alubase4bit_4_cx), .C(buffer_30_out), .CC_8(CC_8), .nZ(NZ), .S(O[15]));

  // Notes on the sheet:
  //   buffer_1 drives only 1 and floats otherwise
  //   buffer_2 drives only 1 and floats otherwise
  //   buffer_3 drives only 1 and floats otherwise
  //   buffer_4 drives only 1 and floats otherwise
  //   buffer_5 drives only 1 and floats otherwise
  //   buffer_6 drives only 1 and floats otherwise
  //   buffer_7 drives only 1 and floats otherwise
  //   buffer_8 drives only 1 and floats otherwise
  //   buffer_9 drives only 1 and floats otherwise
  //   buffer_10 drives only 1 and floats otherwise
  //   buffer_11 drives only 1 and floats otherwise
  //   buffer_12 drives only 1 and floats otherwise
  //   buffer_13 drives only 1 and floats otherwise
  //   buffer_14 drives only 1 and floats otherwise
  //   buffer_15 drives only 1 and floats otherwise
  //   buffer_16 drives only 1 and floats otherwise
  //   buffer_17 drives only 1 and floats otherwise
  //   buffer_18 drives only 1 and floats otherwise
  //   buffer_19 drives only 1 and floats otherwise
  //   buffer_20 drives only 1 and floats otherwise
  //   buffer_21 drives only 1 and floats otherwise
  //   buffer_22 drives only 1 and floats otherwise
  //   buffer_23 drives only 1 and floats otherwise
  //   buffer_24 drives only 1 and floats otherwise
  //   buffer_25 drives only 1 and floats otherwise
  //   buffer_26 drives only 1 and floats otherwise
  //   buffer_27 drives only 1 and floats otherwise
  //   buffer_28 drives only 1 and floats otherwise
  //   buffer_29 drives only 1 and floats otherwise
  //   buffer_30 drives only 1 and floats otherwise
  //   buffer_31 drives only 1 and floats otherwise
endmodule

// ALU4
module ALUBase4Bit (
  input  [7:0] Op,
  input  minus_6,
  input  plus_6,
  input  [3:0] A,
  input  [3:0] B,
  input  Cin,
  output Cout,
  output Cx,
  output [3:0] Q
);

  wire alubase1bit_1_cout, alubase1bit_2_cout;
  wire [3:0] aluadd6_1_q, alubase1bit_1_q;

  ALUAdd6 aluadd6_1 (.I(A), .EN(plus_6), .Q(aluadd6_1_q));
  ALUBase1Bit alubase1bit_1 (
    .A(aluadd6_1_q[0]), .B(B[0]), .Cin(Cin), .Q(alubase1bit_1_q[0]), .Cout(alubase1bit_1_cout), .GS1(Op[5]),
    .GS2(Op[6]), .GS3(Op[7]), .PS0(Op[0]), .PS1(Op[1]), .PS2(Op[2]), .PS3(Op[3]), .GS0(Op[4]));
  ALUBase1Bit alubase1bit_2 (
    .A(aluadd6_1_q[1]), .B(B[1]), .Cin(alubase1bit_1_cout), .Q(alubase1bit_1_q[1]),
    .Cout(alubase1bit_2_cout), .GS1(Op[5]), .GS2(Op[6]), .GS3(Op[7]), .PS0(Op[0]), .PS1(Op[1]), .PS2(Op[2]),
    .PS3(Op[3]), .GS0(Op[4]));
  ALUBase1Bit alubase1bit_3 (
    .A(aluadd6_1_q[2]), .B(B[2]), .Cin(alubase1bit_2_cout), .Q(alubase1bit_1_q[2]), .Cout(Cx), .GS1(Op[5]),
    .GS2(Op[6]), .GS3(Op[7]), .PS0(Op[0]), .PS1(Op[1]), .PS2(Op[2]), .PS3(Op[3]), .GS0(Op[4]));
  ALUBase1Bit alubase1bit_4 (
    .A(aluadd6_1_q[3]), .B(B[3]), .Cin(Cx), .Q(alubase1bit_1_q[3]), .Cout(Cout), .GS1(Op[5]), .GS2(Op[6]),
    .GS3(Op[7]), .PS0(Op[0]), .PS1(Op[1]), .PS2(Op[2]), .PS3(Op[3]), .GS0(Op[4]));
  ALUSub6 alusub6_1 (.I(alubase1bit_1_q), .EN(minus_6), .Q(Q), .Cin(Cout));
endmodule

// ALU-1
module ALUBase1Bit (
  input  A,
  input  GS3,
  input  PS3,
  input  GS2,
  input  PS2,
  input  GS1,
  input  PS1,
  input  GS0,
  input  PS0,
  input  B,
  input  Cin,
  output Cout,
  output Q
);

  wire A_2_com, A_2_com_2, A_com, A_com_2, B_com, B_com_2, dpdtr_1_nc, dpdtr_1_no;

  DPDT u_A (.coil(A), .NC(GS2), .com(A_com), .NO(GS3), .NC_2(GS0), .com_2(A_com_2), .NO_2(GS1));
  DPDT A_2 (.coil(A), .NC(PS2), .com(A_2_com), .NO(PS3), .NC_2(PS0), .com_2(A_2_com_2), .NO_2(PS1));
  DPDT u_B (.coil(B), .NC(A_2_com_2), .com(B_com), .NO(A_2_com), .NC_2(A_com_2), .com_2(B_com_2), .NO_2(A_com));
  DPDTr dpdtr_1 (.coil(Cin), .com(1'b1), .NC(dpdtr_1_nc), .NO(dpdtr_1_no));  // open: com_2, NC_2, NO_2
  DPDT P (.coil(B_com), .NC(B_com_2), .com(Cout), .NO(Cin), .NC_2(dpdtr_1_no), .com_2(Q), .NO_2(dpdtr_1_nc));

  // Notes on the sheet:
  //    GS.PS
  //   0000.0000 Q=0x00
  //   0000.1111 Q=0xff
  //   0000.1010 Q=A
  //   0000.1100 Q=B
  //   0000.0101 Q=/A
  //   0000.0011 Q=/B
  //   0000.1110 Q= A| B
  //   0000.1101 Q=/A| B
  //   0000.1011 Q= A|/B
  //   0000.0111 Q=/A|/B
  //   0000.1000 Q= A& B
  //   0000.0100 Q=/A& B
  //   0000.0010 Q= A&/B
  //   0000.0001 Q=/A&/B
  //   0000.0110 Q=  A^B
  //   0000.1001 Q=/(A^B)
  //    0100.1001 Q=/A+B=B-A 
  //   1000.0110 Q=A+B
  //   0010.1001 Q=A+/B=A-B
  //   1010.0000 Q=A<<1 //shift left
  //   1100.0000 Q=B<<1 //shift left
  //   1010.0101 Q=A+$FF=A-1
  //   1100.0011 Q=B+$FF=B-1
endmodule

module ALUAdd6 (
  input  [3:0] I,
  input  EN,
  output [3:0] Q
);

  wire Bit1_com_2, Bit1_nc_2, Bit1_no_2, Bit2_nc_2, Bit2_no, Bit2_no_2, EN_nc, EN_nc_2;

  DPDTr Bit2 (.coil(I[2]), .com(EN), .com_2(EN), .NO(Bit2_no), .NC_2(Bit2_nc_2), .NO_2(Bit2_no_2));  // open: NC
  DPDTr u_EN (.coil(EN), .com(I[1]), .com_2(I[2]), .NC(EN_nc), .NC_2(EN_nc_2));  // open: NO, NO_2
  DPDTb Bit1 (
    .coil(I[1]), .com(EN), .NC(Bit2_nc_2), .NO(Bit2_no_2), .NC_2(Bit1_nc_2), .NO_2(Bit1_no_2),
    .com_2(Bit1_com_2));
  buf buffer_1 (Q[3], I[3]);
  buf buffer_2 (Q[3], Bit2_no);
  buf buffer_3 (Q[3], Bit1_no_2);
  buf buffer_4 (Q[1], Bit1_nc_2);
  buf buffer_5 (Q[1], EN_nc);
  buf buffer_6 (Q[2], Bit1_com_2);
  buf buffer_7 (Q[2], EN_nc_2);

  assign Q[0] = I[0];

  // Notes on the sheet:
  //   buffer_1 drives only 1 and floats otherwise
  //   buffer_2 drives only 1 and floats otherwise
  //   buffer_3 drives only 1 and floats otherwise
  //   buffer_4 drives only 1 and floats otherwise
  //   buffer_5 drives only 1 and floats otherwise
  //   buffer_6 drives only 1 and floats otherwise
  //   buffer_7 drives only 1 and floats otherwise
endmodule

// -6
module ALUSub6 (
  input  [3:0] I,
  input  Cin,
  input  EN,
  output [3:0] Q
);

  wire Bit1_com_2, Bit1_nc_2, Bit1_no_2, Bit2_nc_2, Bit2_no, Bit2_no_2, Bit3_no, Cin_nc, EN_2_nc, EN_nc,
       EN_nc_2;

  DPDTr u_Cin (.coil(Cin), .com(EN), .NC(Cin_nc));  // open: com_2, NO, NC_2, NO_2
  DPDTr Bit3 (.coil(I[3]), .com(Bit1_no_2), .NO(Bit3_no));  // open: com_2, NC, NC_2, NO_2
  DPDTr Bit2 (
    .coil(I[2]), .com(Bit3_no), .com_2(Cin_nc), .NO(Bit2_no), .NC_2(Bit2_nc_2), .NO_2(Bit2_no_2));  // open: NC
  DPDTr u_EN (.coil(Cin_nc), .com(I[1]), .com_2(I[2]), .NC(EN_nc), .NC_2(EN_nc_2));  // open: NO, NO_2
  DPDTr EN_2 (.coil(Cin_nc), .com(I[3]), .NC(EN_2_nc));  // open: com_2, NO, NC_2, NO_2
  buf buffer_1 (Q[3], Bit2_no);
  DPDTb Bit1 (
    .coil(I[1]), .com(Cin_nc), .NC(Bit2_no_2), .NO(Bit2_nc_2), .NC_2(Bit1_nc_2), .NO_2(Bit1_no_2),
    .com_2(Bit1_com_2));
  buf buffer_2 (Q[3], EN_2_nc);
  buf buffer_3 (Q[1], Bit1_nc_2);
  buf buffer_4 (Q[1], EN_nc);
  buf buffer_5 (Q[2], Bit1_com_2);
  buf buffer_6 (Q[2], EN_nc_2);

  assign Q[0] = I[0];

  // Notes on the sheet:
  //   buffer_1 drives only 1 and floats otherwise
  //   buffer_2 drives only 1 and floats otherwise
  //   buffer_3 drives only 1 and floats otherwise
  //   buffer_4 drives only 1 and floats otherwise
  //   buffer_5 drives only 1 and floats otherwise
  //   buffer_6 drives only 1 and floats otherwise
endmodule

// FLAGS
module ALUFlags (
  input  S,
  input  Cx,
  input  C,
  input  nZ,
  input  [7:0] CC_8,
  output NT
);

  wire buffer_1_out, buffer_2_out, buffer_4_out, buffer_6_out, buffer_8_out, buffer_10_out, buffer_12_out,
       buffer_19_out, buffer_20_out, C_2_nc, C_2_no_2, C_3_com, C_3_com_2, Cx_nc, Cx_nc_2, Cx_no, Cx_no_2,
       nCC_0_com, nZ_2_nc_2, nZ_2_no, S_nc, S_nc_2, S_no, S_no_2;

  // Probe on CC_8[0]
  // Probe on CC_8[1]
  // Probe on CC_8[2]
  // Probe on CC_8[3]
  // Probe on CC_8[4]
  // Probe on CC_8[5]
  // Probe on CC_8[6]
  // Probe on CC_8[7]
  buf buffer_1 (buffer_1_out, CC_8[0]);
  buf buffer_2 (buffer_2_out, CC_8[0]);
  buf buffer_3 (buffer_1_out, CC_8[1]);
  buf buffer_4 (buffer_4_out, CC_8[1]);
  buf buffer_5 (buffer_1_out, CC_8[2]);
  buf buffer_6 (buffer_6_out, CC_8[2]);
  buf buffer_7 (buffer_1_out, CC_8[3]);
  buf buffer_8 (buffer_8_out, CC_8[3]);
  buf buffer_9 (buffer_1_out, CC_8[4]);
  buf buffer_10 (buffer_10_out, CC_8[4]);
  buf buffer_11 (buffer_1_out, CC_8[5]);
  buf buffer_12 (buffer_12_out, CC_8[5]);
  buf buffer_13 (buffer_1_out, CC_8[6]);
  buf buffer_14 (buffer_4_out, CC_8[6]);
  buf buffer_15 (buffer_6_out, CC_8[6]);
  buf buffer_16 (buffer_1_out, CC_8[7]);
  buf buffer_17 (buffer_4_out, CC_8[7]);
  buf buffer_18 (buffer_10_out, CC_8[7]);
  // Probe on buffer_2_out
  // Probe on buffer_4_out
  // Probe on buffer_6_out
  // Probe on buffer_8_out
  // Probe on buffer_10_out
  // Probe on buffer_12_out
  DPDTr u_S (.coil(S), .com(buffer_10_out), .com_2(buffer_12_out), .NC(S_nc), .NO(S_no), .NC_2(S_nc_2), .NO_2(S_no_2));
  buf buffer_19 (buffer_19_out, S_no);
  buf buffer_20 (buffer_20_out, S_nc);
  buf buffer_21 (buffer_20_out, S_no_2);
  buf buffer_22 (buffer_19_out, S_nc_2);
  DPDTr u_Cx (
    .coil(Cx), .com(buffer_20_out), .com_2(buffer_19_out), .NC(Cx_nc), .NO(Cx_no), .NC_2(Cx_nc_2),
    .NO_2(Cx_no_2));
  DPDTr C_2 (.coil(C), .com(buffer_6_out), .com_2(buffer_8_out), .NC(C_2_nc), .NO_2(C_2_no_2));  // open: NO, NC_2
  DPDT C_3 (.coil(C), .NC(Cx_no), .com(C_3_com), .NO(Cx_nc), .NC_2(Cx_nc_2), .com_2(C_3_com_2), .NO_2(Cx_no_2));
  DPDT nCC_0 (.coil(buffer_1_out), .NC(nZ), .com(nCC_0_com));  // open: NO, NC_2, com_2, NO_2
  DPDTr nZ_2 (.coil(nZ), .com(buffer_2_out), .com_2(buffer_4_out), .NO(nZ_2_no), .NC_2(nZ_2_nc_2));  // open: NC, NO_2
  buf buffer_23 (NT, nCC_0_com);
  buf buffer_24 (NT, nZ_2_no);
  buf buffer_25 (NT, nZ_2_nc_2);
  buf buffer_26 (NT, C_2_nc);
  buf buffer_27 (NT, C_2_no_2);
  buf buffer_28 (NT, C_3_com);
  buf buffer_29 (NT, C_3_com_2);

  // Notes on the sheet:
  //   buffer_1 drives only 1 and floats otherwise
  //   buffer_2 drives only 1 and floats otherwise
  //   buffer_3 drives only 1 and floats otherwise
  //   buffer_4 drives only 1 and floats otherwise
  //   buffer_5 drives only 1 and floats otherwise
  //   buffer_6 drives only 1 and floats otherwise
  //   buffer_7 drives only 1 and floats otherwise
  //   buffer_8 drives only 1 and floats otherwise
  //   buffer_9 drives only 1 and floats otherwise
  //   buffer_10 drives only 1 and floats otherwise
  //   buffer_11 drives only 1 and floats otherwise
  //   buffer_12 drives only 1 and floats otherwise
  //   buffer_13 drives only 1 and floats otherwise
  //   buffer_14 drives only 1 and floats otherwise
  //   buffer_15 drives only 1 and floats otherwise
  //   buffer_16 drives only 1 and floats otherwise
  //   buffer_17 drives only 1 and floats otherwise
  //   buffer_18 drives only 1 and floats otherwise
  //   buffer_19 drives only 1 and floats otherwise
  //   V
  //   buffer_20 drives only 1 and floats otherwise
  //   buffer_21 drives only 1 and floats otherwise
  //   /V
  //   buffer_22 drives only 1 and floats otherwise
  //   buffer_23 drives only 1 and floats otherwise
  //   buffer_24 drives only 1 and floats otherwise
  //   buffer_25 drives only 1 and floats otherwise
  //   buffer_26 drives only 1 and floats otherwise
  //   buffer_27 drives only 1 and floats otherwise
  //   buffer_28 drives only 1 and floats otherwise
  //   buffer_29 drives only 1 and floats otherwise
endmodule

// INC
module INCrementer (
  input  [15:0] I0,
  input  Hold,
  input  IE,
  input  OE,
  output COut,
  output [15:0] R,
  output [15:0] B
);

  wire buffer_1_out, buffer_2_out, buffer_3_out, buffer_4_out, buffer_5_out, buffer_6_out, buffer_7_out,
       buffer_8_out, buffer_9_out, buffer_10_out, buffer_11_out, buffer_12_out, buffer_13_out, buffer_14_out,
       buffer_15_out, buffer_16_out, IE_2_com, IE_2_com_2, IE_3_com, IE_3_com_2, IE_4_com, IE_4_com_2,
       IE_5_com, IE_5_com_2, IE_6_com, IE_6_com_2, IE_7_com, IE_7_com_2, IE_8_com, IE_8_com_2, IE_com,
       IE_com_2, incbase1_1_cout, incbase1_1_q, incbase1_2_cout, incbase1_2_q, incbase1_3_cout, incbase1_3_q,
       incbase1_4_cout, incbase1_4_q, incbase1_5_cout, incbase1_5_q, incbase1_6_cout, incbase1_6_q,
       incbase1_7_cout, incbase1_7_q, incbase1_8_cout, incbase1_8_q, incbase1_9_cout, incbase1_9_q,
       incbase1_10_cout, incbase1_10_q, incbase1_11_cout, incbase1_11_q, incbase1_12_cout, incbase1_12_q,
       incbase1_13_cout, incbase1_13_q, incbase1_14_cout, incbase1_14_q, incbase1_15_cout, incbase1_15_q,
       incbase1_16_q;

  INCBase1 incbase1_1 (.I(I0[0]), .Cin(1'b1), .Q(incbase1_1_q), .Cout(incbase1_1_cout));
  INCBase1 incbase1_2 (.I(I0[1]), .Cin(incbase1_1_cout), .Q(incbase1_2_q), .Cout(incbase1_2_cout));
  INCBase1 incbase1_3 (.I(I0[2]), .Cin(incbase1_2_cout), .Q(incbase1_3_q), .Cout(incbase1_3_cout));
  INCBase1 incbase1_4 (.I(I0[3]), .Cin(incbase1_3_cout), .Q(incbase1_4_q), .Cout(incbase1_4_cout));
  INCBase1 incbase1_5 (.I(I0[4]), .Cin(incbase1_4_cout), .Q(incbase1_5_q), .Cout(incbase1_5_cout));
  INCBase1 incbase1_6 (.I(I0[5]), .Cin(incbase1_5_cout), .Q(incbase1_6_q), .Cout(incbase1_6_cout));
  INCBase1 incbase1_7 (.I(I0[6]), .Cin(incbase1_6_cout), .Q(incbase1_7_q), .Cout(incbase1_7_cout));
  INCBase1 incbase1_8 (.I(I0[7]), .Cin(incbase1_7_cout), .Q(incbase1_8_q), .Cout(incbase1_8_cout));
  INCBase1 incbase1_9 (.I(I0[8]), .Cin(incbase1_8_cout), .Q(incbase1_9_q), .Cout(incbase1_9_cout));
  INCBase1 incbase1_10 (.I(I0[9]), .Cin(incbase1_9_cout), .Q(incbase1_10_q), .Cout(incbase1_10_cout));
  INCBase1 incbase1_11 (.I(I0[10]), .Cin(incbase1_10_cout), .Q(incbase1_11_q), .Cout(incbase1_11_cout));
  INCBase1 incbase1_12 (.I(I0[11]), .Cin(incbase1_11_cout), .Q(incbase1_12_q), .Cout(incbase1_12_cout));
  INCBase1 incbase1_13 (.I(I0[12]), .Cin(incbase1_12_cout), .Q(incbase1_13_q), .Cout(incbase1_13_cout));
  INCBase1 incbase1_14 (.I(I0[13]), .Cin(incbase1_13_cout), .Q(incbase1_14_q), .Cout(incbase1_14_cout));
  INCBase1 incbase1_15 (.I(I0[14]), .Cin(incbase1_14_cout), .Q(incbase1_15_q), .Cout(incbase1_15_cout));
  INCBase1 incbase1_16 (.I(I0[15]), .Cin(incbase1_15_cout), .Q(incbase1_16_q), .Cout(COut));
  DPDT u_IE (.coil(IE), .com(IE_com), .NO(incbase1_1_q), .com_2(IE_com_2), .NO_2(incbase1_2_q));  // open: NC, NC_2
  DPDT IE_2 (.coil(IE), .com(IE_2_com), .NO(incbase1_3_q), .com_2(IE_2_com_2), .NO_2(incbase1_4_q));  // open: NC, NC_2
  DPDT IE_3 (.coil(IE), .com(IE_3_com), .NO(incbase1_5_q), .com_2(IE_3_com_2), .NO_2(incbase1_6_q));  // open: NC, NC_2
  DPDT IE_4 (.coil(IE), .com(IE_4_com), .NO(incbase1_7_q), .com_2(IE_4_com_2), .NO_2(incbase1_8_q));  // open: NC, NC_2
  DPDT IE_5 (.coil(IE), .com(IE_5_com), .NO(incbase1_9_q), .com_2(IE_5_com_2), .NO_2(incbase1_10_q));  // open: NC, NC_2
  DPDT IE_6 (
    .coil(IE), .com(IE_6_com), .NO(incbase1_11_q), .com_2(IE_6_com_2), .NO_2(incbase1_12_q));  // open: NC, NC_2
  DPDT IE_7 (
    .coil(IE), .com(IE_7_com), .NO(incbase1_13_q), .com_2(IE_7_com_2), .NO_2(incbase1_14_q));  // open: NC, NC_2
  DPDT IE_8 (
    .coil(IE), .com(IE_8_com), .NO(incbase1_15_q), .com_2(IE_8_com_2), .NO_2(incbase1_16_q));  // open: NC, NC_2
  buf buffer_1 (buffer_1_out, IE_com);
  buf buffer_2 (buffer_2_out, IE_com_2);
  buf buffer_3 (buffer_3_out, IE_2_com);
  buf buffer_4 (buffer_4_out, IE_2_com_2);
  buf buffer_5 (buffer_5_out, IE_3_com);
  buf buffer_6 (buffer_6_out, IE_3_com_2);
  buf buffer_7 (buffer_7_out, IE_4_com);
  buf buffer_8 (buffer_8_out, IE_4_com_2);
  buf buffer_9 (buffer_9_out, IE_5_com);
  buf buffer_10 (buffer_10_out, IE_5_com_2);
  buf buffer_11 (buffer_11_out, IE_6_com);
  buf buffer_12 (buffer_12_out, IE_6_com_2);
  buf buffer_13 (buffer_13_out, IE_7_com);
  buf buffer_14 (buffer_14_out, IE_7_com_2);
  buf buffer_15 (buffer_15_out, IE_8_com);
  buf buffer_16 (buffer_16_out, IE_8_com_2);
  DPDTh dpdth_1 (.coil(buffer_2_out), .NO(Hold), .NO_2(OE), .com(R[1]), .com_2(B[1]));  // open: NC, NC_2
  DPDTh dpdth_2 (.coil(buffer_4_out), .NO(Hold), .NO_2(OE), .com(R[3]), .com_2(B[3]));  // open: NC, NC_2
  DPDTh dpdth_3 (.coil(buffer_6_out), .NO(Hold), .NO_2(OE), .com(R[5]), .com_2(B[5]));  // open: NC, NC_2
  DPDTh dpdth_4 (.coil(buffer_8_out), .NO(Hold), .NO_2(OE), .com(R[7]), .com_2(B[7]));  // open: NC, NC_2
  DPDTh dpdth_5 (.coil(buffer_10_out), .NO(Hold), .NO_2(OE), .com(R[9]), .com_2(B[9]));  // open: NC, NC_2
  DPDTh dpdth_6 (.coil(buffer_12_out), .NO(Hold), .NO_2(OE), .com(R[11]), .com_2(B[11]));  // open: NC, NC_2
  DPDTh dpdth_7 (.coil(buffer_14_out), .NO(Hold), .NO_2(OE), .com(R[13]), .com_2(B[13]));  // open: NC, NC_2
  DPDTh dpdth_8 (.coil(buffer_16_out), .NO(Hold), .NO_2(OE), .com(R[15]), .com_2(B[15]));  // open: NC, NC_2
  DPDTh dpdth_9 (.coil(buffer_1_out), .NO(Hold), .NO_2(OE), .com(R[0]), .com_2(B[0]));  // open: NC, NC_2
  DPDTh dpdth_10 (.coil(buffer_3_out), .NO(Hold), .NO_2(OE), .com(R[2]), .com_2(B[2]));  // open: NC, NC_2
  DPDTh dpdth_11 (.coil(buffer_5_out), .NO(Hold), .NO_2(OE), .com(R[4]), .com_2(B[4]));  // open: NC, NC_2
  DPDTh dpdth_12 (.coil(buffer_7_out), .NO(Hold), .NO_2(OE), .com(R[6]), .com_2(B[6]));  // open: NC, NC_2
  DPDTh dpdth_13 (.coil(buffer_9_out), .NO(Hold), .NO_2(OE), .com(R[8]), .com_2(B[8]));  // open: NC, NC_2
  DPDTh dpdth_14 (.coil(buffer_11_out), .NO(Hold), .NO_2(OE), .com(R[10]), .com_2(B[10]));  // open: NC, NC_2
  DPDTh dpdth_15 (.coil(buffer_13_out), .NO(Hold), .NO_2(OE), .com(R[12]), .com_2(B[12]));  // open: NC, NC_2
  DPDTh dpdth_16 (.coil(buffer_15_out), .NO(Hold), .NO_2(OE), .com(R[14]), .com_2(B[14]));  // open: NC, NC_2

  // Notes on the sheet:
  //   buffer_1 drives only 1 and floats otherwise
  //   buffer_2 drives only 1 and floats otherwise
  //   buffer_3 drives only 1 and floats otherwise
  //   buffer_4 drives only 1 and floats otherwise
  //   buffer_5 drives only 1 and floats otherwise
  //   buffer_6 drives only 1 and floats otherwise
  //   buffer_7 drives only 1 and floats otherwise
  //   buffer_8 drives only 1 and floats otherwise
  //   buffer_9 drives only 1 and floats otherwise
  //   buffer_10 drives only 1 and floats otherwise
  //   buffer_11 drives only 1 and floats otherwise
  //   buffer_12 drives only 1 and floats otherwise
  //   buffer_13 drives only 1 and floats otherwise
  //   buffer_14 drives only 1 and floats otherwise
  //   buffer_15 drives only 1 and floats otherwise
  //   buffer_16 drives only 1 and floats otherwise
endmodule

module INCBase1 (
  input  I,
  input  Cin,
  output Cout,
  output Q
);

  wire Ci_nc, Ci_no;

  DPDTr Ci (.coil(Cin), .com(1'b1), .NC(Ci_nc), .NO(Ci_no));  // open: com_2, NC_2, NO_2
  DPDT u_I (.coil(I), .com(Cout), .NO(Cin), .NC_2(Ci_no), .com_2(Q), .NO_2(Ci_nc));  // open: NC
endmodule

// INPUT SEL
module InputSelect (
  input  [15:0] I0,
  input  [15:0] I1,
  input  EN0,
  input  EN1,
  output [15:0] A
);

  wire EN0_2_com, EN0_2_com_2, EN0_3_com, EN0_3_com_2, EN0_4_com, EN0_4_com_2, EN0_5_com, EN0_5_com_2,
       EN0_6_com, EN0_6_com_2, EN0_7_com, EN0_7_com_2, EN0_8_com, EN0_8_com_2, EN0_com, EN0_com_2, EN1_2_com,
       EN1_2_com_2, EN1_3_com, EN1_3_com_2, EN1_4_com, EN1_4_com_2, EN1_5_com, EN1_5_com_2, EN1_6_com,
       EN1_6_com_2, EN1_7_com, EN1_7_com_2, EN1_8_com, EN1_8_com_2, EN1_com, EN1_com_2;

  DPDT u_EN1 (.coil(EN1), .com(EN1_com), .NO(I1[0]), .com_2(EN1_com_2), .NO_2(I1[1]));  // open: NC, NC_2
  DPDT EN1_2 (.coil(EN1), .com(EN1_2_com), .NO(I1[2]), .com_2(EN1_2_com_2), .NO_2(I1[3]));  // open: NC, NC_2
  DPDT EN1_3 (.coil(EN1), .com(EN1_3_com), .NO(I1[4]), .com_2(EN1_3_com_2), .NO_2(I1[5]));  // open: NC, NC_2
  DPDT EN1_4 (.coil(EN1), .com(EN1_4_com), .NO(I1[6]), .com_2(EN1_4_com_2), .NO_2(I1[7]));  // open: NC, NC_2
  DPDT EN1_5 (.coil(EN1), .com(EN1_5_com), .NO(I1[8]), .com_2(EN1_5_com_2), .NO_2(I1[9]));  // open: NC, NC_2
  DPDT EN1_6 (.coil(EN1), .com(EN1_6_com), .NO(I1[10]), .com_2(EN1_6_com_2), .NO_2(I1[11]));  // open: NC, NC_2
  DPDT EN1_7 (.coil(EN1), .com(EN1_7_com), .NO(I1[12]), .com_2(EN1_7_com_2), .NO_2(I1[13]));  // open: NC, NC_2
  DPDT EN1_8 (.coil(EN1), .com(EN1_8_com), .NO(I1[14]), .com_2(EN1_8_com_2), .NO_2(I1[15]));  // open: NC, NC_2
  DPDT u_EN0 (.coil(EN0), .com(EN0_com), .NO(I0[0]), .com_2(EN0_com_2), .NO_2(I0[1]));  // open: NC, NC_2
  DPDT EN0_2 (.coil(EN0), .com(EN0_2_com), .NO(I0[2]), .com_2(EN0_2_com_2), .NO_2(I0[3]));  // open: NC, NC_2
  DPDT EN0_3 (.coil(EN0), .com(EN0_3_com), .NO(I0[4]), .com_2(EN0_3_com_2), .NO_2(I0[5]));  // open: NC, NC_2
  DPDT EN0_4 (.coil(EN0), .com(EN0_4_com), .NO(I0[6]), .com_2(EN0_4_com_2), .NO_2(I0[7]));  // open: NC, NC_2
  DPDT EN0_5 (.coil(EN0), .com(EN0_5_com), .NO(I0[8]), .com_2(EN0_5_com_2), .NO_2(I0[9]));  // open: NC, NC_2
  DPDT EN0_6 (.coil(EN0), .com(EN0_6_com), .NO(I0[10]), .com_2(EN0_6_com_2), .NO_2(I0[11]));  // open: NC, NC_2
  DPDT EN0_7 (.coil(EN0), .com(EN0_7_com), .NO(I0[12]), .com_2(EN0_7_com_2), .NO_2(I0[13]));  // open: NC, NC_2
  DPDT EN0_8 (.coil(EN0), .com(EN0_8_com), .NO(I0[14]), .com_2(EN0_8_com_2), .NO_2(I0[15]));  // open: NC, NC_2
  buf buffer_1 (A[0], EN0_com);
  buf buffer_2 (A[1], EN0_com_2);
  buf buffer_3 (A[0], EN1_com);
  buf buffer_4 (A[1], EN1_com_2);
  buf buffer_5 (A[2], EN0_2_com);
  buf buffer_6 (A[3], EN0_2_com_2);
  buf buffer_7 (A[2], EN1_2_com);
  buf buffer_8 (A[3], EN1_2_com_2);
  buf buffer_9 (A[4], EN0_3_com);
  buf buffer_10 (A[5], EN0_3_com_2);
  buf buffer_11 (A[4], EN1_3_com);
  buf buffer_12 (A[5], EN1_3_com_2);
  buf buffer_13 (A[6], EN0_4_com);
  buf buffer_14 (A[7], EN0_4_com_2);
  buf buffer_15 (A[6], EN1_4_com);
  buf buffer_16 (A[7], EN1_4_com_2);
  buf buffer_17 (A[8], EN0_5_com);
  buf buffer_18 (A[9], EN0_5_com_2);
  buf buffer_19 (A[8], EN1_5_com);
  buf buffer_20 (A[9], EN1_5_com_2);
  buf buffer_21 (A[10], EN0_6_com);
  buf buffer_22 (A[11], EN0_6_com_2);
  buf buffer_23 (A[10], EN1_6_com);
  buf buffer_24 (A[11], EN1_6_com_2);
  buf buffer_25 (A[12], EN0_7_com);
  buf buffer_26 (A[13], EN0_7_com_2);
  buf buffer_27 (A[12], EN1_7_com);
  buf buffer_28 (A[13], EN1_7_com_2);
  buf buffer_29 (A[14], EN0_8_com);
  buf buffer_30 (A[15], EN0_8_com_2);
  buf buffer_31 (A[14], EN1_8_com);
  buf buffer_32 (A[15], EN1_8_com_2);

  // Notes on the sheet:
  //   buffer_1 drives only 1 and floats otherwise
  //   buffer_2 drives only 1 and floats otherwise
  //   buffer_3 drives only 1 and floats otherwise
  //   buffer_4 drives only 1 and floats otherwise
  //   buffer_5 drives only 1 and floats otherwise
  //   buffer_6 drives only 1 and floats otherwise
  //   buffer_7 drives only 1 and floats otherwise
  //   buffer_8 drives only 1 and floats otherwise
  //   buffer_9 drives only 1 and floats otherwise
  //   buffer_10 drives only 1 and floats otherwise
  //   buffer_11 drives only 1 and floats otherwise
  //   buffer_12 drives only 1 and floats otherwise
  //   buffer_13 drives only 1 and floats otherwise
  //   buffer_14 drives only 1 and floats otherwise
  //   buffer_15 drives only 1 and floats otherwise
  //   buffer_16 drives only 1 and floats otherwise
  //   buffer_17 drives only 1 and floats otherwise
  //   buffer_18 drives only 1 and floats otherwise
  //   buffer_19 drives only 1 and floats otherwise
  //   buffer_20 drives only 1 and floats otherwise
  //   buffer_21 drives only 1 and floats otherwise
  //   buffer_22 drives only 1 and floats otherwise
  //   buffer_23 drives only 1 and floats otherwise
  //   buffer_24 drives only 1 and floats otherwise
  //   buffer_25 drives only 1 and floats otherwise
  //   buffer_26 drives only 1 and floats otherwise
  //   buffer_27 drives only 1 and floats otherwise
  //   buffer_28 drives only 1 and floats otherwise
  //   buffer_29 drives only 1 and floats otherwise
  //   buffer_30 drives only 1 and floats otherwise
  //   buffer_31 drives only 1 and floats otherwise
  //   buffer_32 drives only 1 and floats otherwise
endmodule

// INPUT SW
module InputSwitch (
  input  [15:0] I1,
  input  [15:0] I0,
  input  S1,
  output [15:0] O
);

  DPDT u_S1 (.coil(S1), .NC(I0[0]), .com(O[0]), .NO(I1[0]), .NC_2(I0[1]), .com_2(O[1]), .NO_2(I1[1]));
  DPDT S1_2 (.coil(S1), .NC(I0[2]), .com(O[2]), .NO(I1[2]), .NC_2(I0[3]), .com_2(O[3]), .NO_2(I1[3]));
  DPDT S1_3 (.coil(S1), .NC(I0[4]), .com(O[4]), .NO(I1[4]), .NC_2(I0[5]), .com_2(O[5]), .NO_2(I1[5]));
  DPDT S1_4 (.coil(S1), .NC(I0[6]), .com(O[6]), .NO(I1[6]), .NC_2(I0[7]), .com_2(O[7]), .NO_2(I1[7]));
  DPDT S1_5 (.coil(S1), .NC(I0[8]), .com(O[8]), .NO(I1[8]), .NC_2(I0[9]), .com_2(O[9]), .NO_2(I1[9]));
  DPDT S1_6 (.coil(S1), .NC(I0[10]), .com(O[10]), .NO(I1[10]), .NC_2(I0[11]), .com_2(O[11]), .NO_2(I1[11]));
  DPDT S1_7 (.coil(S1), .NC(I0[12]), .com(O[12]), .NO(I1[12]), .NC_2(I0[13]), .com_2(O[13]), .NO_2(I1[13]));
  DPDT S1_8 (.coil(S1), .NC(I0[14]), .com(O[14]), .NO(I1[14]), .NC_2(I0[15]), .com_2(O[15]), .NO_2(I1[15]));
endmodule

// BUS SEL
module BusSelect (
  input  [15:0] I1,
  input  SA,
  input  SB,
  output [15:0] A,
  output [15:0] B
);

  DPDT u_SB (.coil(SB), .com(B[0]), .NO(I1[0]), .com_2(B[1]), .NO_2(I1[1]));  // open: NC, NC_2
  DPDT SB_2 (.coil(SB), .com(B[2]), .NO(I1[2]), .com_2(B[3]), .NO_2(I1[3]));  // open: NC, NC_2
  DPDT SB_3 (.coil(SB), .com(B[4]), .NO(I1[4]), .com_2(B[5]), .NO_2(I1[5]));  // open: NC, NC_2
  DPDT SB_4 (.coil(SB), .com(B[6]), .NO(I1[6]), .com_2(B[7]), .NO_2(I1[7]));  // open: NC, NC_2
  DPDT SB_5 (.coil(SB), .com(B[8]), .NO(I1[8]), .com_2(B[9]), .NO_2(I1[9]));  // open: NC, NC_2
  DPDT SB_6 (.coil(SB), .com(B[10]), .NO(I1[10]), .com_2(B[11]), .NO_2(I1[11]));  // open: NC, NC_2
  DPDT SB_7 (.coil(SB), .com(B[12]), .NO(I1[12]), .com_2(B[13]), .NO_2(I1[13]));  // open: NC, NC_2
  DPDT SB_8 (.coil(SB), .com(B[14]), .NO(I1[14]), .com_2(B[15]), .NO_2(I1[15]));  // open: NC, NC_2
  DPDT u_SA (.coil(SA), .com(A[0]), .NO(I1[0]), .com_2(A[1]), .NO_2(I1[1]));  // open: NC, NC_2
  DPDT SA_2 (.coil(SA), .com(A[2]), .NO(I1[2]), .com_2(A[3]), .NO_2(I1[3]));  // open: NC, NC_2
  DPDT SA_3 (.coil(SA), .com(A[4]), .NO(I1[4]), .com_2(A[5]), .NO_2(I1[5]));  // open: NC, NC_2
  DPDT SA_4 (.coil(SA), .com(A[6]), .NO(I1[6]), .com_2(A[7]), .NO_2(I1[7]));  // open: NC, NC_2
  DPDT SA_5 (.coil(SA), .com(A[8]), .NO(I1[8]), .com_2(A[9]), .NO_2(I1[9]));  // open: NC, NC_2
  DPDT SA_6 (.coil(SA), .com(A[10]), .NO(I1[10]), .com_2(A[11]), .NO_2(I1[11]));  // open: NC, NC_2
  DPDT SA_7 (.coil(SA), .com(A[12]), .NO(I1[12]), .com_2(A[13]), .NO_2(I1[13]));  // open: NC, NC_2
  DPDT SA_8 (.coil(SA), .com(A[14]), .NO(I1[14]), .com_2(A[15]), .NO_2(I1[15]));  // open: NC, NC_2
endmodule

// TRANS
module Transceiver (
  input  [15:0] I0,
  input  [15:0] I1,
  input  S0,
  input  S1,
  output [15:0] O0,
  output [15:0] O1
);

  DPDT u_S1 (.coil(S1), .com(O1[0]), .NO(I1[0]), .com_2(O1[1]), .NO_2(I1[1]));  // open: NC, NC_2
  DPDT S1_2 (.coil(S1), .com(O1[2]), .NO(I1[2]), .com_2(O1[3]), .NO_2(I1[3]));  // open: NC, NC_2
  DPDT S1_3 (.coil(S1), .com(O1[4]), .NO(I1[4]), .com_2(O1[5]), .NO_2(I1[5]));  // open: NC, NC_2
  DPDT S1_4 (.coil(S1), .com(O1[6]), .NO(I1[6]), .com_2(O1[7]), .NO_2(I1[7]));  // open: NC, NC_2
  DPDT S1_5 (.coil(S1), .com(O1[8]), .NO(I1[8]), .com_2(O1[9]), .NO_2(I1[9]));  // open: NC, NC_2
  DPDT S1_6 (.coil(S1), .com(O1[10]), .NO(I1[10]), .com_2(O1[11]), .NO_2(I1[11]));  // open: NC, NC_2
  DPDT S1_7 (.coil(S1), .com(O1[12]), .NO(I1[12]), .com_2(O1[13]), .NO_2(I1[13]));  // open: NC, NC_2
  DPDT S1_8 (.coil(S1), .com(O1[14]), .NO(I1[14]), .com_2(O1[15]), .NO_2(I1[15]));  // open: NC, NC_2
  DPDT u_S0 (.coil(S0), .com(O0[0]), .NO(I0[0]), .com_2(O0[1]), .NO_2(I0[1]));  // open: NC, NC_2
  DPDT S0_2 (.coil(S0), .com(O0[2]), .NO(I0[2]), .com_2(O0[3]), .NO_2(I0[3]));  // open: NC, NC_2
  DPDT S0_3 (.coil(S0), .com(O0[4]), .NO(I0[4]), .com_2(O0[5]), .NO_2(I0[5]));  // open: NC, NC_2
  DPDT S0_4 (.coil(S0), .com(O0[6]), .NO(I0[6]), .com_2(O0[7]), .NO_2(I0[7]));  // open: NC, NC_2
  DPDT S0_5 (.coil(S0), .com(O0[8]), .NO(I0[8]), .com_2(O0[9]), .NO_2(I0[9]));  // open: NC, NC_2
  DPDT S0_6 (.coil(S0), .com(O0[10]), .NO(I0[10]), .com_2(O0[11]), .NO_2(I0[11]));  // open: NC, NC_2
  DPDT S0_7 (.coil(S0), .com(O0[12]), .NO(I0[12]), .com_2(O0[13]), .NO_2(I0[13]));  // open: NC, NC_2
  DPDT S0_8 (.coil(S0), .com(O0[14]), .NO(I0[14]), .com_2(O0[15]), .NO_2(I0[15]));  // open: NC, NC_2
endmodule

// INST SPLIT
module InstFieldDecoder (
  input  [15:0] I,
  output [1:0] Ty,
  output [2:0] Op,
  output [2:0] Ri,
  output [1:0] FN,
  output St,
  output [2:0] Rj,
  output [2:0] Rk,
  output [4:0] imm5,
  output [10:0] pfix11
);


  assign FN = I[7:6];
  assign imm5 = I[4:0];
  assign Op = I[13:11];
  assign pfix11 = I[10:0];
  assign Ri = I[10:8];
  assign Rj = I[5:3];
  assign Rk = I[2:0];
  assign St = I[5];
  assign Ty = I[15:14];
endmodule
// INSTDECODER
module InstDecoder (
  input  [2:0] Op,
  input  [1:0] Ty,
  input  [1:0] Fn_Ak,
  input  St,
  input  PH0,
  input  PH1,
  input  PH2,
  input  CLR2,
  input  CLR1,
  input  [2:0] Ri_CC,
  input  [2:0] Rk,
  input  [2:0] Rj,
  output LPDM,
  output A_WIT,
  output A_WIF,
  output A_C,
  output A_C1,
  output A_D6_plus,
  output A_D6_minus,
  output A_LDA,
  output A_LDB,
  output A_SELT,
  output A_SELF,
  output A_ADD,
  output A_SUB,
  output A_RSB,
  output A_AND,
  output A_OR,
  output A_XOR,
  output SB_R7,
  output SB_R6,
  output SB_R5,
  output IE_LK,
  output SB_R4,
  output [7:0] A_CC,
  output SB_R3,
  output SB_R2,
  output SB_R1,
  output SB_R0,
  output HLT,
  output S_BUS,
  output IE_R7,
  output IE_R6,
  output IE_R5,
  output IE_R4,
  output IE_R3,
  output IE_R2,
  output WI_SR,
  output IE_R1,
  output S_P,
  output IE_R0,
  output SA_R7,
  output S_D,
  output SA_R6,
  output SA_R5,
  output IE_D,
  output SA_R4,
  output S_IMM,
  output SA_R3,
  output IE_MAR,
  output SA_R2,
  output SA_R1,
  output OE_M,
  output SA_R0,
  output WE_M,
  output S_SL4,
  output S_SL1,
  output S_SR4,
  output S_SR1,
  output S_ROT,
  output S_ZERO,
  output IE_PFR
);

  wire _00_011, _01_100, _01_101, _01_110, _01_111, _11_100, _11_101, A_HLT, A_LK, A_WISR, adc, add, adf,
       adt, \and , Bit1_2_nc, Bit1_2_nc_2, Bit1_2_no, Bit1_2_no_2, Bit1_3_nc, Bit1_3_nc_2, Bit1_3_no,
       Bit1_3_no_2, Bit1_4_nc, Bit1_4_nc_2, Bit1_4_no, Bit1_4_no_2, Bit1_5_nc, Bit1_5_nc_2, Bit1_5_no,
       Bit1_5_no_2, Bit1_6_nc, Bit1_6_no, Bit1_nc, Bit1_nc_2, Bit1_no, Bit1_no_2, Bit2_2_nc, Bit2_2_nc_2,
       Bit2_2_no, Bit2_2_no_2, Bit2_3_nc, Bit2_3_no, Bit2_4_nc, Bit2_4_no, Bit2_nc, Bit2_no, buffer_1_out,
       buffer_3_out, buffer_5_out, buffer_7_out, buffer_9_out, buffer_55_out, buffer_56_out, buffer_57_out,
       buffer_59_out, buffer_61_out, buffer_63_out, buffer_64_out, buffer_65_out, buffer_66_out,
       buffer_77_out, buffer_100_out, buffer_102_out, buffer_134_out, buffer_141_out, buffer_192_out,
       buffer_195_out, buffer_197_out, buffer_199_out, buffer_201_out, CLR1_nc_2, CLR2_nc_2, cmp, cpc, dac,
       dad, dsb, dsb_r, dsc, dsc_r, DST_Ri, Fn_1x_3_nc, Fn_1x_3_no, Fn_x1_2_nc, Fn_x1_2_nc_2, Fn_x1_2_no,
       Fn_x1_2_no_2, hlt_t, lp, mov, mov_r, mvl, nFn_00_2_nc, nFn_00_2_nc_2, nFn_00_no, nFn_00_no_2,
       nMem_2_nc, nMem_2_nc_2, nMem_2_no, nMem_2_no_2, nMem_3_nc, nMem_3_nc_2, nMem_3_no, nMem_3_no_2,
       nMem_4_nc, nMem_4_no, nMem_nc, nMem_nc_2, nMem_no, nMem_no_2, nOp_0x0_nc, nOp_0x0_nc_2, nOp_00x_2_no,
       nOp_00x_2_no_2, nOp_00x_3_nc, nOp_00x_3_nc_2, nOp_00x_nc, nOp_00x_nc_2, nPH0_Ex, nPH0_ex_p1, nPH2_Ex,
       nTy_00_3_nc, nTy_00_3_nc_2, nTy_00_3_no, nTy_00_3_no_2, nTy_00_no, nTy_00_no_2, Op_1xx_2_nc,
       Op_1xx_2_nc_2, Op_1xx_2_no, Op_1xx_2_no_2, Op_1xx_3_nc, Op_1xx_3_nc_2, Op_1xx_3_no, Op_1xx_3_no_2,
       Op_1xx_4_nc, Op_1xx_4_nc_2, Op_1xx_4_no, Op_1xx_4_no_2, Op_1xx_5_nc, Op_1xx_5_no, Op_1xx_no,
       Op_1xx_no_2, Op_x1x_2_nc, Op_x1x_2_nc_2, Op_x1x_2_no, Op_x1x_2_no_2, Op_x1x_3_nc, Op_x1x_3_nc_2,
       Op_x1x_3_no, Op_x1x_3_no_2, Op_x1x_4_nc, Op_x1x_4_nc_2, Op_x1x_4_no, Op_x1x_4_no_2, Op_x1x_5_nc,
       Op_x1x_5_nc_2, Op_x1x_5_no, Op_x1x_5_no_2, Op_x1x_6_nc, Op_x1x_6_nc_2, Op_x1x_6_no, Op_x1x_6_no_2,
       Op_x1x_7_nc, Op_x1x_7_nc_2, Op_x1x_7_no, Op_x1x_7_no_2, Op_x1x_nc, Op_x1x_nc_2, Op_x1x_no,
       Op_x1x_no_2, Op_xx1_2_nc_2, Op_xx1_2_no_2, Op_xx1_3_nc, Op_xx1_3_nc_2, Op_xx1_3_no_2, Op_xx1_4_nc_2,
       Op_xx1_4_no_2, Op_xx1_5_nc, Op_xx1_5_no_2, Op_xx1_9_no, Op_xx1_14_nc_2, Op_xx1_14_no_2, Op_xx1_15_nc,
       Op_xx1_nc, Op_xx1_no, \or , pfx, PH0_Ex, PH0_ex_p1, PH0CC, PH0Ldp1, PH0Ldp2, PH0lp, PH0R0a, PH0R1a,
       PH0TypeI, PH0TypeM, PH0TypeR, PH0TypeZP, PH2_Ex, PH2Ldp1, PH2Ldp2, PH2lp, PH2Mem, PH2R0a, PH2R1a,
       PH2Reg, r0a, r1a, rl1, rl4, rr1, rr4, rsb, sbc, sbc_r, sbf, sbf_r, sbt, sbt_r, sef, sel, set, sl1,
       sl4, sr1, sr4, SRC_An, SRC_CC, SRC_KBUS, SRC_Ri, SRC_Rj, SRC_Rk, St_2_nc, St_2_nc_2, St_3_nc,
       St_3_nc_2, St_4_nc, St_4_nc_2, St_5_nc, St_nc_2, sub, sub_r, Ty_1x_nc, Ty_1x_no, Ty__1x_nc, Ty__1x_no,
       \xor ;

  buf buffer_1 (buffer_1_out, Op[1]);
  buf buffer_2 (buffer_1_out, Op[2]);
  buf buffer_3 (buffer_3_out, Ty[0]);
  buf buffer_4 (buffer_3_out, Ty[1]);
  buf buffer_5 (buffer_5_out, Fn_Ak[0]);
  buf buffer_6 (buffer_5_out, Fn_Ak[1]);
  buf buffer_7 (buffer_7_out, Op[1]);
  buf buffer_8 (buffer_7_out, Op[2]);
  DPDTr Ty__1x (.coil(Ty[1]), .com(nPH0_Ex), .NC(Ty__1x_nc), .NO(Ty__1x_no));  // open: com_2, NC_2, NO_2
  DPDTr nOp_00x (
    .coil(buffer_1_out), .com(nPH0_Ex), .com_2(nPH0_Ex), .NC(nOp_00x_nc), .NC_2(nOp_00x_nc_2));  // open: NO, NO_2
  buf buffer_9 (buffer_9_out, Op[0]);
  buf buffer_10 (buffer_9_out, Op[2]);
  DPDTr Op_1xx (.coil(Op[1]), .com(PH0TypeR), .com_2(nPH0_Ex), .NO(Op_1xx_no), .NO_2(Op_1xx_no_2));  // open: NC, NC_2
  DPDTr Ty_1x (.coil(Ty[1]), .com(nPH2_Ex), .NC(Ty_1x_nc), .NO(Ty_1x_no));  // open: com_2, NC_2, NO_2
  DPDTr Op_1xx_2 (
    .coil(Op[2]), .com(PH0_Ex), .com_2(PH2_Ex), .NC(Op_1xx_2_nc), .NO(Op_1xx_2_no), .NC_2(Op_1xx_2_nc_2),
    .NO_2(Op_1xx_2_no_2));
  DPDTr Bit2 (.coil(Ri_CC[2]), .com(SRC_CC), .NC(Bit2_nc), .NO(Bit2_no));  // open: com_2, NC_2, NO_2
  DPDTr Bit2_2 (
    .coil(Ri_CC[2]), .com(DST_Ri), .com_2(SRC_Ri), .NC(Bit2_2_nc), .NO(Bit2_2_no), .NC_2(Bit2_2_nc_2),
    .NO_2(Bit2_2_no_2));
  DPDTr Bit2_3 (.coil(Rj[2]), .com(SRC_Rj), .NC(Bit2_3_nc), .NO(Bit2_3_no));  // open: com_2, NC_2, NO_2
  DPDTr nOp_00x_2 (
    .coil(buffer_7_out), .com(PH0), .com_2(PH2), .NO(nOp_00x_2_no), .NO_2(nOp_00x_2_no_2));  // open: NC, NC_2
  DPDTr Ty_x1 (
    .coil(Ty[0]), .com(Ty__1x_no), .com_2(Ty__1x_nc), .NC(PH0TypeR), .NO(PH0TypeI), .NC_2(PH0TypeM),
    .NO_2(PH0TypeZP));
  DPDTr Op_xx1 (.coil(Op[0]), .com(nOp_00x_nc), .NC(Op_xx1_nc), .NO(Op_xx1_no));  // open: com_2, NC_2, NO_2
  DPDTr nOp_0x0 (
    .coil(buffer_9_out), .com(Op_1xx_no), .com_2(Op_1xx_no_2), .NC(nOp_0x0_nc), .NC_2(nOp_0x0_nc_2));  // open: NO, NO_2
  DPDTr Bit1 (
    .coil(Ri_CC[1]), .com(Bit2_no), .com_2(Bit2_nc), .NC(Bit1_nc), .NO(Bit1_no), .NC_2(Bit1_nc_2),
    .NO_2(Bit1_no_2));
  DPDTr Bit1_2 (
    .coil(Ri_CC[1]), .com(Bit2_2_no), .com_2(Bit2_2_nc), .NC(Bit1_2_nc), .NO(Bit1_2_no), .NC_2(Bit1_2_nc_2),
    .NO_2(Bit1_2_no_2));
  DPDTr Bit1_3 (
    .coil(Ri_CC[1]), .com(Bit2_2_no_2), .com_2(Bit2_2_nc_2), .NC(Bit1_3_nc), .NO(Bit1_3_no),
    .NC_2(Bit1_3_nc_2), .NO_2(Bit1_3_no_2));
  DPDTr Bit1_4 (
    .coil(Rj[1]), .com(Bit2_3_no), .com_2(Bit2_3_nc), .NC(Bit1_4_nc), .NO(Bit1_4_no), .NC_2(Bit1_4_nc_2),
    .NO_2(Bit1_4_no_2));
  DPDTr Op_x1x (
    .coil(Op[1]), .com(Op_1xx_2_no), .com_2(Op_1xx_2_nc), .NC(Op_x1x_nc), .NO(Op_x1x_no), .NC_2(Op_x1x_nc_2),
    .NO_2(Op_x1x_no_2));
  DPDTr Op_x1x_2 (
    .coil(Op[1]), .com(Op_1xx_2_no_2), .com_2(Op_1xx_2_nc_2), .NC(Op_x1x_2_nc), .NO(Op_x1x_2_no),
    .NC_2(Op_x1x_2_nc_2), .NO_2(Op_x1x_2_no_2));
  buf buffer_11 (SRC_CC, PH0CC);
  buf buffer_12 (SRC_Ri, PH0TypeI);
  buf buffer_13 (S_IMM, PH0TypeI);
  buf buffer_14 (SRC_Rj, PH0TypeR);
  buf buffer_15 (SRC_Rk, PH0TypeR);
  buf buffer_16 (SRC_KBUS, PH0TypeR);
  buf buffer_17 (SRC_Ri, PH0TypeZP);
  buf buffer_18 (S_D, PH0TypeZP);
  buf buffer_19 (IE_MAR, PH0TypeZP);
  buf buffer_20 (OE_M, PH0TypeZP);
  buf buffer_21 (SRC_Ri, PH0TypeM);
  buf buffer_22 (S_D, PH0TypeM);
  buf buffer_23 (SRC_An, PH0TypeM);
  buf buffer_24 (IE_MAR, PH0TypeM);
  buf buffer_25 (OE_M, PH0TypeM);
  buf buffer_26 (DST_Ri, PH2Reg);
  buf buffer_27 (IE_D, PH2Mem);
  buf buffer_28 (WE_M, PH2Mem);
  DPDTr Bit0 (
    .coil(Ri_CC[0]), .com(Bit1_no), .com_2(Bit1_nc), .NC(A_CC[6]), .NO(A_CC[7]), .NC_2(A_CC[4]),
    .NO_2(A_CC[5]));
  DPDTr Bit0_2 (
    .coil(Ri_CC[0]), .com(Bit1_no_2), .com_2(Bit1_nc_2), .NC(A_CC[2]), .NO(A_CC[3]), .NC_2(A_CC[0]),
    .NO_2(A_CC[1]));
  DPDTr Bit0_3 (
    .coil(Ri_CC[0]), .com(Bit1_2_no), .com_2(Bit1_2_nc), .NC(IE_R6), .NO(IE_R7), .NC_2(IE_R4), .NO_2(IE_R5));
  DPDTr Bit0_4 (
    .coil(Ri_CC[0]), .com(Bit1_2_no_2), .com_2(Bit1_2_nc_2), .NC(IE_R2), .NO(IE_R3), .NC_2(IE_R0),
    .NO_2(IE_R1));
  DPDTr Bit0_5 (
    .coil(Ri_CC[0]), .com(Bit1_3_no), .com_2(Bit1_3_nc), .NC(SA_R6), .NO(SA_R7), .NC_2(SA_R4), .NO_2(SA_R5));
  DPDTr Bit0_6 (
    .coil(Ri_CC[0]), .com(Bit1_3_no_2), .com_2(Bit1_3_nc_2), .NC(SA_R2), .NO(SA_R3), .NC_2(SA_R0),
    .NO_2(SA_R1));
  DPDTr Bit0_7 (.coil(Rj[0]), .com(Bit1_4_no), .com_2(Bit1_4_nc), .NC(SA_R6), .NO(SA_R7), .NC_2(SA_R4), .NO_2(SA_R5));
  DPDTr Bit0_8 (
    .coil(Rj[0]), .com(Bit1_4_no_2), .com_2(Bit1_4_nc_2), .NC(SA_R2), .NO(SA_R3), .NC_2(SA_R0), .NO_2(SA_R1));
  DPDTr nTy_00 (.coil(buffer_3_out), .com(PH0), .com_2(PH2), .NO(nTy_00_no), .NO_2(nTy_00_no_2));  // open: NC, NC_2
  buf buffer_29 (nPH2_Ex, nTy_00_no_2);
  DPDTr nFn_00 (
    .coil(buffer_5_out), .com(nOp_00x_2_no), .com_2(nOp_00x_2_no_2), .NO(nFn_00_no), .NO_2(nFn_00_no_2));  // open: NC, NC_2
  buf buffer_30 (nPH2_Ex, nFn_00_no_2);
  DPDTr Fn_1x (.coil(Fn_Ak[1]), .com(Op_xx1_no), .com_2(Op_xx1_nc), .NC(S_SL1), .NO(S_SL4), .NC_2(S_SR1), .NO_2(S_SR4));
  DPDTr Fn_1x_2 (.coil(Fn_Ak[1]), .com(nOp_0x0_nc), .com_2(nOp_0x0_nc_2), .NC(PH0CC), .NO_2(S_ZERO));  // open: NO, NC_2
  DPDTr u_St (.coil(St), .com_2(Ty_1x_nc), .NC_2(St_nc_2), .NO_2(PH2Mem));  // open: com, NC, NO
  buf buffer_31 (PH2Reg, St_nc_2);
  buf buffer_32 (PH2Reg, Ty_1x_no);
  DPDTr Op_xx1_2 (
    .coil(Op[0]), .com(Op_x1x_no), .com_2(Op_x1x_nc), .NC(PH0R0a), .NO(PH0R1a), .NC_2(Op_xx1_2_nc_2),
    .NO_2(Op_xx1_2_no_2));
  DPDTr Op_xx1_3 (
    .coil(Op[0]), .com(Op_x1x_no_2), .com_2(Op_x1x_nc_2), .NC(Op_xx1_3_nc), .NO(PH0lp), .NC_2(Op_xx1_3_nc_2),
    .NO_2(Op_xx1_3_no_2));
  DPDTr Op_xx1_4 (
    .coil(Op[0]), .com(Op_x1x_2_no), .com_2(Op_x1x_2_nc), .NC(PH2R0a), .NO(PH2R1a), .NC_2(Op_xx1_4_nc_2),
    .NO_2(Op_xx1_4_no_2));
  DPDTr Op_xx1_5 (
    .coil(Op[0]), .com(Op_x1x_2_no_2), .com_2(Op_x1x_2_nc_2), .NC(Op_xx1_5_nc), .NO(PH2lp), .NC_2(IE_PFR),
    .NO_2(Op_xx1_5_no_2));
  buf buffer_33 (nPH0_Ex, nTy_00_no);
  buf buffer_34 (nPH0_Ex, nFn_00_no);
  DPDTr Fn_x1 (.coil(Fn_Ak[0]), .com(nOp_00x_nc_2), .NO(S_ROT));  // open: com_2, NC, NC_2, NO_2
  buf buffer_35 (SRC_Rk, PH0Ldp1);
  buf buffer_36 (SRC_KBUS, PH0Ldp1);
  buf buffer_37 (IE_R7, PH2Ldp1);
  buf buffer_38 (S_P, PH0Ldp2);
  buf buffer_39 (S_BUS, PH0Ldp2);
  buf buffer_40 (DST_Ri, PH2Ldp2);
  buf buffer_41 (SRC_Ri, PH0R0a);
  buf buffer_42 (SB_R0, PH0R0a);
  buf buffer_43 (SB_R4, PH0R0a);
  buf buffer_44 (IE_MAR, PH0R0a);
  buf buffer_45 (IE_R0, PH2R0a);
  buf buffer_46 (IE_D, PH2R0a);
  buf buffer_47 (WE_M, PH2R0a);
  buf buffer_48 (SRC_Ri, PH0R1a);
  buf buffer_49 (SB_R1, PH0R1a);
  buf buffer_50 (SB_R4, PH0R1a);
  buf buffer_51 (IE_MAR, PH0R1a);
  buf buffer_52 (IE_R1, PH2R1a);
  buf buffer_53 (IE_D, PH2R1a);
  buf buffer_54 (WE_M, PH2R1a);
  DPDTr Bit2_4 (
    .coil(Rk[2]), .com(SRC_Rk), .com_2(SRC_KBUS), .NC(Bit2_4_nc), .NO(Bit2_4_no), .NO_2(S_BUS));  // open: NC_2
  buf buffer_55 (buffer_55_out, CLR2);
  buf buffer_56 (buffer_56_out, CLR1);
  DPDTr Bit1_5 (
    .coil(Rk[1]), .com(Bit2_4_no), .com_2(Bit2_4_nc), .NC(Bit1_5_nc), .NO(Bit1_5_no), .NC_2(Bit1_5_nc_2),
    .NO_2(Bit1_5_no_2));
  DPDTr Bit1_6 (.coil(Fn_Ak[1]), .com(SRC_An), .NC(Bit1_6_nc), .NO(Bit1_6_no));  // open: com_2, NC_2, NO_2
  buf buffer_57 (buffer_57_out, Ty[0]);
  buf buffer_58 (buffer_57_out, Ty[1]);
  buf buffer_59 (buffer_59_out, Fn_Ak[0]);
  buf buffer_60 (buffer_59_out, Fn_Ak[1]);
  buf buffer_61 (buffer_61_out, Op[1]);
  buf buffer_62 (buffer_61_out, Op[2]);
  DPDTr nFn_00_2 (
    .coil(buffer_59_out), .com(PH0), .com_2(PH2), .NC(nFn_00_2_nc), .NC_2(nFn_00_2_nc_2));  // open: NO, NO_2
  DPDTr nOp_00x_3 (
    .coil(buffer_61_out), .com(PH0), .com_2(PH2), .NC(nOp_00x_3_nc), .NC_2(nOp_00x_3_nc_2));  // open: NO, NO_2
  DPDTr u_CLR2 (.coil(buffer_55_out), .com_2(1'b1), .NC_2(CLR2_nc_2));  // open: com, NC, NO, NO_2
  buf buffer_63 (buffer_63_out, PH2Ldp1);
  DPDTr u_CLR1 (.coil(buffer_56_out), .com_2(1'b1), .NC_2(CLR1_nc_2));  // open: com, NC, NO, NO_2
  buf buffer_64 (buffer_64_out, PH0Ldp2);
  DPDTr Bit0_9 (.coil(Rk[0]), .com(Bit1_5_no), .com_2(Bit1_5_nc), .NC(SB_R6), .NO(SB_R7), .NC_2(SB_R4), .NO_2(SB_R5));
  DPDTr Bit0_10 (
    .coil(Rk[0]), .com(Bit1_5_no_2), .com_2(Bit1_5_nc_2), .NC(SB_R2), .NO(SB_R3), .NC_2(SB_R0), .NO_2(SB_R1));
  DPDTr Bit0_11 (
    .coil(Fn_Ak[0]), .com(Bit1_6_no), .com_2(Bit1_6_nc), .NC(SB_R5), .NO(SB_R6), .NO_2(SB_R4));  // open: NC_2
  buf buffer_65 (buffer_65_out, nFn_00_2_nc);
  buf buffer_66 (buffer_66_out, nFn_00_2_nc_2);
  buf buffer_67 (buffer_65_out, nOp_00x_3_nc);
  buf buffer_68 (buffer_66_out, nOp_00x_3_nc_2);
  DPDThb dpdthb_1 (
    .coil(buffer_63_out), .NO(CLR2_nc_2), .com(PH0lp), .com_2(LPDM), .NC_2(PH0Ldp1), .NO_2(PH0Ldp2));  // open: NC
  DPDThb dpdthb_2 (
    .coil(buffer_64_out), .NO(CLR1_nc_2), .com(PH2lp), .NC_2(PH2Ldp1), .NO_2(PH2Ldp2));  // open: NC, com_2
  DPDTr nTy_00_2 (
    .coil(buffer_57_out), .com(buffer_65_out), .com_2(buffer_66_out), .NC(PH0_Ex), .NC_2(PH2_Ex));  // open: NO, NO_2
  buf buffer_69 (A_LK, mvl);
  // DPDTr nPH0_ex: pin names not known; wires that end beside it: nPH0_ex_p1, PH1, nPH0_Ex
  // DPDTr PH0_ex: pin names not known; wires that end beside it: PH0_ex_p1, PH1, PH0_Ex
  buf buffer_70 (A_WIT, cmp);
  buf buffer_71 (A_WIT, cpc);
  buf buffer_72 (A_WIT, adf);
  buf buffer_73 (A_WIT, sbf);
  buf buffer_74 (A_WIT, sbf_r);
  buf buffer_75 (A_WIT, pfx);
  buf buffer_76 (A_WIT, hlt_t);
  buf buffer_77 (buffer_77_out, A_WISR);
  buf buffer_78 (A_WISR, mov);
  buf buffer_79 (A_WISR, mov_r);
  buf buffer_80 (A_WISR, set);
  buf buffer_81 (A_WISR, sef);
  buf buffer_82 (A_WISR, sel);
  buf buffer_83 (A_WIF, cmp);
  buf buffer_84 (A_WIF, cpc);
  buf buffer_85 (A_WIF, adt);
  buf buffer_86 (A_WISR, adt);
  buf buffer_87 (A_WISR, adf);
  buf buffer_88 (A_WIF, sbt);
  buf buffer_89 (A_WISR, sbt);
  buf buffer_90 (A_WISR, sbf);
  buf buffer_91 (A_WIF, sbt_r);
  buf buffer_92 (A_WISR, sbt_r);
  buf buffer_93 (A_WISR, sbf_r);
  buf buffer_94 (A_WISR, mvl);
  buf buffer_95 (A_WISR, pfx);
  buf buffer_96 (A_WIF, pfx);
  buf buffer_97 (A_WISR, hlt_t);
  buf buffer_98 (A_WIF, hlt_t);
  buf buffer_99 (A_WISR, lp);
  buf buffer_100 (buffer_100_out, Ty[0]);
  buf buffer_101 (buffer_100_out, Ty[1]);
  buf buffer_102 (buffer_102_out, Fn_1x_3_nc);
  DPDTr Fn_1x_3 (.coil(Fn_Ak[1]), .com(nPH0_Ex), .NC(Fn_1x_3_nc), .NO(Fn_1x_3_no));  // open: com_2, NC_2, NO_2
  buf buffer_103 (buffer_102_out, nTy_00_3_nc);
  DPDTr nMem (
    .coil(Ty[1]), .com(_11_101), .com_2(_11_100), .NC(nMem_nc), .NO(nMem_no), .NC_2(nMem_nc_2),
    .NO_2(nMem_no_2));
  DPDTr nMem_2 (
    .coil(Ty[1]), .com(_01_111), .com_2(_01_110), .NC(nMem_2_nc), .NO(nMem_2_no), .NC_2(nMem_2_nc_2),
    .NO_2(nMem_2_no_2));
  DPDTr nMem_3 (
    .coil(Ty[1]), .com(_01_101), .com_2(_01_100), .NC(nMem_3_nc), .NO(nMem_3_no), .NC_2(nMem_3_nc_2),
    .NO_2(nMem_3_no_2));
  DPDTr nMem_4 (.coil(Ty[1]), .com(_00_011), .NC(nMem_4_nc), .NO(nMem_4_no));  // open: com_2, NC_2, NO_2
  buf buffer_104 (A_C, adc);
  buf buffer_105 (A_C, dac);
  buf buffer_106 (A_C1, cmp);
  buf buffer_107 (A_C, cpc);
  buf buffer_108 (A_C1, sub);
  buf buffer_109 (A_C, sbc);
  buf buffer_110 (A_C1, dsb);
  buf buffer_111 (A_C, dsc);
  buf buffer_112 (A_C1, sub_r);
  buf buffer_113 (A_C, sbc_r);
  buf buffer_114 (A_C1, dsb_r);
  buf buffer_115 (A_C, dsc_r);
  buf buffer_116 (A_C1, sbt);
  buf buffer_117 (A_C1, sbf);
  buf buffer_118 (A_C1, sbt_r);
  buf buffer_119 (A_C1, sbf_r);
  buf buffer_120 (A_C1, rsb);
  buf buffer_121 (A_C, r1a);
  DPDTr u_A_LK (.coil(A_LK), .com(PH1), .NO(IE_LK));  // open: com_2, NC, NC_2, NO_2
  DPDTr A_LK_2 (.coil(A_HLT), .com(PH1), .NO(HLT));  // open: com_2, NC, NC_2, NO_2
  DPDTh dpdth_1 (.coil(buffer_77_out), .NO(CLR1_nc_2), .NO_2(1'b1), .com_2(WI_SR));  // open: NC, NC_2, com
  DPDTr Fn_x1_2 (
    .coil(Fn_Ak[0]), .com(nTy_00_3_no), .com_2(buffer_102_out), .NC(Fn_x1_2_nc), .NO(Fn_x1_2_no),
    .NC_2(Fn_x1_2_nc_2), .NO_2(Fn_x1_2_no_2));
  DPDTr St_2 (.coil(St), .com(nMem_nc), .com_2(nMem_nc_2), .NC(St_2_nc), .NO(sbf_r), .NC_2(St_2_nc_2), .NO_2(sbt_r));
  buf buffer_122 (sbf, St_2_nc);
  buf buffer_123 (sbf, nMem_no);
  buf buffer_124 (dsc, St_3_nc);
  DPDTr St_3 (
    .coil(St), .com(nMem_2_nc), .com_2(nMem_2_nc_2), .NC(St_3_nc), .NO(dsc_r), .NC_2(St_3_nc_2), .NO_2(dsb_r));
  buf buffer_125 (dsc, nMem_2_no);
  DPDTr St_4 (
    .coil(St), .com(nMem_3_nc), .com_2(nMem_3_nc_2), .NC(St_4_nc), .NO(sbc_r), .NC_2(St_4_nc_2), .NO_2(sub_r));
  buf buffer_126 (sbc, St_4_nc);
  buf buffer_127 (sbc, nMem_3_no);
  DPDTr St_5 (.coil(St), .com(nMem_4_nc), .NC(St_5_nc), .NO(mov_r));  // open: com_2, NC_2, NO_2
  buf buffer_128 (mov, St_5_nc);
  buf buffer_129 (mov, nMem_4_no);
  buf buffer_130 (A_D6_plus, dad);
  buf buffer_131 (A_D6_plus, dac);
  buf buffer_132 (A_D6_plus, r0a);
  buf buffer_133 (A_D6_plus, r1a);
  DPDTr nTy_00_3 (
    .coil(buffer_100_out), .com(Fn_1x_3_no), .com_2(Fn_x1_2_no_2), .NC(nTy_00_3_nc), .NO(nTy_00_3_no),
    .NC_2(nTy_00_3_nc_2), .NO_2(nTy_00_3_no_2));
  buf buffer_134 (buffer_134_out, Fn_x1_2_nc_2);
  buf buffer_135 (sbt, St_2_nc_2);
  buf buffer_136 (sbt, nMem_no_2);
  buf buffer_137 (dsb, St_3_nc_2);
  buf buffer_138 (dsb, nMem_2_no_2);
  buf buffer_139 (sub, St_4_nc_2);
  buf buffer_140 (sub, nMem_3_no_2);
  buf buffer_141 (buffer_141_out, set);
  buf buffer_142 (buffer_141_out, sef);
  buf buffer_143 (A_D6_minus, dad);
  buf buffer_144 (A_D6_minus, dac);
  buf buffer_145 (A_D6_minus, dsb);
  buf buffer_146 (A_D6_minus, dsc);
  buf buffer_147 (A_D6_minus, dsb_r);
  buf buffer_148 (A_D6_minus, dsc_r);
  buf buffer_149 (A_D6_minus, r0a);
  buf buffer_150 (A_D6_minus, r1a);
  buf buffer_151 (buffer_134_out, nTy_00_3_nc_2);
  buf buffer_152 (A_LDA, mov_r);
  DPDTr Op_1xx_3 (
    .coil(Op[2]), .com(Fn_x1_2_no), .com_2(Fn_x1_2_nc), .NC(Op_1xx_3_nc), .NO(Op_1xx_3_no),
    .NC_2(Op_1xx_3_nc_2), .NO_2(Op_1xx_3_no_2));
  DPDTr Op_1xx_4 (
    .coil(Op[2]), .com(nTy_00_3_no_2), .com_2(buffer_134_out), .NC(Op_1xx_4_nc), .NO(Op_1xx_4_no),
    .NC_2(Op_1xx_4_nc_2), .NO_2(Op_1xx_4_no_2));
  DPDTr Op_1xx_5 (.coil(Op[2]), .com(PH0_Ex), .NC(Op_1xx_5_nc), .NO(Op_1xx_5_no));  // open: com_2, NC_2, NO_2
  buf buffer_153 (A_LDB, sl1);
  buf buffer_154 (A_LDB, rl1);
  buf buffer_155 (A_LDB, sl4);
  buf buffer_156 (A_LDB, rl4);
  buf buffer_157 (A_LDB, sr1);
  buf buffer_158 (A_LDB, rr1);
  buf buffer_159 (A_LDB, sr4);
  buf buffer_160 (A_LDB, rr4);
  buf buffer_161 (A_LDB, mov);
  buf buffer_162 (A_SELT, set);
  buf buffer_163 (A_SELT, sel);
  buf buffer_164 (A_LDB, mvl);
  buf buffer_165 (A_LDB, lp);
  DPDTr Op_x1x_3 (
    .coil(Op[1]), .com(Op_1xx_3_no), .com_2(Op_1xx_3_nc), .NC(Op_x1x_3_nc), .NO(Op_x1x_3_no),
    .NC_2(Op_x1x_3_nc_2), .NO_2(Op_x1x_3_no_2));
  DPDTr Op_x1x_4 (
    .coil(Op[1]), .com(Op_1xx_3_no_2), .com_2(Op_1xx_3_nc_2), .NC(Op_x1x_4_nc), .NO(Op_x1x_4_no),
    .NC_2(Op_x1x_4_nc_2), .NO_2(Op_x1x_4_no_2));
  DPDTr Op_x1x_5 (
    .coil(Op[1]), .com(Op_1xx_4_no), .com_2(Op_1xx_4_nc), .NC(Op_x1x_5_nc), .NO(Op_x1x_5_no),
    .NC_2(Op_x1x_5_nc_2), .NO_2(Op_x1x_5_no_2));
  DPDTr Op_x1x_6 (
    .coil(Op[1]), .com(Op_1xx_4_no_2), .com_2(Op_1xx_4_nc_2), .NC(Op_x1x_6_nc), .NO(Op_x1x_6_no),
    .NC_2(Op_x1x_6_nc_2), .NO_2(Op_x1x_6_no_2));
  DPDTr Op_x1x_7 (
    .coil(Op[1]), .com(Op_1xx_5_no), .com_2(Op_1xx_5_nc), .NC(Op_x1x_7_nc), .NO(Op_x1x_7_no),
    .NC_2(Op_x1x_7_nc_2), .NO_2(Op_x1x_7_no_2));
  buf buffer_166 (A_SELF, sef);
  buf buffer_167 (A_ADD, add);
  buf buffer_168 (A_ADD, adc);
  buf buffer_169 (A_ADD, dad);
  buf buffer_170 (A_ADD, dac);
  buf buffer_171 (A_ADD, adt);
  buf buffer_172 (A_ADD, adf);
  buf buffer_173 (A_ADD, r0a);
  buf buffer_174 (A_ADD, r1a);
  buf buffer_175 (A_SUB, cmp);
  buf buffer_176 (A_SUB, cpc);
  buf buffer_177 (A_SUB, sub);
  buf buffer_178 (A_SUB, sbc);
  buf buffer_179 (A_SUB, dsb);
  buf buffer_180 (A_SUB, dsc);
  buf buffer_181 (A_SUB, sbt);
  buf buffer_182 (A_SUB, sbf);
  DPDTr Op_xx1_6 (
    .coil(Op[0]), .com(Op_x1x_3_no), .com_2(Op_x1x_3_nc), .NC(\xor ), .NO(rsb), .NC_2(_11_100), .NO_2(_01_101));
  DPDTr Op_xx1_7 (.coil(Op[0]), .com(Op_x1x_3_no_2), .com_2(Op_x1x_3_nc_2), .NC(sef), .NO(sel), .NC_2(rr4), .NO_2(rl4));
  DPDTr Op_xx1_8 (.coil(Op[0]), .com(Op_x1x_4_no), .com_2(Op_x1x_4_nc), .NC(\or ), .NO(\and ), .NC_2(adt), .NO_2(adf));
  DPDTr Op_xx1_9 (
    .coil(Op[0]), .com(Op_x1x_4_no_2), .com_2(Op_x1x_4_nc_2), .NC(set), .NO(Op_xx1_9_no), .NC_2(sr4),
    .NO_2(sl4));
  DPDTr Op_xx1_10 (
    .coil(Op[0]), .com(Op_x1x_5_no), .com_2(Op_x1x_5_nc), .NC(_01_110), .NO(_01_111), .NC_2(_01_100),
    .NO_2(_01_101));
  DPDTr Op_xx1_11 (
    .coil(Op[0]), .com(Op_x1x_5_no_2), .com_2(Op_x1x_5_nc_2), .NC(cpc), .NO(mvl), .NC_2(rr1), .NO_2(rl1));
  DPDTr Op_xx1_12 (.coil(Op[0]), .com(Op_x1x_6_no), .com_2(Op_x1x_6_nc), .NC(dad), .NO(dac), .NC_2(add), .NO_2(adc));
  DPDTr Op_xx1_13 (
    .coil(Op[0]), .com(Op_x1x_6_no_2), .com_2(Op_x1x_6_nc_2), .NC(cmp), .NO(_00_011), .NC_2(sr1), .NO_2(sl1));
  DPDTr Op_xx1_14 (
    .coil(Op[0]), .com(Op_x1x_7_no), .com_2(Op_x1x_7_nc), .NC(r0a), .NO(r1a), .NC_2(Op_xx1_14_nc_2),
    .NO_2(Op_xx1_14_no_2));
  DPDTr Op_xx1_15 (
    .coil(Op[0]), .com(Op_x1x_7_no_2), .com_2(Op_x1x_7_nc_2), .NC(Op_xx1_15_nc), .NO(lp), .NC_2(pfx),
    .NO_2(hlt_t));
  buf buffer_183 (A_RSB, sub_r);
  buf buffer_184 (A_RSB, sbc_r);
  buf buffer_185 (A_RSB, dsb_r);
  buf buffer_186 (A_RSB, dsc_r);
  buf buffer_187 (A_AND, \and );
  buf buffer_188 (A_RSB, sbt_r);
  buf buffer_189 (A_RSB, sbf_r);
  buf buffer_190 (A_RSB, rsb);
  buf buffer_191 (A_OR, \or );
  buf buffer_192 (buffer_192_out, sr1);
  buf buffer_193 (buffer_192_out, rr1);
  buf buffer_194 (A_XOR, \xor );
  buf buffer_195 (buffer_195_out, sl1);
  buf buffer_196 (buffer_195_out, rl1);
  buf buffer_197 (buffer_197_out, sr4);
  buf buffer_198 (buffer_197_out, rr4);
  buf buffer_199 (buffer_199_out, sl4);
  buf buffer_200 (buffer_199_out, rl4);
  buf buffer_201 (buffer_201_out, rl1);
  buf buffer_202 (buffer_201_out, rl4);
  buf buffer_203 (buffer_201_out, rr1);
  buf buffer_204 (buffer_201_out, rr4);
  buf buffer_205 (A_HLT, hlt_t);

  // Other names for the same wires on the sheet: DST_D = IE_D; DST_MAR = IE_MAR; DST_PC = IE_R7; DST_R0 = IE_R0;
  //   DST_R1 = IE_R1; Fn[1:0] = Fn_Ak; MEM_OE = OE_M; MEM_WE = WE_M; Oper[2:0] = Op; PH0rot = S_ROT; PH0sl1 = S_SL1;
  //   PH0sl4 = S_SL4; PH0sr1 = S_SR1; PH0sr4 = S_SR4; PH0Zero = S_ZERO; PH2Pfx = IE_PFR; SRC_D = S_D; SRC_IMM = S_IMM;
  //   SRC_P = S_P; SRC_PBUS = S_BUS; SRC_R0 = SB_R0; SRC_R1 = SB_R1; SRC_R4 = SB_R4; Type[1:0] = Ty

  // Notes on the sheet:
  //   buffer_1 drives only 1 and floats otherwise
  //   buffer_2 drives only 1 and floats otherwise
  //   buffer_3 drives only 1 and floats otherwise
  //   buffer_4 drives only 1 and floats otherwise
  //   buffer_5 drives only 1 and floats otherwise
  //   buffer_6 drives only 1 and floats otherwise
  //   buffer_7 drives only 1 and floats otherwise
  //   buffer_8 drives only 1 and floats otherwise
  //   buffer_9 drives only 1 and floats otherwise
  //   buffer_10 drives only 1 and floats otherwise
  //   buffer_11 drives only 1 and floats otherwise
  //   buffer_12 drives only 1 and floats otherwise
  //   buffer_13 drives only 1 and floats otherwise
  //   buffer_14 drives only 1 and floats otherwise
  //   buffer_15 drives only 1 and floats otherwise
  //   buffer_16 drives only 1 and floats otherwise
  //   buffer_17 drives only 1 and floats otherwise
  //   buffer_18 drives only 1 and floats otherwise
  //   buffer_19 drives only 1 and floats otherwise
  //   buffer_20 drives only 1 and floats otherwise
  //   buffer_21 drives only 1 and floats otherwise
  //   buffer_22 drives only 1 and floats otherwise
  //   buffer_23 drives only 1 and floats otherwise
  //   buffer_24 drives only 1 and floats otherwise
  //   buffer_25 drives only 1 and floats otherwise
  //   buffer_26 drives only 1 and floats otherwise
  //   buffer_27 drives only 1 and floats otherwise
  //   buffer_28 drives only 1 and floats otherwise
  //   buffer_29 drives only 1 and floats otherwise
  //   buffer_30 drives only 1 and floats otherwise
  //   buffer_31 drives only 1 and floats otherwise
  //   buffer_32 drives only 1 and floats otherwise
  //   buffer_33 drives only 1 and floats otherwise
  //   buffer_34 drives only 1 and floats otherwise
  //   buffer_35 drives only 1 and floats otherwise
  //   buffer_36 drives only 1 and floats otherwise
  //   buffer_37 drives only 1 and floats otherwise
  //   buffer_38 drives only 1 and floats otherwise
  //   buffer_39 drives only 1 and floats otherwise
  //   buffer_40 drives only 1 and floats otherwise
  //   buffer_41 drives only 1 and floats otherwise
  //   buffer_42 drives only 1 and floats otherwise
  //   buffer_43 drives only 1 and floats otherwise
  //   buffer_44 drives only 1 and floats otherwise
  //   buffer_45 drives only 1 and floats otherwise
  //   buffer_46 drives only 1 and floats otherwise
  //   buffer_47 drives only 1 and floats otherwise
  //   buffer_48 drives only 1 and floats otherwise
  //   buffer_49 drives only 1 and floats otherwise
  //   buffer_50 drives only 1 and floats otherwise
  //   buffer_51 drives only 1 and floats otherwise
  //   buffer_52 drives only 1 and floats otherwise
  //   buffer_53 drives only 1 and floats otherwise
  //   buffer_54 drives only 1 and floats otherwise
  //   buffer_55 drives only 1 and floats otherwise
  //   buffer_56 drives only 1 and floats otherwise
  //   buffer_57 drives only 1 and floats otherwise
  //   buffer_58 drives only 1 and floats otherwise
  //   buffer_59 drives only 1 and floats otherwise
  //   buffer_60 drives only 1 and floats otherwise
  //   buffer_61 drives only 1 and floats otherwise
  //   buffer_62 drives only 1 and floats otherwise
  //   buffer_63 drives only 1 and floats otherwise
  //   buffer_64 drives only 1 and floats otherwise
  //   buffer_65 drives only 1 and floats otherwise
  //   buffer_66 drives only 1 and floats otherwise
  //   buffer_67 drives only 1 and floats otherwise
  //   buffer_68 drives only 1 and floats otherwise
  //   buffer_69 drives only 1 and floats otherwise
  //   buffer_70 drives only 1 and floats otherwise
  //   buffer_71 drives only 1 and floats otherwise
  //   buffer_72 drives only 1 and floats otherwise
  //   buffer_73 drives only 1 and floats otherwise
  //   buffer_74 drives only 1 and floats otherwise
  //   buffer_75 drives only 1 and floats otherwise
  //   buffer_76 drives only 1 and floats otherwise
  //   buffer_77 drives only 1 and floats otherwise
  //   buffer_78 drives only 1 and floats otherwise
  //   buffer_79 drives only 1 and floats otherwise
  //   buffer_80 drives only 1 and floats otherwise
  //   buffer_81 drives only 1 and floats otherwise
  //   buffer_82 drives only 1 and floats otherwise
  //   buffer_83 drives only 1 and floats otherwise
  //   buffer_84 drives only 1 and floats otherwise
  //   buffer_85 drives only 1 and floats otherwise
  //   buffer_86 drives only 1 and floats otherwise
  //   buffer_87 drives only 1 and floats otherwise
  //   buffer_88 drives only 1 and floats otherwise
  //   buffer_89 drives only 1 and floats otherwise
  //   buffer_90 drives only 1 and floats otherwise
  //   buffer_91 drives only 1 and floats otherwise
  //   buffer_92 drives only 1 and floats otherwise
  //   buffer_93 drives only 1 and floats otherwise
  //   buffer_94 drives only 1 and floats otherwise
  //   buffer_95 drives only 1 and floats otherwise
  //   buffer_96 drives only 1 and floats otherwise
  //   buffer_97 drives only 1 and floats otherwise
  //   buffer_98 drives only 1 and floats otherwise
  //   buffer_99 drives only 1 and floats otherwise
  //   buffer_100 drives only 1 and floats otherwise
  //   buffer_101 drives only 1 and floats otherwise
  //   buffer_102 drives only 1 and floats otherwise
  //   buffer_103 drives only 1 and floats otherwise
  //   buffer_104 drives only 1 and floats otherwise
  //   buffer_105 drives only 1 and floats otherwise
  //   buffer_106 drives only 1 and floats otherwise
  //   buffer_107 drives only 1 and floats otherwise
  //   buffer_108 drives only 1 and floats otherwise
  //   buffer_109 drives only 1 and floats otherwise
  //   buffer_110 drives only 1 and floats otherwise
  //   buffer_111 drives only 1 and floats otherwise
  //   buffer_112 drives only 1 and floats otherwise
  //   buffer_113 drives only 1 and floats otherwise
  //   buffer_114 drives only 1 and floats otherwise
  //   buffer_115 drives only 1 and floats otherwise
  //   buffer_116 drives only 1 and floats otherwise
  //   buffer_117 drives only 1 and floats otherwise
  //   buffer_118 drives only 1 and floats otherwise
  //   buffer_119 drives only 1 and floats otherwise
  //   buffer_120 drives only 1 and floats otherwise
  //   buffer_121 drives only 1 and floats otherwise
  //   buffer_122 drives only 1 and floats otherwise
  //   buffer_123 drives only 1 and floats otherwise
  //   buffer_124 drives only 1 and floats otherwise
  //   buffer_125 drives only 1 and floats otherwise
  //   buffer_126 drives only 1 and floats otherwise
  //   buffer_127 drives only 1 and floats otherwise
  //   buffer_128 drives only 1 and floats otherwise
  //   buffer_129 drives only 1 and floats otherwise
  //   buffer_130 drives only 1 and floats otherwise
  //   buffer_131 drives only 1 and floats otherwise
  //   buffer_132 drives only 1 and floats otherwise
  //   buffer_133 drives only 1 and floats otherwise
  //   buffer_134 drives only 1 and floats otherwise
  //   buffer_135 drives only 1 and floats otherwise
  //   buffer_136 drives only 1 and floats otherwise
  //   buffer_137 drives only 1 and floats otherwise
  //   buffer_138 drives only 1 and floats otherwise
  //   buffer_139 drives only 1 and floats otherwise
  //   buffer_140 drives only 1 and floats otherwise
  //   buffer_141 drives only 1 and floats otherwise
  //   buffer_142 drives only 1 and floats otherwise
  //   buffer_143 drives only 1 and floats otherwise
  //   buffer_144 drives only 1 and floats otherwise
  //   buffer_145 drives only 1 and floats otherwise
  //   buffer_146 drives only 1 and floats otherwise
  //   buffer_147 drives only 1 and floats otherwise
  //   buffer_148 drives only 1 and floats otherwise
  //   buffer_149 drives only 1 and floats otherwise
  //   buffer_150 drives only 1 and floats otherwise
  //   buffer_151 drives only 1 and floats otherwise
  //   buffer_152 drives only 1 and floats otherwise
  //   buffer_153 drives only 1 and floats otherwise
  //   buffer_154 drives only 1 and floats otherwise
  //   buffer_155 drives only 1 and floats otherwise
  //   buffer_156 drives only 1 and floats otherwise
  //   buffer_157 drives only 1 and floats otherwise
  //   buffer_158 drives only 1 and floats otherwise
  //   buffer_159 drives only 1 and floats otherwise
  //   buffer_160 drives only 1 and floats otherwise
  //   buffer_161 drives only 1 and floats otherwise
  //   buffer_162 drives only 1 and floats otherwise
  //   buffer_163 drives only 1 and floats otherwise
  //   buffer_164 drives only 1 and floats otherwise
  //   buffer_165 drives only 1 and floats otherwise
  //   buffer_166 drives only 1 and floats otherwise
  //   buffer_167 drives only 1 and floats otherwise
  //   buffer_168 drives only 1 and floats otherwise
  //   buffer_169 drives only 1 and floats otherwise
  //   buffer_170 drives only 1 and floats otherwise
  //   buffer_171 drives only 1 and floats otherwise
  //   buffer_172 drives only 1 and floats otherwise
  //   buffer_173 drives only 1 and floats otherwise
  //   buffer_174 drives only 1 and floats otherwise
  //   buffer_175 drives only 1 and floats otherwise
  //   buffer_176 drives only 1 and floats otherwise
  //   buffer_177 drives only 1 and floats otherwise
  //   buffer_178 drives only 1 and floats otherwise
  //   buffer_179 drives only 1 and floats otherwise
  //   buffer_180 drives only 1 and floats otherwise
  //   buffer_181 drives only 1 and floats otherwise
  //   buffer_182 drives only 1 and floats otherwise
  //   buffer_183 drives only 1 and floats otherwise
  //   buffer_184 drives only 1 and floats otherwise
  //   buffer_185 drives only 1 and floats otherwise
  //   buffer_186 drives only 1 and floats otherwise
  //   buffer_187 drives only 1 and floats otherwise
  //   buffer_188 drives only 1 and floats otherwise
  //   buffer_189 drives only 1 and floats otherwise
  //   buffer_190 drives only 1 and floats otherwise
  //   buffer_191 drives only 1 and floats otherwise
  //   buffer_192 drives only 1 and floats otherwise
  //   buffer_193 drives only 1 and floats otherwise
  //   buffer_194 drives only 1 and floats otherwise
  //   buffer_195 drives only 1 and floats otherwise
  //   buffer_196 drives only 1 and floats otherwise
  //   buffer_197 drives only 1 and floats otherwise
  //   buffer_198 drives only 1 and floats otherwise
  //   buffer_199 drives only 1 and floats otherwise
  //   buffer_200 drives only 1 and floats otherwise
  //   buffer_201 drives only 1 and floats otherwise
  //   buffer_202 drives only 1 and floats otherwise
  //   buffer_203 drives only 1 and floats otherwise
  //   buffer_204 drives only 1 and floats otherwise
  //   buffer_205 drives only 1 and floats otherwise
endmodule

// OR
module OR16 (
  input  [15:0] I,
  input  [15:0] Imm,
  output [15:0] Q
);

  buf buffer_1 (Q[0], I[0]);
  buf buffer_2 (Q[1], I[1]);
  buf buffer_3 (Q[2], I[2]);
  buf buffer_4 (Q[3], I[3]);
  buf buffer_5 (Q[4], I[4]);
  buf buffer_6 (Q[5], I[5]);
  buf buffer_7 (Q[6], I[6]);
  buf buffer_8 (Q[7], I[7]);
  buf buffer_9 (Q[8], I[8]);
  buf buffer_10 (Q[9], I[9]);
  buf buffer_11 (Q[10], I[10]);
  buf buffer_12 (Q[11], I[11]);
  buf buffer_13 (Q[12], I[12]);
  buf buffer_14 (Q[13], I[13]);
  buf buffer_15 (Q[14], I[14]);
  buf buffer_16 (Q[15], I[15]);
  buf buffer_17 (Q[0], Imm[0]);
  buf buffer_18 (Q[1], Imm[1]);
  buf buffer_19 (Q[2], Imm[2]);
  buf buffer_20 (Q[3], Imm[3]);
  buf buffer_21 (Q[4], Imm[4]);
  buf buffer_22 (Q[5], Imm[5]);
  buf buffer_23 (Q[6], Imm[6]);
  buf buffer_24 (Q[7], Imm[7]);
  buf buffer_25 (Q[8], Imm[8]);
  buf buffer_26 (Q[9], Imm[9]);
  buf buffer_27 (Q[10], Imm[10]);
  buf buffer_28 (Q[11], Imm[11]);
  buf buffer_29 (Q[12], Imm[12]);
  buf buffer_30 (Q[13], Imm[13]);
  buf buffer_31 (Q[14], Imm[14]);
  buf buffer_32 (Q[15], Imm[15]);

  // Notes on the sheet:
  //   buffer_1 drives only 1 and floats otherwise
  //   buffer_2 drives only 1 and floats otherwise
  //   buffer_3 drives only 1 and floats otherwise
  //   buffer_4 drives only 1 and floats otherwise
  //   buffer_5 drives only 1 and floats otherwise
  //   buffer_6 drives only 1 and floats otherwise
  //   buffer_7 drives only 1 and floats otherwise
  //   buffer_8 drives only 1 and floats otherwise
  //   buffer_9 drives only 1 and floats otherwise
  //   buffer_10 drives only 1 and floats otherwise
  //   buffer_11 drives only 1 and floats otherwise
  //   buffer_12 drives only 1 and floats otherwise
  //   buffer_13 drives only 1 and floats otherwise
  //   buffer_14 drives only 1 and floats otherwise
  //   buffer_15 drives only 1 and floats otherwise
  //   buffer_16 drives only 1 and floats otherwise
  //   buffer_17 drives only 1 and floats otherwise
  //   buffer_18 drives only 1 and floats otherwise
  //   buffer_19 drives only 1 and floats otherwise
  //   buffer_20 drives only 1 and floats otherwise
  //   buffer_21 drives only 1 and floats otherwise
  //   buffer_22 drives only 1 and floats otherwise
  //   buffer_23 drives only 1 and floats otherwise
  //   buffer_24 drives only 1 and floats otherwise
  //   buffer_25 drives only 1 and floats otherwise
  //   buffer_26 drives only 1 and floats otherwise
  //   buffer_27 drives only 1 and floats otherwise
  //   buffer_28 drives only 1 and floats otherwise
  //   buffer_29 drives only 1 and floats otherwise
  //   buffer_30 drives only 1 and floats otherwise
  //   buffer_31 drives only 1 and floats otherwise
  //   buffer_32 drives only 1 and floats otherwise
endmodule

module SHIFT (
  input  SHR4,
  input  SHL4,
  input  SHR1,
  input  SHL1,
  input  ROT,
  input  ZERO,
  input  [3:0] RR,
  input  [15:0] B,
  output Sh,
  output [15:0] O,
  output Csh,
  output [3:0] RR_2
);

  wire buffer_1_out, ROT_2_com, ROT_2_com_2, ROT_3_com, ROT_3_com_2, ROT_4_com, ROT_4_com_2, ROT_5_com,
       ROT_5_com_2, ROT_com, ROT_com_2;

  buf buffer_1 (buffer_1_out, ZERO);
  buf buffer_2 (buffer_1_out, SHL4);
  buf buffer_3 (buffer_1_out, SHR1);
  buf buffer_4 (buffer_1_out, SHL1);
  buf buffer_5 (Sh, SHL1);
  buf buffer_6 (buffer_1_out, SHR4);
  buf buffer_7 (Sh, SHL4);
  buf buffer_8 (Sh, SHR4);
  buf buffer_9 (Sh, SHR1);
  DPDT nEN (.coil(buffer_1_out), .NC(B[0]), .com(O[0]), .NC_2(B[1]), .com_2(O[1]));  // open: NO, NO_2
  DPDT nEN_2 (.coil(buffer_1_out), .NC(B[2]), .com(O[2]), .NC_2(B[3]), .com_2(O[3]));  // open: NO, NO_2
  DPDT nEN_3 (.coil(buffer_1_out), .NC(B[4]), .com(O[4]), .NC_2(B[5]), .com_2(O[5]));  // open: NO, NO_2
  DPDT nEN_4 (.coil(buffer_1_out), .NC(B[6]), .com(O[6]), .NC_2(B[7]), .com_2(O[7]));  // open: NO, NO_2
  DPDT nEN_5 (.coil(buffer_1_out), .NC(B[8]), .com(O[8]), .NC_2(B[9]), .com_2(O[9]));  // open: NO, NO_2
  DPDT nEN_6 (.coil(buffer_1_out), .NC(B[10]), .com(O[10]), .NC_2(B[11]), .com_2(O[11]));  // open: NO, NO_2
  DPDT nEN_7 (.coil(buffer_1_out), .NC(B[12]), .com(O[12]), .NC_2(B[13]), .com_2(O[13]));  // open: NO, NO_2
  DPDT nEN_8 (.coil(buffer_1_out), .NC(B[14]), .com(O[14]), .NC_2(B[15]), .com_2(O[15]));  // open: NO, NO_2
  DPDT u_ROT (.coil(ROT), .com(ROT_com), .NO(RR[0]), .com_2(ROT_com_2), .NO_2(RR[0]));  // open: NC, NC_2
  DPDT RL1 (.coil(SHL1), .com_2(O[0]), .NO_2(ROT_com));  // open: NC, com, NO, NC_2
  DPDT u_SHL1 (.coil(SHL1), .com(O[1]), .NO(B[0]), .com_2(O[2]), .NO_2(B[1]));  // open: NC, NC_2
  DPDT SHL1_2 (.coil(SHL1), .com(O[3]), .NO(B[2]), .com_2(O[4]), .NO_2(B[3]));  // open: NC, NC_2
  DPDT SHL1_3 (.coil(SHL1), .com(O[5]), .NO(B[4]), .com_2(O[6]), .NO_2(B[5]));  // open: NC, NC_2
  DPDT SHL1_4 (.coil(SHL1), .com(O[7]), .NO(B[6]), .com_2(O[8]), .NO_2(B[7]));  // open: NC, NC_2
  DPDT SHL1_5 (.coil(SHL1), .com(O[9]), .NO(B[8]), .com_2(O[10]), .NO_2(B[9]));  // open: NC, NC_2
  DPDT SHL1_6 (.coil(SHL1), .com(O[11]), .NO(B[10]), .com_2(O[12]), .NO_2(B[11]));  // open: NC, NC_2
  DPDT SHL1_7 (.coil(SHL1), .com(O[13]), .NO(B[12]), .com_2(O[14]), .NO_2(B[13]));  // open: NC, NC_2
  DPDT SHL1_8 (.coil(SHL1), .com(O[15]), .NO(B[14]), .com_2(RR_2[0]), .NO_2(B[15]));  // open: NC, NC_2
  DPDT u_SHR1 (.coil(SHR1), .com(RR_2[0]), .NO(B[0]), .com_2(O[0]), .NO_2(B[1]));  // open: NC, NC_2
  DPDT SHR1_2 (.coil(SHR1), .com(O[1]), .NO(B[2]), .com_2(O[2]), .NO_2(B[3]));  // open: NC, NC_2
  DPDT SHR1_3 (.coil(SHR1), .com(O[3]), .NO(B[4]), .com_2(O[4]), .NO_2(B[5]));  // open: NC, NC_2
  DPDT SHR1_4 (.coil(SHR1), .com(O[5]), .NO(B[6]), .com_2(O[6]), .NO_2(B[7]));  // open: NC, NC_2
  DPDT SHR1_5 (.coil(SHR1), .com(O[7]), .NO(B[8]), .com_2(O[8]), .NO_2(B[9]));  // open: NC, NC_2
  DPDT SHR1_6 (.coil(SHR1), .com(O[9]), .NO(B[10]), .com_2(O[10]), .NO_2(B[11]));  // open: NC, NC_2
  DPDT SHR1_7 (.coil(SHR1), .com(O[11]), .NO(B[12]), .com_2(O[12]), .NO_2(B[13]));  // open: NC, NC_2
  DPDT SHR1_8 (.coil(SHR1), .com(O[13]), .NO(B[14]), .com_2(O[14]), .NO_2(B[15]));  // open: NC, NC_2
  DPDT RR1 (.coil(SHR1), .com(O[15]), .NO(ROT_com_2));  // open: NC, NC_2, com_2, NO_2
  buf buffer_10 (Csh, RR_2[0]);
  buf buffer_11 (Csh, RR_2[0]);
  DPDT ROT_2 (.coil(ROT), .com(ROT_2_com), .NO(RR[0]), .com_2(ROT_2_com_2), .NO_2(RR[1]));  // open: NC, NC_2
  DPDT ROT_3 (.coil(ROT), .com(ROT_3_com), .NO(RR[2]), .com_2(ROT_3_com_2), .NO_2(RR[3]));  // open: NC, NC_2
  DPDT ROT_4 (.coil(ROT), .com(ROT_4_com), .NO(RR[0]), .com_2(ROT_4_com_2), .NO_2(RR[1]));  // open: NC, NC_2
  DPDT ROT_5 (.coil(ROT), .com(ROT_5_com), .NO(RR[2]), .com_2(ROT_5_com_2), .NO_2(RR[3]));  // open: NC, NC_2
  DPDT RL4 (.coil(SHL4), .com(O[0]), .NO(ROT_2_com), .com_2(O[1]), .NO_2(ROT_2_com_2));  // open: NC, NC_2
  DPDT RL4_2 (.coil(SHL4), .com(O[2]), .NO(ROT_3_com), .com_2(O[3]), .NO_2(ROT_3_com_2));  // open: NC, NC_2
  DPDT u_SHL4 (.coil(SHL4), .com(O[4]), .NO(B[0]), .com_2(O[5]), .NO_2(B[1]));  // open: NC, NC_2
  DPDT SHL4_2 (.coil(SHL4), .com(O[6]), .NO(B[2]), .com_2(O[7]), .NO_2(B[3]));  // open: NC, NC_2
  DPDT SHL4_3 (.coil(SHL4), .com(O[8]), .NO(B[4]), .com_2(O[9]), .NO_2(B[5]));  // open: NC, NC_2
  DPDT SHL4_4 (.coil(SHL4), .com(O[10]), .NO(B[6]), .com_2(O[11]), .NO_2(B[7]));  // open: NC, NC_2
  DPDT SHL4_5 (.coil(SHL4), .com(O[12]), .NO(B[8]), .com_2(O[13]), .NO_2(B[9]));  // open: NC, NC_2
  DPDT SHL4_6 (.coil(SHL4), .com(O[14]), .NO(B[10]), .com_2(O[15]), .NO_2(B[11]));  // open: NC, NC_2
  DPDT SHL4_7 (.coil(SHL4), .com(RR_2[0]), .NO(B[12]), .com_2(RR_2[1]), .NO_2(B[13]));  // open: NC, NC_2
  DPDT SHL4_8 (.coil(SHL4), .com(RR_2[2]), .NO(B[14]), .com_2(RR_2[3]), .NO_2(B[15]));  // open: NC, NC_2
  DPDT u_SHR4 (.coil(SHR4), .com(RR_2[0]), .NO(B[0]), .com_2(RR_2[1]), .NO_2(B[1]));  // open: NC, NC_2
  DPDT SHR4_2 (.coil(SHR4), .com(RR_2[2]), .NO(B[2]), .com_2(RR_2[3]), .NO_2(B[3]));  // open: NC, NC_2
  DPDT SHR4_3 (.coil(SHR4), .com(O[0]), .NO(B[4]), .com_2(O[1]), .NO_2(B[5]));  // open: NC, NC_2
  DPDT SHR4_4 (.coil(SHR4), .com(O[2]), .NO(B[6]), .com_2(O[3]), .NO_2(B[7]));  // open: NC, NC_2
  DPDT SHR4_5 (.coil(SHR4), .com(O[4]), .NO(B[8]), .com_2(O[5]), .NO_2(B[9]));  // open: NC, NC_2
  DPDT SHR4_6 (.coil(SHR4), .com(O[6]), .NO(B[10]), .com_2(O[7]), .NO_2(B[11]));  // open: NC, NC_2
  DPDT SHR4_7 (.coil(SHR4), .com(O[8]), .NO(B[12]), .com_2(O[9]), .NO_2(B[13]));  // open: NC, NC_2
  DPDT SHR4_8 (.coil(SHR4), .com(O[10]), .NO(B[14]), .com_2(O[11]), .NO_2(B[15]));  // open: NC, NC_2
  DPDT RR4 (.coil(SHR4), .com(O[12]), .NO(ROT_4_com), .com_2(O[13]), .NO_2(ROT_4_com_2));  // open: NC, NC_2
  DPDT RR4_2 (.coil(SHR4), .com(O[14]), .NO(ROT_5_com), .com_2(O[15]), .NO_2(ROT_5_com_2));  // open: NC, NC_2
  buf buffer_12 (Csh, RR_2[0]);
  buf buffer_13 (Csh, RR_2[1]);
  buf buffer_14 (Csh, RR_2[2]);
  buf buffer_15 (Csh, RR_2[3]);
  buf buffer_16 (Csh, RR_2[0]);
  buf buffer_17 (Csh, RR_2[1]);
  buf buffer_18 (Csh, RR_2[2]);
  buf buffer_19 (Csh, RR_2[3]);

  // Notes on the sheet:
  //   buffer_1 drives only 1 and floats otherwise
  //   buffer_2 drives only 1 and floats otherwise
  //   buffer_3 drives only 1 and floats otherwise
  //   buffer_4 drives only 1 and floats otherwise
  //   buffer_5 drives only 1 and floats otherwise
  //   buffer_6 drives only 1 and floats otherwise
  //   buffer_7 drives only 1 and floats otherwise
  //   buffer_8 drives only 1 and floats otherwise
  //   buffer_9 drives only 1 and floats otherwise
  //   buffer_10 drives only 1 and floats otherwise
  //   buffer_11 drives only 1 and floats otherwise
  //   buffer_12 drives only 1 and floats otherwise
  //   buffer_13 drives only 1 and floats otherwise
  //   buffer_14 drives only 1 and floats otherwise
  //   buffer_15 drives only 1 and floats otherwise
  //   buffer_16 drives only 1 and floats otherwise
  //   buffer_17 drives only 1 and floats otherwise
  //   buffer_18 drives only 1 and floats otherwise
  //   buffer_19 drives only 1 and floats otherwise
endmodule

// 0/1
module Buffer1 (
  input  in_1,
  output out_2
);

  wire buffer_1_out;

  buf buffer_1 (buffer_1_out, in_1);
  Pull_Resistor pull_resistor_1 (.node(buffer_1_out));
  buf buffer_2 (out_2, buffer_1_out);

  // Notes on the sheet:
  //   buffer_1 drives only 1 and floats otherwise
endmodule

// 0/1
module Buffer16 (
  input  [15:0] in_1,
  output [15:0] out_2
);

  wire buffer_1_out, buffer_2_out, buffer_3_out, buffer_4_out, buffer_5_out, buffer_6_out, buffer_7_out,
       buffer_8_out, buffer_9_out, buffer_10_out, buffer_11_out, buffer_12_out, buffer_13_out, buffer_14_out,
       buffer_15_out, buffer_16_out;

  buf buffer_1 (buffer_1_out, in_1[0]);
  buf buffer_2 (buffer_2_out, in_1[2]);
  buf buffer_3 (buffer_3_out, in_1[4]);
  buf buffer_4 (buffer_4_out, in_1[6]);
  buf buffer_5 (buffer_5_out, in_1[8]);
  buf buffer_6 (buffer_6_out, in_1[10]);
  buf buffer_7 (buffer_7_out, in_1[12]);
  buf buffer_8 (buffer_8_out, in_1[14]);
  buf buffer_9 (buffer_9_out, in_1[1]);
  buf buffer_10 (buffer_10_out, in_1[3]);
  buf buffer_11 (buffer_11_out, in_1[5]);
  buf buffer_12 (buffer_12_out, in_1[7]);
  buf buffer_13 (buffer_13_out, in_1[9]);
  buf buffer_14 (buffer_14_out, in_1[11]);
  buf buffer_15 (buffer_15_out, in_1[13]);
  buf buffer_16 (buffer_16_out, in_1[15]);
  Pull_Resistor pull_resistor_1 (.node(buffer_1_out));
  Pull_Resistor pull_resistor_2 (.node(buffer_11_out));
  Pull_Resistor pull_resistor_3 (.node(buffer_9_out));
  Pull_Resistor pull_resistor_4 (.node(buffer_2_out));
  Pull_Resistor pull_resistor_5 (.node(buffer_10_out));
  Pull_Resistor pull_resistor_6 (.node(buffer_3_out));
  Pull_Resistor pull_resistor_7 (.node(buffer_4_out));
  Pull_Resistor pull_resistor_8 (.node(buffer_7_out));
  Pull_Resistor pull_resistor_9 (.node(buffer_5_out));
  Pull_Resistor pull_resistor_10 (.node(buffer_13_out));
  Pull_Resistor pull_resistor_11 (.node(buffer_12_out));
  Pull_Resistor pull_resistor_12 (.node(buffer_6_out));
  Pull_Resistor pull_resistor_13 (.node(buffer_15_out));
  Pull_Resistor pull_resistor_14 (.node(buffer_14_out));
  buf buffer_17 (out_2[0], buffer_1_out);
  buf buffer_18 (out_2[2], buffer_2_out);
  buf buffer_19 (out_2[4], buffer_3_out);
  buf buffer_20 (out_2[6], buffer_4_out);
  buf buffer_21 (out_2[8], buffer_5_out);
  buf buffer_22 (out_2[10], buffer_6_out);
  buf buffer_23 (out_2[12], buffer_7_out);
  buf buffer_24 (out_2[14], buffer_8_out);
  Pull_Resistor pull_resistor_15 (.node(buffer_8_out));
  Pull_Resistor pull_resistor_16 (.node(buffer_16_out));
  buf buffer_25 (out_2[1], buffer_9_out);
  buf buffer_26 (out_2[3], buffer_10_out);
  buf buffer_27 (out_2[5], buffer_11_out);
  buf buffer_28 (out_2[7], buffer_12_out);
  buf buffer_29 (out_2[9], buffer_13_out);
  buf buffer_30 (out_2[11], buffer_14_out);
  buf buffer_31 (out_2[13], buffer_15_out);
  buf buffer_32 (out_2[15], buffer_16_out);

  // Notes on the sheet:
  //   buffer_1 drives only 1 and floats otherwise
  //   buffer_2 drives only 1 and floats otherwise
  //   buffer_3 drives only 1 and floats otherwise
  //   buffer_4 drives only 1 and floats otherwise
  //   buffer_5 drives only 1 and floats otherwise
  //   buffer_6 drives only 1 and floats otherwise
  //   buffer_7 drives only 1 and floats otherwise
  //   buffer_8 drives only 1 and floats otherwise
  //   buffer_9 drives only 1 and floats otherwise
  //   buffer_10 drives only 1 and floats otherwise
  //   buffer_11 drives only 1 and floats otherwise
  //   buffer_12 drives only 1 and floats otherwise
  //   buffer_13 drives only 1 and floats otherwise
  //   buffer_14 drives only 1 and floats otherwise
  //   buffer_15 drives only 1 and floats otherwise
  //   buffer_16 drives only 1 and floats otherwise
endmodule

// EA16
module ADD16_NotUsed (
  input  ldB,
  input  add,
  input  [15:0] I,
  input  [15:0] Imm,
  output [15:0] Q
);

  wire addbase4bit_notused_1_cout, addbase4bit_notused_2_cout, addbase4bit_notused_3_cout;

  ADDBase4Bit_NotUsed addbase4bit_notused_1 (
    .A(I[3:0]), .B(Imm[3:0]), .Q(Q[3:0]), .Cout(addbase4bit_notused_1_cout), .ldB(ldB), .add(add));  // open: Cin
  ADDBase4Bit_NotUsed addbase4bit_notused_2 (
    .A(I[7:4]), .B(Imm[7:4]), .Q(Q[7:4]), .Cin(addbase4bit_notused_1_cout),
    .Cout(addbase4bit_notused_2_cout), .ldB(ldB), .add(add));
  ADDBase4Bit_NotUsed addbase4bit_notused_3 (
    .A(I[11:8]), .B(Imm[11:8]), .Q(Q[11:8]), .Cin(addbase4bit_notused_2_cout),
    .Cout(addbase4bit_notused_3_cout), .ldB(ldB), .add(add));
  ADDBase4Bit_NotUsed addbase4bit_notused_4 (
    .A(I[15:12]), .B(Imm[15:12]), .Q(Q[15:12]), .Cin(addbase4bit_notused_3_cout), .ldB(ldB), .add(add));  // open: Cout
endmodule

// ADD1
module ADDBase1Bit_NotUsed (
  input  B,
  input  A,
  input  ldB,
  input  add,
  input  Cin,
  output Cout,
  output Q
);

  wire A_nc, A_no, A_no_2, B_com, B_com_2, buffer_1_out, dpdtr_1_nc, dpdtr_1_no;

  DPDTr u_A (.coil(A), .com(add), .com_2(add), .NC(A_nc), .NO(A_no), .NO_2(A_no_2));  // open: NC_2
  buf buffer_1 (buffer_1_out, ldB);
  buf buffer_2 (buffer_1_out, A_nc);
  DPDT u_B (.coil(B), .NC(A_no), .com(B_com), .NO(buffer_1_out), .com_2(B_com_2), .NO_2(A_no_2));  // open: NC_2
  DPDTr dpdtr_1 (.coil(Cin), .com(1'b1), .NC(dpdtr_1_nc), .NO(dpdtr_1_no));  // open: com_2, NC_2, NO_2
  DPDT P (.coil(B_com), .NC(B_com_2), .com(Cout), .NO(Cin), .NC_2(dpdtr_1_no), .com_2(Q), .NO_2(dpdtr_1_nc));

  // Notes on the sheet:
  //   buffer_1 drives only 1 and floats otherwise
  //   buffer_2 drives only 1 and floats otherwise
endmodule

// ADD4
module ADDBase4Bit_NotUsed (
  input  ldB,
  input  add,
  input  [3:0] A,
  input  [3:0] B,
  input  Cin,
  output Cout,
  output [3:0] Q
);

  wire addbase1bit_notused_1_cout, addbase1bit_notused_2_cout, addbase1bit_notused_3_cout;

  ADDBase1Bit_NotUsed addbase1bit_notused_1 (
    .B(B[0]), .A(A[0]), .Cin(Cin), .Cout(addbase1bit_notused_1_cout), .Q(Q[0]), .add(add), .ldB(ldB));
  ADDBase1Bit_NotUsed addbase1bit_notused_2 (
    .B(B[1]), .A(A[1]), .Cin(addbase1bit_notused_1_cout), .Cout(addbase1bit_notused_2_cout), .Q(Q[1]),
    .add(add), .ldB(ldB));
  ADDBase1Bit_NotUsed addbase1bit_notused_3 (
    .B(B[2]), .A(A[2]), .Cin(addbase1bit_notused_2_cout), .Cout(addbase1bit_notused_3_cout), .Q(Q[2]),
    .add(add), .ldB(ldB));
  ADDBase1Bit_NotUsed addbase1bit_notused_4 (
    .B(B[3]), .A(A[3]), .Cin(addbase1bit_notused_3_cout), .Cout(Cout), .Q(Q[3]), .add(add), .ldB(ldB));
endmodule

module Nou_6 (
  input  [3:0] I,
  input  EN,
  input  Cin,
  input  EN_2,
  output [3:0] Q
);

  wire Bit1_2_no, Bit1_com_2, Bit1_nc_2, Bit1_no_2, Bit2_2_no, Bit2_nc_2, Bit2_no, Bit2_no_2, Bit3_no,
       Bit3_no_2, EN_nc, EN_no;

  DPDTr u_EN (.coil(EN), .com(1'b1), .NC(EN_nc), .NO(EN_no));  // open: com_2, NC_2, NO_2
  // DPDTr Cin: pin names not known
  DPDTr Bit3 (.coil(I[3]), .com(Bit1_no_2), .com_2(EN_nc), .NO(Bit3_no), .NO_2(Bit3_no_2));  // open: NC, NC_2
  DPDTr Bit2 (.coil(I[2]), .com(Bit3_no), .com_2(EN_no), .NO(Bit2_no), .NC_2(Bit2_nc_2), .NO_2(Bit2_no_2));  // open: NC
  DPDTr Bit2_2 (.coil(I[2]), .com(EN_nc), .NO(Bit2_2_no));  // open: com_2, NC, NC_2, NO_2
  buf buffer_1 (Q[3], Bit3_no_2);
  buf buffer_2 (Q[3], Bit2_no);
  DPDTb Bit1 (
    .coil(I[1]), .com(EN_no), .NC(Bit2_no_2), .NO(Bit2_nc_2), .NC_2(Bit1_nc_2), .NO_2(Bit1_no_2),
    .com_2(Bit1_com_2));
  DPDTr Bit1_2 (.coil(I[1]), .com(EN_nc), .NO(Bit1_2_no));  // open: com_2, NC, NC_2, NO_2
  buf buffer_3 (Q[1], Bit1_nc_2);
  buf buffer_4 (Q[1], Bit1_2_no);
  buf buffer_5 (Q[2], Bit2_2_no);
  buf buffer_6 (Q[2], Bit1_com_2);

  assign Q[0] = I[0];

  // Notes on the sheet:
  //   buffer_1 drives only 1 and floats otherwise
  //   buffer_2 drives only 1 and floats otherwise
  //   buffer_3 drives only 1 and floats otherwise
  //   buffer_4 drives only 1 and floats otherwise
  //   buffer_5 drives only 1 and floats otherwise
  //   buffer_6 drives only 1 and floats otherwise
endmodule
