// Logisim project RELAYS.circ as structural Verilog: 7 circuits, main circuit DPDT
module Main (
  input  in_1,
  input  in_2
);

  wire buffer_1_out, buffer_2_out;

  DPDTr dpdtr_1 ();  // open: coil, com, com_2, NC, NO, NC_2, NO_2
  DPDTh dpdth_1 ();  // open: coil, NC, NO, NC_2, NO_2, com, com_2
  buf buffer_1 (buffer_1_out, in_1);
  buf buffer_2 (buffer_2_out, in_2);
  DPDT dpdt_1 (.coil(buffer_1_out), .com(buffer_1_out), .NO(buffer_2_out));  // open: NC, NC_2, com_2, NO_2
  DPDThb dpdthb_1 ();  // open: coil, NC, NO, com, com_2, NC_2, NO_2

  // Notes on the sheet:
  //   buffer_1 drives only 1 and floats otherwise
  //   buffer_2 drives only 1 and floats otherwise
endmodule

module DPDT (
  input  coil,
  input  NC,
  input  NO,
  input  NC_2,
  input  NO_2,
  output com,
  output com_2
);

  wire buffer_1_out;

  buf buffer_1 (buffer_1_out, coil);
  Pull_Resistor pull_resistor_1 (.node(buffer_1_out));
  Multiplexer #(.enable("false")) multiplexer_1 (.in0(NC), .in1(NO), .out(com), .sel(buffer_1_out));
  Multiplexer #(.enable("false")) multiplexer_2 (.in0(NC_2), .in1(NO_2), .out(com_2), .sel(buffer_1_out));

  // Notes on the sheet:
  //   buffer_1 drives only 1 and floats otherwise
endmodule

module DPDTr (
  input  coil,
  input  com,
  input  com_2,
  output NC,
  output NO,
  output NC_2,
  output NO_2
);

  wire buffer_1_out;

  buf buffer_1 (buffer_1_out, coil);
  Demultiplexer #(.tristate("true"), .enable("false")) demultiplexer_1 (
    .out0(NC), .out1(NO), .in(com), .sel(buffer_1_out));
  Demultiplexer #(.tristate("true"), .enable("false")) demultiplexer_2 (
    .out0(NC_2), .out1(NO_2), .in(com_2), .sel(buffer_1_out));
  Pull_Resistor pull_resistor_1 (.node(buffer_1_out));

  // Notes on the sheet:
  //   buffer_1 drives only 1 and floats otherwise
endmodule

module SPDT (
  input  coil,
  input  NC,
  input  NO,
  output com
);

  Pull_Resistor pull_resistor_1 (.node(coil));
  Multiplexer #(.enable("false")) multiplexer_1 (.in0(NC), .in1(NO), .out(com), .sel(coil));
endmodule

module DPDTb (
  input  coil,
  input  com,
  input  NC,
  input  NO,
  output NC_2,
  output NO_2,
  output com_2
);

  wire buffer_1_out;

  buf buffer_1 (buffer_1_out, coil);
  Demultiplexer #(.tristate("true"), .enable("false")) demultiplexer_1 (
    .out0(NC_2), .out1(NO_2), .in(com), .sel(buffer_1_out));
  Pull_Resistor pull_resistor_1 (.node(buffer_1_out));
  Multiplexer #(.enable("false")) multiplexer_1 (.in0(NC), .in1(NO), .out(com_2), .sel(buffer_1_out));

  // Notes on the sheet:
  //   buffer_1 drives only 1 and floats otherwise
endmodule

module DPDTh (
  input  coil,
  input  NC,
  input  NO,
  input  NC_2,
  input  NO_2,
  output com,
  output com_2
);

  wire buffer_3_out, multiplexer_1_out;

  buf buffer_1 (com, multiplexer_1_out);
  buf buffer_2 (com, coil);
  buf buffer_3 (buffer_3_out, com);
  Pull_Resistor pull_resistor_1 (.node(buffer_3_out));
  Multiplexer #(.enable("false")) multiplexer_1 (.in0(NC), .in1(NO), .out(multiplexer_1_out), .sel(buffer_3_out));
  Multiplexer #(.enable("false")) multiplexer_2 (.in0(NC_2), .in1(NO_2), .out(com_2), .sel(buffer_3_out));

  // Notes on the sheet:
  //   buffer_1 drives only 1 and floats otherwise
  //   buffer_2 drives only 1 and floats otherwise
  //   buffer_3 drives only 1 and floats otherwise
endmodule

module DPDThb (
  input  coil,
  input  NC,
  input  NO,
  input  com,
  output com_2,
  output NC_2,
  output NO_2
);

  wire buffer_3_out, multiplexer_1_out;

  buf buffer_1 (com_2, multiplexer_1_out);
  buf buffer_2 (com_2, coil);
  buf buffer_3 (buffer_3_out, com_2);
  Demultiplexer #(.tristate("true"), .enable("false")) demultiplexer_1 (
    .out0(NC_2), .out1(NO_2), .in(com), .sel(buffer_3_out));
  Pull_Resistor pull_resistor_1 (.node(buffer_3_out));
  Multiplexer #(.enable("false")) multiplexer_1 (.in0(NC), .in1(NO), .out(multiplexer_1_out), .sel(buffer_3_out));

  // Notes on the sheet:
  //   buffer_1 drives only 1 and floats otherwise
  //   buffer_2 drives only 1 and floats otherwise
  //   buffer_3 drives only 1 and floats otherwise
endmodule
