// Logisim project G6A-Risc.circ as structural Verilog: 32 circuits, main circuit REG16bit
module Main (
  input  Reset,
  input  Run,
  output [15:0] out_3,
  output [15:0] out_4,
  output [15:0] out_5,
  output [15:0] out_6,
  output [15:0] A,
  output [15:0] B,
  output [15:0] out_9,
  output [15:0] out_10,
  output [15:0] out_11,
  output [15:0] out_12,
  output [15:0] out_13,
  output [15:0] out_14,
  output [15:0] Inc,
  output [15:0] out_16,
  output [10:0] out_17,
  output [15:0] PC,
  output [15:0] out_19,
  output [15:0] out_20
);

  wire A_ADD, A_AND, A_C, A_C1, A_D6_minus, A_D6_plus, A_LDA, A_LDB, A_OR, A_ROT1, A_ROT4, A_RSB, A_SELF,
       A_SELT, A_SL1, A_SL4, A_SR1, A_SR4, A_SUB, A_WiF, A_WiT, A_XOR, A_ZERO, alu16bit_1_cout,
       alu16bit_1_nt_2, alu16bit_1_nw, alu16bit_1_nz, and_1_out, buffer1_1_out_2, buffer1_2_out_2,
       buffer1_3_out_2, buffer1_4_out_2, buffer_1_out, buffer_2_out, buffer_3_out, buffer_4_out, clock_1_out,
       CLR1, CLR2, decoder_1_st, HLT, IE_D, IE_LK, IE_MAR, IE_PFR, IE_R0, IE_R1, IE_R2, IE_R3, IE_R4, IE_R5,
       IE_R6, IE_R7, LDPM, not_1_out, OE_M, PH0, PH1, PH2, S_BUS, S_D, S_IMM, S_P, SA_R0, SA_R1, SA_R2,
       SA_R3, SA_R4, SA_R5, SA_R6, SA_R7, SB_R0, SB_R1, SB_R2, SB_R3, SB_R4, SB_R5, SB_R6, SB_R7,
       shift_1_csh, shift_1_sh, SR_c_2, SR_nt_2, SR_nz_2, WE_M, WI_R, WI_SR;
  wire [1:0] decoder_1_fn, decoder_1_ty;
  wire [2:0] ALUR_nt_2, decoder_1_op, decoder_1_ri, decoder_1_rj, decoder_1_rk;
  wire [7:0] A_CC;
  wire [10:0] Imm11;
  wire [15:0] A0_out, A1_out, add16_1_q, alu16bit_1_o, ALUR_out, buffer16_1_out_2, buffer16_2_out_2,
       buffer16_3_out_2, IR_out, MAR_out, R0_out, R1_out, R2_out, R3_out, reg_link_1_out, reg_pc_1_out, S0_a,
       S0_b;

  Clock_part clock_1 (.out(clock_1_out));
  Buffer16 buffer16_1 (.in_1(reg_pc_1_out), .out_2(buffer16_1_out_2));
  REG16bit R0 (.IE(IE_R0), .OE(1'b1), .In(ALUR_out), .Test(out_3), .CLR(CLR2), .Out(R0_out), .nWE(WI_R));
  REG16bit R1 (.IE(IE_R1), .OE(1'b1), .In(ALUR_out), .Test(out_5), .CLR(CLR2), .Out(R1_out), .nWE(WI_R));
  REG16bit R2 (.IE(IE_R2), .OE(1'b1), .In(ALUR_out), .Test(out_6), .CLR(CLR2), .Out(R2_out), .nWE(WI_R));
  REG16bit R3 (.IE(IE_R3), .OE(1'b1), .In(ALUR_out), .Test(out_9), .CLR(CLR2), .Out(R3_out), .nWE(WI_R));
  REG16bit A0 (.IE(IE_R4), .OE(1'b1), .In(ALUR_out), .Test(out_11), .CLR(CLR2), .Out(A0_out), .nWE(WI_R));
  REG16bit A1 (.IE(IE_R5), .OE(1'b1), .In(ALUR_out), .Test(out_13), .CLR(CLR2), .Out(A1_out), .nWE(WI_R));
  REG_LINK reg_link_1 (
    .IElk(IE_LK), .CLR(CLR2), .OE(1'b1), .InLK(Inc), .In(ALUR_out), .Out(reg_link_1_out), .Test(out_14),
    .CLRlk(CLR1), .nWE(WI_R), .IE(IE_R6));
  REG_PC reg_pc_1 (
    .OE(1'b1), .In(ALUR_out), .CLR1(CLR1), .Out(reg_pc_1_out), .Test(PC), .PH1(PH1), .PH(PH2), .nWE(WI_R),
    .IE(IE_R7), .CLR(CLR2), .Out_plus(Inc), .nWE1(LDPM));
  ROM #(.addrWidth(16), .dataWidth(16)) rom_1 (.addr(buffer16_1_out_2), .data(out_20), .sel(1'b1));
  Sequencer sequencer_1 (
    .Reset(Reset), .CLKIn(clock_1_out), .PH1(PH1), .CLR1(CLR1), .nHalt(Run), .PH2(PH2), .CLR2(CLR2), .PH0(PH0));  // open: Test, Test_3, Test_2, Test_4
  BusSelect S0 (.SA(SA_R0), .SB(SB_R0), .I1(R0_out), .A(S0_a), .B(S0_b));
  BusSelect S1 (.SA(SA_R1), .SB(SB_R1), .I1(R1_out), .A(S0_a), .B(S0_b));
  BusSelect S2 (.SA(SA_R2), .SB(SB_R2), .I1(R2_out), .A(S0_a), .B(S0_b));
  BusSelect S3 (.SA(SA_R3), .SB(SB_R3), .I1(R3_out), .A(S0_a), .B(S0_b));
  BusSelect S4 (.SA(SA_R4), .SB(SB_R4), .I1(A0_out), .A(S0_a), .B(S0_b));
  BusSelect S5 (.SA(SA_R5), .SB(SB_R5), .I1(A1_out), .A(S0_a), .B(S0_b));
  BusSelect S6 (.SA(SA_R6), .SB(SB_R6), .I1(reg_link_1_out), .A(S0_a), .B(S0_b));
  BusSelect S7 (.SA(SA_R7), .SB(SB_R7), .I1(reg_pc_1_out), .A(S0_a), .B(S0_b));
  Transceiver transceiver_1 (.S0(S_P), .I0(out_20), .O0(S0_b));  // open: S1, I1, O1
  Buffer1 buffer1_1 (.in_1(WI_R), .out_2(buffer1_1_out_2));
  Buffer1 buffer1_2 (.in_1(WE_M), .out_2(buffer1_2_out_2));
  Buffer1 buffer1_3 (.in_1(CLR2), .out_2(buffer1_3_out_2));
  Buffer1 buffer1_4 (.in_1(OE_M), .out_2(buffer1_4_out_2));
  REG_STATUS SR (
    .IE(PH2), .CLR(CLR2), .OE(1'b1), .NZ(ALUR_nt_2[1]), .C(ALUR_nt_2[2]), .NT(ALUR_nt_2[0]), .NZ_2(SR_nz_2),
    .C_2(SR_c_2), .NT_2(SR_nt_2), .nWE(WI_SR));
  SHIFT shift_1 (
    .SHR1(A_SR1), .SHL1(A_SL1), .A(S0_a), .K(S0_b), .SHR4(A_SR4), .SHL4(A_SL4), .Csh(shift_1_csh), .O(A),
    .Sh(shift_1_sh), .ZERO(A_ZERO), .ROT1(A_ROT1), .ROT4(A_ROT4));
  InputSelect inputselect_1 (.EN1(S_IMM), .I1(out_16), .I0(S0_b), .A(B), .EN0(S_BUS));
  ADD16 add16_1 (.B(S0_b), .Imm(out_16), .Q(add16_1_q));
  not not_1 (not_1_out, buffer1_1_out_2);
  REG_PFIX reg_pfix_1 (.IE(IE_PFR), .CLR(CLR2), .OE(1'b1), .In(Imm11), .Out(out_16[15:5]), .Test(out_17));
  REG16bit IR (.IE(PH0), .OE(1'b1), .In(out_20), .Test(out_19), .CLR(CLR1), .Out(IR_out), .nWE(LDPM));
  Buffer16 buffer16_2 (.in_1(ALUR_out), .out_2(buffer16_2_out_2));
  buf buffer_1 (buffer_1_out, and_1_out);
  and and_1 (and_1_out, not_1_out, buffer1_2_out_2, buffer1_3_out_2);
  buf buffer_2 (buffer_2_out, buffer_1_out);
  Transceiver transceiver_2 (.S0(IE_D), .S1(S_D), .I0(buffer16_2_out_2), .I1(out_10), .O0(out_10), .O1(B));
  buf buffer_3 (buffer_3_out, buffer_2_out);
  buf buffer_4 (buffer_4_out, buffer_3_out);
  Decoder decoder_1 (
    .I(IR_out), .Op(decoder_1_op), .FN(decoder_1_fn), .Ri(decoder_1_ri), .imm5(out_16[4:0]), .pfix11(Imm11),
    .Ty(decoder_1_ty), .St(decoder_1_st), .Rj(decoder_1_rj), .Rk(decoder_1_rk));
  ALU16Bit alu16bit_1 (
    .And(A_AND), .Or(A_OR), .Xor(A_XOR), .Add(A_ADD), .Sub(A_SUB), .Rsb(A_RSB), .CIn(SR_c_2), .A(A), .B(B),
    .Cout(alu16bit_1_cout), .O(alu16bit_1_o), .LdA(A_LDA), .LdB(A_LDB), .NZIn(SR_nz_2), .CC_8(A_CC),
    .NT_2(alu16bit_1_nt_2), .NZ(alu16bit_1_nz), .NT(SR_nt_2), .SelT(A_SELT), .SH(shift_1_sh),
    .Csh(shift_1_csh), .SelF(A_SELF), .A_C(A_C), .A_C1(A_C1), .A_D6_plus(A_D6_plus), .A_D6_minus(A_D6_minus),
    .WiT(A_WiT), .WiF(A_WiF), .NW(alu16bit_1_nw));
  REG16bit MAR (.IE(IE_MAR), .OE(1'b1), .In(add16_1_q), .Test(out_12), .CLR(CLR1), .Out(MAR_out));  // open: nWE
  Buffer16 buffer16_3 (.in_1(MAR_out), .out_2(buffer16_3_out_2));
  InstDecoder instdecoder_1 (
    .Op(decoder_1_op), .Fn_Ak(decoder_1_fn), .IE_R7(IE_R7), .IE_R6(IE_R6), .IE_R5(IE_R5), .IE_R4(IE_R4),
    .IE_R3(IE_R3), .IE_R2(IE_R2), .IE_R0(IE_R0), .SA_R7(SA_R7), .SA_R6(SA_R6), .SA_R5(SA_R5), .SA_R4(SA_R4),
    .SA_R3(SA_R3), .SA_R2(SA_R2), .SA_R1(SA_R1), .SA_R0(SA_R0), .IE_R1(IE_R1), .Rj(decoder_1_rj),
    .Rk(decoder_1_rk), .SB_R7(SB_R7), .SB_R6(SB_R6), .SB_R5(SB_R5), .SB_R4(SB_R4), .SB_R3(SB_R3),
    .SB_R2(SB_R2), .SB_R1(SB_R1), .SB_R0(SB_R0), .Ty(decoder_1_ty), .PH1(PH1), .PH2(PH2), .St(decoder_1_st),
    .IE_D(IE_D), .S_IMM(S_IMM), .IE_MAR(IE_MAR), .WE_M(WE_M), .OE_M(OE_M), .S_BUS(S_BUS), .WI_SR(WI_SR),
    .A_C(A_C), .A_C1(A_C1), .A_D6_plus(A_D6_plus), .A_D6_minus(A_D6_minus), .A_ZERO(A_ZERO), .A_LDB(A_LDB),
    .A_SELT(A_SELT), .A_SELF(A_SELF), .A_ADD(A_ADD), .A_SUB(A_SUB), .A_RSB(A_RSB), .A_AND(A_AND),
    .A_OR(A_OR), .A_XOR(A_XOR), .A_SR1(A_SR1), .A_SR4(A_SR4), .A_SL1(A_SL1), .A_SL4(A_SL4), .A_ROT1(A_ROT1),
    .A_ROT4(A_ROT4), .IE_PFR(IE_PFR), .A_CC(A_CC), .IE_LK(IE_LK), .A_WIT(A_WiT), .A_WIF(A_WiF), .HLT(HLT),
    .Ri_CC(decoder_1_ri), .A_LDA(A_LDA), .S_D(S_D), .CLR1(CLR1), .CLR2(CLR2), .S_P(S_P), .LPDM(LDPM));
  REG_ALU ALUR (
    .IE(PH1), .CLR(CLR1), .OE(1'b1), .NZ(alu16bit_1_nz), .C(alu16bit_1_cout), .NT(alu16bit_1_nt_2),
    .In(alu16bit_1_o), .NZ_2(ALUR_nt_2[1]), .C_2(ALUR_nt_2[2]), .Out(ALUR_out), .Test(out_4),
    .NW(alu16bit_1_nw), .NW_2(WI_R), .NT_2(ALUR_nt_2[0]));
  RAM #(.addrWidth(16), .dataWidth(16)) ram_1 (
    .addr(buffer16_3_out_2), .data(out_10), .sel(1'b1), .clk(buffer_4_out), .ld(buffer1_4_out_2));  // open: clr

  // Other names for the same wires on the sheet: Imm5[4:0] = out_16[4:0]; IMM16_D[15:0] = out_16

  // Notes on the sheet:
  //   contents of rom_1 (hex, n*v repeats v):
  //   ff da07 db0f 1a03 122f 22 22 4*0 666 555 444 333 222
endmodule

module Clock (
  input  Reset,
  input  Fast_Slow,
  input  Osc_Man,
  input  Tick,
  output CLK_PH
);

  wire and_1_out, and_2_out, buffer_1_out, buffer_2_out, clock_1_out, clock_2_out, d_ff_1_q, d_ff_1_qn,
       d_ff_2_q, d_ff_2_qn, d_ff_3_q, d_ff_4_q, d_ff_5_qn, d_ff_6_qn, nand_1_out, not_1_out, not_2_out,
       not_3_out, or_1_out, or_2_out, or_3_out;

  Button u_Reset (.out(Reset));
  Button button_1 ();  // open: out
  Clock_part clock_1 (.out(clock_1_out));
  Button button_2 ();  // open: out
  Clock_part #(.highDuration(3), .lowDuration(3)) clock_2 (.out(clock_2_out));
  Button u_Tick ();  // open: out
  buf buffer_1 (buffer_1_out, Fast_Slow);
  not not_1 (not_1_out, Fast_Slow);
  buf buffer_2 (buffer_2_out, Osc_Man);
  not not_2 (not_2_out, Osc_Man);
  not not_3 (not_3_out, Tick);
  D_Flip_Flop d_ff_1 (.clk(clock_1_out), .D(d_ff_1_qn), .Q(d_ff_1_q), .Qn(d_ff_1_qn));  // open: preset, en, reset
  D_Flip_Flop d_ff_2 (.clk(clock_2_out), .D(d_ff_2_qn), .Q(d_ff_2_q), .Qn(d_ff_2_qn));  // open: preset, en, reset
  and and_1 (and_1_out, buffer_1_out, buffer_2_out, d_ff_6_qn);
  and and_2 (and_2_out, not_1_out, buffer_2_out, d_ff_5_qn);
  nand nand_1 (nand_1_out, d_ff_5_qn, d_ff_6_qn, not_2_out);
  D_Flip_Flop d_ff_3 (.clk(d_ff_1_q), .D(and_1_out), .Q(d_ff_3_q));  // open: Qn, preset, en, reset
  D_Flip_Flop d_ff_4 (.clk(d_ff_2_q), .D(and_2_out), .Q(d_ff_4_q));  // open: Qn, preset, en, reset
  D_Flip_Flop d_ff_5 (.clk(d_ff_1_qn), .D(d_ff_3_q), .Qn(d_ff_5_qn), .reset(Reset));  // open: Q, preset, en
  D_Flip_Flop d_ff_6 (.clk(d_ff_2_qn), .D(d_ff_4_q), .Qn(d_ff_6_qn), .reset(Reset));  // open: Q, preset, en
  or or_1 (or_1_out, d_ff_5_qn, d_ff_1_qn);
  or or_2 (or_2_out, d_ff_6_qn, d_ff_2_qn);
  or or_3 (or_3_out, nand_1_out, not_3_out);
  nand nand_2 (CLK_PH, or_1_out, or_2_out, or_3_out);

  // Other names for the same wires on the sheet: RST = Reset
endmodule

// SEQ
module Sequencer (
  input  Reset,
  input  CLKIn,
  input  nHalt,
  output PH0,
  output PH1,
  output CLR1,
  output PH2,
  output CLR2,
  output Test,
  output Test_2,
  output Test_3,
  output Test_4
);

  wire buffer_1_out, buffer_3_out, buffer_4_out, buffer_7_out, buffer_8_out, buffer_11_out, buffer_15_out,
       buffer_16_out, buffer_17_out, buffer_20_out, buffer_21_out, CLK, dpdt_1_com_2, dpdth_1_com_2,
       dpdth_2_com, dpdth_2_com_2, dpdth_4_com_2, dpdth_5_com, dpdth_5_com_2, dpdth_6_com_2, dpdth_7_com,
       dpdth_7_com_2, dpdth_8_com_2, dpdth_9_com, dpdth_9_com_2, dpdth_10_com_2, dpdtr_1_nc_2, dpdtr_1_no,
       dpdtr_3_nc_2, dpdtr_3_no, dpdtr_3_no_2, dpdtr_4_nc_2, dpdtr_4_no, dpdtr_5_nc_2, dpdtr_6_nc_2,
       dpdtr_6_no, dpdtr_7_nc_2, dpdtr_7_no, dpdtr_7_no_2, dpdtr_8_nc_2, dpdtr_9_nc_2, nCLK, Reset_t, SEQRun;

  buf buffer_1 (buffer_1_out, dpdth_10_com_2);
  buf buffer_2 (Reset_t, Reset);
  buf buffer_3 (buffer_3_out, CLKIn);
  buf buffer_4 (buffer_4_out, nHalt);
  DPDTr dpdtr_1 (.coil(Test), .com(1'b1), .com_2(1'b1), .NO(dpdtr_1_no), .NC_2(dpdtr_1_nc_2));  // open: NC, NO_2
  DPDTh dpdth_1 (
    .coil(buffer_1_out), .NO(dpdtr_4_nc_2), .NO_2(nCLK), .com(Test), .com_2(dpdth_1_com_2));  // open: NC, NC_2
  DPDTr dpdtr_2 (.coil(buffer_3_out), .com(1'b1), .NC(nCLK), .NO(CLK));  // open: com_2, NC_2, NO_2
  DPDT dpdt_1 (.coil(buffer_4_out), .com_2(dpdt_1_com_2), .NO_2(nCLK));  // open: NC, com, NO, NC_2
  buf buffer_5 (CLR1, dpdtr_1_no);
  buf buffer_6 (PH0, dpdtr_1_no);
  buf buffer_7 (buffer_7_out, dpdth_1_com_2);
  buf buffer_8 (buffer_8_out, dpdt_1_com_2);
  buf buffer_9 (PH0, dpdtr_3_no);
  buf buffer_10 (PH1, dpdtr_3_no);
  DPDTr dpdtr_3 (
    .coil(dpdth_2_com), .com(1'b1), .com_2(1'b1), .NO(dpdtr_3_no), .NC_2(dpdtr_3_nc_2), .NO_2(dpdtr_3_no_2));  // open: NC
  buf buffer_11 (buffer_11_out, dpdth_2_com_2);
  DPDTh dpdth_2 (
    .coil(buffer_7_out), .NO(dpdtr_5_nc_2), .NO_2(CLK), .com(dpdth_2_com), .com_2(dpdth_2_com_2));  // open: NC, NC_2
  DPDTh dpdth_3 (.coil(buffer_8_out), .NO(buffer_4_out), .NO_2(CLK), .com_2(SEQRun));  // open: NC, NC_2, com
  buf buffer_12 (CLR1, dpdtr_3_no);
  buf buffer_13 (PH0, dpdtr_4_no);
  DPDTr dpdtr_4 (.coil(Test_2), .com(1'b1), .com_2(1'b1), .NO(dpdtr_4_no), .NC_2(dpdtr_4_nc_2));  // open: NC, NO_2
  DPDTh dpdth_4 (
    .coil(buffer_11_out), .NO(dpdtr_6_nc_2), .NO_2(nCLK), .com(Test_2), .com_2(dpdth_4_com_2));  // open: NC, NC_2
  buf buffer_14 (PH1, dpdtr_4_no);
  buf buffer_15 (buffer_15_out, dpdth_4_com_2);
  DPDTr dpdtr_5 (.coil(dpdth_5_com), .com_2(1'b1), .NC_2(dpdtr_5_nc_2));  // open: com, NC, NO, NO_2
  DPDTh dpdth_5 (
    .coil(buffer_15_out), .NO(dpdtr_7_nc_2), .NO_2(CLK), .com(dpdth_5_com), .com_2(dpdth_5_com_2));  // open: NC, NC_2
  buf buffer_16 (buffer_16_out, dpdth_5_com_2);
  DPDTr dpdtr_6 (.coil(Test_3), .com(1'b1), .com_2(1'b1), .NO(dpdtr_6_no), .NC_2(dpdtr_6_nc_2));  // open: NC, NO_2
  DPDTh dpdth_6 (
    .coil(buffer_16_out), .NO(dpdtr_8_nc_2), .NO_2(nCLK), .com(Test_3), .com_2(dpdth_6_com_2));  // open: NC, NC_2
  buf buffer_17 (buffer_17_out, dpdth_6_com_2);
  buf buffer_18 (CLR2, dpdtr_7_no);
  buf buffer_19 (PH2, dpdtr_7_no_2);
  DPDTr dpdtr_7 (
    .coil(dpdth_7_com), .com(dpdtr_6_no), .com_2(1'b1), .NO(dpdtr_7_no), .NC_2(dpdtr_7_nc_2),
    .NO_2(dpdtr_7_no_2));  // open: NC
  buf buffer_20 (buffer_20_out, dpdth_7_com_2);
  DPDTh dpdth_7 (
    .coil(buffer_17_out), .NO(dpdtr_9_nc_2), .NO_2(CLK), .com(dpdth_7_com), .com_2(dpdth_7_com_2));  // open: NC, NC_2
  DPDTr dpdtr_8 (.coil(Test_4), .com_2(1'b1), .NC_2(dpdtr_8_nc_2));  // open: com, NC, NO, NO_2
  DPDTh dpdth_8 (
    .coil(buffer_20_out), .NO(dpdtr_1_nc_2), .NO_2(nCLK), .com(Test_4), .com_2(dpdth_8_com_2));  // open: NC, NC_2
  buf buffer_21 (buffer_21_out, dpdth_8_com_2);
  DPDTr dpdtr_9 (.coil(dpdth_9_com), .com_2(1'b1), .NC_2(dpdtr_9_nc_2));  // open: com, NC, NO, NO_2
  DPDTh dpdth_9 (
    .coil(buffer_21_out), .NO(dpdtr_3_nc_2), .NC_2(1'b1), .NO_2(CLK), .com(dpdth_9_com), .com_2(dpdth_9_com_2));  // open: NC
  DPDTh dpdth_10 (
    .coil(dpdtr_3_no_2), .NO(dpdth_9_com_2), .NC_2(SEQRun), .com_2(dpdth_10_com_2));  // open: NC, NO_2, com

  // Notes on the sheet:
  //   buffer_1 drives only 1 and floats otherwise
  //   buffer_2 drives only 1 and floats otherwise
  //   buffer_3 drives only 1 and floats otherwise
  //   buffer_4 drives only 1 and floats otherwise
  //   buffer_5 drives only 1 and floats otherwise
  //   buffer_6 drives only 1 and floats otherwise
  //   buffer_7 drives only 1 and floats otherwise
  //   buffer_8 drives only 1 and floats otherwise
  //   buffer_9 drives only 1 and floats otherwise
  //   buffer_10 drives only 1 and floats otherwise
  //   buffer_11 drives only 1 and floats otherwise
  //   buffer_12 drives only 1 and floats otherwise
  //   buffer_13 drives only 1 and floats otherwise
  //   buffer_14 drives only 1 and floats otherwise
  //   buffer_15 drives only 1 and floats otherwise
  //   Nota: Totes les senyals CLK, /CLK requreixen diodes per aillar-se de les altres
  //   buffer_16 drives only 1 and floats otherwise
  //   buffer_17 drives only 1 and floats otherwise
  //   buffer_18 drives only 1 and floats otherwise
  //   buffer_19 drives only 1 and floats otherwise
  //   buffer_20 drives only 1 and floats otherwise
  //   buffer_21 drives only 1 and floats otherwise
endmodule

// REG
module REG16bit (
  input  nWE,
  input  IE,
  input  CLR,
  input  OE,
  input  [15:0] In,
  output [15:0] Out,
  output [15:0] Test
);

  wire buffer_1_out, buffer_2_out, buffer_3_out, dpdtr_1_nc, dpdtr_2_no, dpdtr_3_nc_2;

  DPDTr dpdtr_1 (.coil(nWE), .com(buffer_1_out), .NC(dpdtr_1_nc));  // open: com_2, NO, NC_2, NO_2
  buf buffer_1 (buffer_1_out, IE);
  buf buffer_2 (buffer_2_out, CLR);
  buf buffer_3 (buffer_3_out, OE);
  DPDTr dpdtr_2 (.coil(dpdtr_1_nc), .com(buffer_2_out), .NO(dpdtr_2_no));  // open: com_2, NC, NC_2, NO_2
  DPDTr dpdtr_3 (.coil(dpdtr_2_no), .com_2(1'b1), .NC_2(dpdtr_3_nc_2));  // open: com, NC, NO, NO_2
  REGBase16bit regbase16bit_1 (.Hold(dpdtr_3_nc_2), .IE(dpdtr_1_nc), .OE(buffer_3_out), .R(Test), .A(Out), .I0(In));

  // Notes on the sheet:
  //   buffer_1 drives only 1 and floats otherwise
  //   buffer_2 drives only 1 and floats otherwise
  //   buffer_3 drives only 1 and floats otherwise
endmodule

// PC
module REG_PC (
  input  nWE,
  input  IE,
  input  PH,
  input  CLR,
  input  OE,
  input  [15:0] In,
  input  nWE1,
  input  PH1,
  input  CLR1,
  output [15:0] Out,
  output [15:0] Out_plus,
  output [15:0] Test
);

  wire buffer_1_out, buffer_2_out, buffer_3_out, buffer_4_out, buffer_5_out, buffer_6_out, buffer_7_out,
       buffer_9_out, dpdtr_1_nc, dpdtr_2_nc, dpdtr_3_no, dpdtr_4_no, dpdtr_5_nc_2, dpdtr_6_nc_2;
  wire [15:0] inputswitch_1_o;

  buf buffer_1 (buffer_1_out, IE);
  buf buffer_2 (buffer_2_out, PH);
  buf buffer_3 (buffer_3_out, CLR);
  buf buffer_4 (buffer_4_out, OE);
  DPDTr dpdtr_1 (.coil(nWE), .com(buffer_1_out), .NC(dpdtr_1_nc));  // open: com_2, NO, NC_2, NO_2
  buf buffer_5 (buffer_5_out, PH1);
  buf buffer_6 (buffer_6_out, CLR1);
  buf buffer_7 (buffer_7_out, dpdtr_1_nc);
  buf buffer_8 (buffer_7_out, buffer_2_out);
  buf buffer_9 (buffer_9_out, dpdtr_1_nc);
  buf buffer_10 (buffer_9_out, buffer_2_out);
  DPDTr dpdtr_2 (.coil(nWE1), .com(buffer_5_out), .NC(dpdtr_2_nc));  // open: com_2, NO, NC_2, NO_2
  DPDTr dpdtr_3 (.coil(buffer_7_out), .com(buffer_3_out), .NO(dpdtr_3_no));  // open: com_2, NC, NC_2, NO_2
  DPDTr dpdtr_4 (.coil(dpdtr_2_nc), .com(buffer_6_out), .NO(dpdtr_4_no));  // open: com_2, NC, NC_2, NO_2
  DPDTr dpdtr_5 (.coil(dpdtr_3_no), .com_2(1'b1), .NC_2(dpdtr_5_nc_2));  // open: com, NC, NO, NO_2
  InputSwitch inputswitch_1 (.S1(dpdtr_1_nc), .I0(Out_plus), .I1(In), .O(inputswitch_1_o));
  DPDTr dpdtr_6 (.coil(dpdtr_4_no), .com_2(1'b1), .NC_2(dpdtr_6_nc_2));  // open: com, NC, NO, NO_2
  REGBase16bit PC (.Hold(dpdtr_5_nc_2), .IE(buffer_9_out), .OE(buffer_4_out), .R(Test), .A(Out), .I0(inputswitch_1_o));
  INCrementer INC_R (.Hold(dpdtr_6_nc_2), .OE(1'b1), .I0(Test), .B(Out_plus), .IE(dpdtr_2_nc));  // open: COut, R

  // Notes on the sheet:
  //   buffer_1 drives only 1 and floats otherwise
  //   buffer_2 drives only 1 and floats otherwise
  //   buffer_3 drives only 1 and floats otherwise
  //   buffer_4 drives only 1 and floats otherwise
  //   buffer_5 drives only 1 and floats otherwise
  //   buffer_6 drives only 1 and floats otherwise
  //   buffer_7 drives only 1 and floats otherwise
  //   buffer_8 drives only 1 and floats otherwise
  //   buffer_9 drives only 1 and floats otherwise
  //   buffer_10 drives only 1 and floats otherwise
endmodule

// REG_LNK
module REG_LINK (
  input  nWE,
  input  IE,
  input  CLR,
  input  IElk,
  input  CLRlk,
  input  OE,
  input  [15:0] In,
  input  [15:0] InLK,
  output [15:0] Out,
  output [15:0] Test
);

  wire buffer_1_out, buffer_2_out, buffer_3_out, buffer_5_out, buffer_6_out, dpdtr_1_nc, dpdtr_2_no,
       dpdtr_3_nc_2;

  DPDTr dpdtr_1 (.coil(nWE), .com(buffer_1_out), .NC(dpdtr_1_nc));  // open: com_2, NO, NC_2, NO_2
  buf buffer_1 (buffer_1_out, IE);
  buf buffer_2 (buffer_2_out, CLR);
  buf buffer_3 (buffer_3_out, IElk);
  buf buffer_4 (buffer_2_out, CLRlk);
  buf buffer_5 (buffer_5_out, OE);
  buf buffer_6 (buffer_6_out, dpdtr_1_nc);
  buf buffer_7 (buffer_6_out, buffer_3_out);
  DPDTr dpdtr_2 (.coil(buffer_6_out), .com(buffer_2_out), .NO(dpdtr_2_no));  // open: com_2, NC, NC_2, NO_2
  DPDTr dpdtr_3 (.coil(dpdtr_2_no), .com_2(1'b1), .NC_2(dpdtr_3_nc_2));  // open: com, NC, NO, NO_2
  REGBase16bit_2 regbase16bit_2_1 (
    .Hold(dpdtr_3_nc_2), .IE0(dpdtr_1_nc), .IE1(buffer_3_out), .OE(buffer_5_out), .I0(In), .I1(InLK),
    .R(Test), .A(Out));

  // Notes on the sheet:
  //   buffer_1 drives only 1 and floats otherwise
  //   buffer_2 drives only 1 and floats otherwise
  //   buffer_3 drives only 1 and floats otherwise
  //   buffer_4 drives only 1 and floats otherwise
  //   buffer_5 drives only 1 and floats otherwise
  //   buffer_6 drives only 1 and floats otherwise
  //   buffer_7 drives only 1 and floats otherwise
endmodule

// STATUS REG
module REG_STATUS (
  input  nWE,
  input  IE,
  input  CLR,
  input  OE,
  input  NZ,
  input  C,
  input  NT,
  output NZ_2,
  output C_2,
  output NT_2
);

  wire buffer_1_out, buffer_2_out, buffer_3_out, buffer_4_out, buffer_5_out, buffer_6_out, CLR_nc_2,
       IE_2_com, IE_2_com_2, IE_3_com, IE_no, nWE_nc;

  buf buffer_1 (buffer_1_out, IE);
  buf buffer_2 (buffer_2_out, CLR);
  buf buffer_3 (buffer_3_out, OE);
  DPDTr u_nWE (.coil(nWE), .com(buffer_1_out), .NC(nWE_nc));  // open: com_2, NO, NC_2, NO_2
  DPDTr u_IE (.coil(nWE_nc), .com(buffer_2_out), .NO(IE_no));  // open: com_2, NC, NC_2, NO_2
  buf buffer_4 (buffer_4_out, IE_2_com);
  DPDT IE_2 (.coil(nWE_nc), .com(IE_2_com), .NO(NZ), .com_2(IE_2_com_2), .NO_2(C));  // open: NC, NC_2
  buf buffer_5 (buffer_5_out, IE_2_com_2);
  DPDT IE_3 (.coil(nWE_nc), .com(IE_3_com), .NO(NT));  // open: NC, NC_2, com_2, NO_2
  buf buffer_6 (buffer_6_out, IE_3_com);
  DPDTr u_CLR (.coil(IE_no), .com_2(1'b1), .NC_2(CLR_nc_2));  // open: com, NC, NO, NO_2
  DPDTh u_C (.coil(buffer_5_out), .NO(CLR_nc_2), .NO_2(buffer_3_out), .com_2(C_2));  // open: NC, NC_2, com
  DPDTh u_NZ (.coil(buffer_4_out), .NO(CLR_nc_2), .NO_2(buffer_3_out), .com_2(NZ_2));  // open: NC, NC_2, com
  DPDTh T (.coil(buffer_6_out), .NO(CLR_nc_2), .NO_2(buffer_3_out), .com_2(NT_2));  // open: NC, NC_2, com

  // Notes on the sheet:
  //   buffer_1 drives only 1 and floats otherwise
  //   buffer_2 drives only 1 and floats otherwise
  //   buffer_3 drives only 1 and floats otherwise
  //   buffer_4 drives only 1 and floats otherwise
  //   buffer_5 drives only 1 and floats otherwise
  //   buffer_6 drives only 1 and floats otherwise
endmodule

// PREFIX
module REG_PFIX (
  input  IE,
  input  CLR,
  input  OE,
  input  [10:0] In,
  output [10:0] Out,
  output [10:0] Test
);

  wire buffer_1_out, buffer_2_out, buffer_3_out, dpdtr_1_nc_2;
  wire [15:11] regbase16bit_1_a, regbase16bit_1_r, undriven;

  buf buffer_1 (buffer_1_out, IE);
  buf buffer_2 (buffer_2_out, CLR);
  buf buffer_3 (buffer_3_out, OE);
  DPDTr dpdtr_1 (.coil(buffer_2_out), .com_2(1'b1), .NC_2(dpdtr_1_nc_2));  // open: com, NC, NO, NO_2
  REGBase16bit regbase16bit_1 (
    .Hold(dpdtr_1_nc_2), .IE(buffer_1_out), .OE(buffer_3_out), .R({regbase16bit_1_r, Test}),
    .A({regbase16bit_1_a, Out}), .I0({undriven, In}));

  // Notes on the sheet:
  //   buffer_1 drives only 1 and floats otherwise
  //   buffer_2 drives only 1 and floats otherwise
  //   buffer_3 drives only 1 and floats otherwise
endmodule

// ALU REG
module REG_ALU (
  input  IE,
  input  CLR,
  input  OE,
  input  NT,
  input  NZ,
  input  C,
  input  NW,
  input  [15:0] In,
  output NT_2,
  output NZ_2,
  output C_2,
  output NW_2,
  output [15:0] Out,
  output [15:0] Test
);

  wire buffer_1_out, buffer_2_out, buffer_3_out, buffer_4_out, buffer_5_out, buffer_6_out, buffer_7_out,
       dpdt_1_com, dpdt_1_com_2, dpdt_2_com, dpdt_2_com_2, dpdtr_1_no, dpdtr_2_nc_2;

  buf buffer_1 (buffer_1_out, IE);
  buf buffer_2 (buffer_2_out, CLR);
  buf buffer_3 (buffer_3_out, OE);
  DPDTr dpdtr_1 (.coil(buffer_1_out), .com(buffer_2_out), .NO(dpdtr_1_no));  // open: com_2, NC, NC_2, NO_2
  DPDT dpdt_1 (.coil(buffer_1_out), .com(dpdt_1_com), .NO(NT), .com_2(dpdt_1_com_2), .NO_2(NZ));  // open: NC, NC_2
  DPDT dpdt_2 (.coil(buffer_1_out), .com(dpdt_2_com), .NO(C), .com_2(dpdt_2_com_2), .NO_2(NW));  // open: NC, NC_2
  buf buffer_4 (buffer_4_out, dpdt_1_com);
  buf buffer_5 (buffer_5_out, dpdt_1_com_2);
  buf buffer_6 (buffer_6_out, dpdt_2_com);
  buf buffer_7 (buffer_7_out, dpdt_2_com_2);
  DPDTr dpdtr_2 (.coil(dpdtr_1_no), .com_2(1'b1), .NC_2(dpdtr_2_nc_2));  // open: com, NC, NO, NO_2
  DPDTh dpdth_1 (.coil(buffer_5_out), .NO(dpdtr_2_nc_2), .NO_2(buffer_3_out), .com_2(NZ_2));  // open: NC, NC_2, com
  DPDTh dpdth_2 (.coil(buffer_7_out), .NO(dpdtr_2_nc_2), .NO_2(buffer_3_out), .com_2(NW_2));  // open: NC, NC_2, com
  REGBase16bit regbase16bit_1 (.Hold(dpdtr_2_nc_2), .IE(buffer_1_out), .OE(buffer_3_out), .R(Test), .A(Out), .I0(In));
  DPDTh dpdth_3 (.coil(buffer_4_out), .NO(dpdtr_2_nc_2), .NO_2(buffer_3_out), .com_2(NT_2));  // open: NC, NC_2, com
  DPDTh dpdth_4 (.coil(buffer_6_out), .NO(dpdtr_2_nc_2), .NO_2(buffer_3_out), .com_2(C_2));  // open: NC, NC_2, com

  // Notes on the sheet:
  //   buffer_1 drives only 1 and floats otherwise
  //   buffer_2 drives only 1 and floats otherwise
  //   buffer_3 drives only 1 and floats otherwise
  //   buffer_4 drives only 1 and floats otherwise
  //   buffer_5 drives only 1 and floats otherwise
  //   buffer_6 drives only 1 and floats otherwise
  //   buffer_7 drives only 1 and floats otherwise
endmodule

// REG BASE
module REGBase16bit (
  input  [15:0] I0,
  input  Hold,
  input  IE,
  input  OE,
  output [15:0] R,
  output [15:0] A
);

  wire buffer_1_out, buffer_2_out, buffer_3_out, buffer_4_out, buffer_5_out, buffer_6_out, buffer_7_out,
       buffer_8_out, buffer_9_out, buffer_10_out, buffer_11_out, buffer_12_out, buffer_13_out, buffer_14_out,
       buffer_15_out, buffer_16_out, dpdt_1_com, dpdt_1_com_2, dpdt_2_com, dpdt_2_com_2, dpdt_3_com,
       dpdt_3_com_2, dpdt_4_com, dpdt_4_com_2, dpdt_5_com, dpdt_5_com_2, dpdt_6_com, dpdt_6_com_2,
       dpdt_7_com, dpdt_7_com_2, dpdt_8_com, dpdt_8_com_2;

  DPDT dpdt_1 (.coil(IE), .com(dpdt_1_com), .NO(I0[0]), .com_2(dpdt_1_com_2), .NO_2(I0[1]));  // open: NC, NC_2
  DPDT dpdt_2 (.coil(IE), .com(dpdt_2_com), .NO(I0[2]), .com_2(dpdt_2_com_2), .NO_2(I0[3]));  // open: NC, NC_2
  DPDT dpdt_3 (.coil(IE), .com(dpdt_3_com), .NO(I0[4]), .com_2(dpdt_3_com_2), .NO_2(I0[5]));  // open: NC, NC_2
  DPDT dpdt_4 (.coil(IE), .com(dpdt_4_com), .NO(I0[6]), .com_2(dpdt_4_com_2), .NO_2(I0[7]));  // open: NC, NC_2
  DPDT dpdt_5 (.coil(IE), .com(dpdt_5_com), .NO(I0[8]), .com_2(dpdt_5_com_2), .NO_2(I0[9]));  // open: NC, NC_2
  DPDT dpdt_6 (.coil(IE), .com(dpdt_6_com), .NO(I0[10]), .com_2(dpdt_6_com_2), .NO_2(I0[11]));  // open: NC, NC_2
  DPDT dpdt_7 (.coil(IE), .com(dpdt_7_com), .NO(I0[12]), .com_2(dpdt_7_com_2), .NO_2(I0[13]));  // open: NC, NC_2
  DPDT dpdt_8 (.coil(IE), .com(dpdt_8_com), .NO(I0[14]), .com_2(dpdt_8_com_2), .NO_2(I0[15]));  // open: NC, NC_2
  buf buffer_1 (buffer_1_out, dpdt_1_com);
  buf buffer_2 (buffer_2_out, dpdt_1_com_2);
  buf buffer_3 (buffer_3_out, dpdt_2_com);
  buf buffer_4 (buffer_4_out, dpdt_2_com_2);
  buf buffer_5 (buffer_5_out, dpdt_3_com);
  buf buffer_6 (buffer_6_out, dpdt_3_com_2);
  buf buffer_7 (buffer_7_out, dpdt_4_com);
  buf buffer_8 (buffer_8_out, dpdt_4_com_2);
  buf buffer_9 (buffer_9_out, dpdt_5_com);
  buf buffer_10 (buffer_10_out, dpdt_5_com_2);
  buf buffer_11 (buffer_11_out, dpdt_6_com);
  buf buffer_12 (buffer_12_out, dpdt_6_com_2);
  buf buffer_13 (buffer_13_out, dpdt_7_com);
  buf buffer_14 (buffer_14_out, dpdt_7_com_2);
  buf buffer_15 (buffer_15_out, dpdt_8_com);
  buf buffer_16 (buffer_16_out, dpdt_8_com_2);
  DPDTh dpdth_1 (.coil(buffer_2_out), .NO(Hold), .NO_2(OE), .com(R[1]), .com_2(A[1]));  // open: NC, NC_2
  DPDTh dpdth_2 (.coil(buffer_4_out), .NO(Hold), .NO_2(OE), .com(R[3]), .com_2(A[3]));  // open: NC, NC_2
  DPDTh dpdth_3 (.coil(buffer_6_out), .NO(Hold), .NO_2(OE), .com(R[5]), .com_2(A[5]));  // open: NC, NC_2
  DPDTh dpdth_4 (.coil(buffer_8_out), .NO(Hold), .NO_2(OE), .com(R[7]), .com_2(A[7]));  // open: NC, NC_2
  DPDTh dpdth_5 (.coil(buffer_10_out), .NO(Hold), .NO_2(OE), .com(R[9]), .com_2(A[9]));  // open: NC, NC_2
  DPDTh dpdth_6 (.coil(buffer_12_out), .NO(Hold), .NO_2(OE), .com(R[11]), .com_2(A[11]));  // open: NC, NC_2
  DPDTh dpdth_7 (.coil(buffer_14_out), .NO(Hold), .NO_2(OE), .com(R[13]), .com_2(A[13]));  // open: NC, NC_2
  DPDTh dpdth_8 (.coil(buffer_16_out), .NO(Hold), .NO_2(OE), .com(R[15]), .com_2(A[15]));  // open: NC, NC_2
  DPDTh dpdth_9 (.coil(buffer_1_out), .NO(Hold), .NO_2(OE), .com(R[0]), .com_2(A[0]));  // open: NC, NC_2
  DPDTh dpdth_10 (.coil(buffer_3_out), .NO(Hold), .NO_2(OE), .com(R[2]), .com_2(A[2]));  // open: NC, NC_2
  DPDTh dpdth_11 (.coil(buffer_5_out), .NO(Hold), .NO_2(OE), .com(R[4]), .com_2(A[4]));  // open: NC, NC_2
  DPDTh dpdth_12 (.coil(buffer_7_out), .NO(Hold), .NO_2(OE), .com(R[6]), .com_2(A[6]));  // open: NC, NC_2
  DPDTh dpdth_13 (.coil(buffer_9_out), .NO(Hold), .NO_2(OE), .com(R[8]), .com_2(A[8]));  // open: NC, NC_2
  DPDTh dpdth_14 (.coil(buffer_11_out), .NO(Hold), .NO_2(OE), .com(R[10]), .com_2(A[10]));  // open: NC, NC_2
  DPDTh dpdth_15 (.coil(buffer_13_out), .NO(Hold), .NO_2(OE), .com(R[12]), .com_2(A[12]));  // open: NC, NC_2
  DPDTh dpdth_16 (.coil(buffer_15_out), .NO(Hold), .NO_2(OE), .com(R[14]), .com_2(A[14]));  // open: NC, NC_2

  // Notes on the sheet:
  //   buffer_1 drives only 1 and floats otherwise
  //   buffer_2 drives only 1 and floats otherwise
  //   buffer_3 drives only 1 and floats otherwise
  //   buffer_4 drives only 1 and floats otherwise
  //   buffer_5 drives only 1 and floats otherwise
  //   buffer_6 drives only 1 and floats otherwise
  //   buffer_7 drives only 1 and floats otherwise
  //   buffer_8 drives only 1 and floats otherwise
  //   buffer_9 drives only 1 and floats otherwise
  //   buffer_10 drives only 1 and floats otherwise
  //   buffer_11 drives only 1 and floats otherwise
  //   buffer_12 drives only 1 and floats otherwise
  //   buffer_13 drives only 1 and floats otherwise
  //   buffer_14 drives only 1 and floats otherwise
  //   buffer_15 drives only 1 and floats otherwise
  //   buffer_16 drives only 1 and floats otherwise
endmodule

// REGBASE_2
module REGBase16bit_2 (
  input  [15:0] I0,
  input  [15:0] I1,
  input  Hold,
  input  IE0,
  input  IE1,
  input  OE,
  output [15:0] R,
  output [15:0] A
);

  wire buffer_1_out, buffer_2_out, buffer_3_out, buffer_4_out, buffer_5_out, buffer_6_out, buffer_7_out,
       buffer_8_out, buffer_9_out, buffer_10_out, buffer_11_out, buffer_12_out, buffer_13_out, buffer_14_out,
       buffer_15_out, buffer_16_out, dpdt_1_com, dpdt_1_com_2, dpdt_2_com, dpdt_2_com_2, dpdt_3_com,
       dpdt_3_com_2, dpdt_4_com, dpdt_4_com_2, dpdt_5_com, dpdt_5_com_2, dpdt_6_com, dpdt_6_com_2,
       dpdt_7_com, dpdt_7_com_2, dpdt_8_com, dpdt_8_com_2, dpdt_9_com, dpdt_9_com_2, dpdt_10_com,
       dpdt_10_com_2, dpdt_11_com, dpdt_11_com_2, dpdt_12_com, dpdt_12_com_2, dpdt_13_com, dpdt_13_com_2,
       dpdt_14_com, dpdt_14_com_2, dpdt_15_com, dpdt_15_com_2, dpdt_16_com, dpdt_16_com_2;

  DPDT dpdt_1 (.coil(IE1), .com(dpdt_1_com), .NO(I1[0]), .com_2(dpdt_1_com_2), .NO_2(I1[1]));  // open: NC, NC_2
  DPDT dpdt_2 (.coil(IE1), .com(dpdt_2_com), .NO(I1[2]), .com_2(dpdt_2_com_2), .NO_2(I1[3]));  // open: NC, NC_2
  DPDT dpdt_3 (.coil(IE1), .com(dpdt_3_com), .NO(I1[4]), .com_2(dpdt_3_com_2), .NO_2(I1[5]));  // open: NC, NC_2
  DPDT dpdt_4 (.coil(IE1), .com(dpdt_4_com), .NO(I1[6]), .com_2(dpdt_4_com_2), .NO_2(I1[7]));  // open: NC, NC_2
  DPDT dpdt_5 (.coil(IE1), .com(dpdt_5_com), .NO(I1[8]), .com_2(dpdt_5_com_2), .NO_2(I1[9]));  // open: NC, NC_2
  DPDT dpdt_6 (.coil(IE1), .com(dpdt_6_com), .NO(I1[10]), .com_2(dpdt_6_com_2), .NO_2(I1[11]));  // open: NC, NC_2
  DPDT dpdt_7 (.coil(IE1), .com(dpdt_7_com), .NO(I1[12]), .com_2(dpdt_7_com_2), .NO_2(I1[13]));  // open: NC, NC_2
  DPDT dpdt_8 (.coil(IE1), .com(dpdt_8_com), .NO(I1[14]), .com_2(dpdt_8_com_2), .NO_2(I1[15]));  // open: NC, NC_2
  buf buffer_1 (buffer_1_out, dpdt_1_com);
  buf buffer_2 (buffer_2_out, dpdt_1_com_2);
  buf buffer_3 (buffer_3_out, dpdt_2_com);
  buf buffer_4 (buffer_4_out, dpdt_2_com_2);
  buf buffer_5 (buffer_5_out, dpdt_3_com);
  buf buffer_6 (buffer_6_out, dpdt_3_com_2);
  buf buffer_7 (buffer_7_out, dpdt_4_com);
  buf buffer_8 (buffer_8_out, dpdt_4_com_2);
  buf buffer_9 (buffer_9_out, dpdt_5_com);
  buf buffer_10 (buffer_10_out, dpdt_5_com_2);
  buf buffer_11 (buffer_11_out, dpdt_6_com);
  buf buffer_12 (buffer_12_out, dpdt_6_com_2);
  buf buffer_13 (buffer_13_out, dpdt_7_com);
  buf buffer_14 (buffer_14_out, dpdt_7_com_2);
  buf buffer_15 (buffer_15_out, dpdt_8_com);
  buf buffer_16 (buffer_16_out, dpdt_8_com_2);
  DPDT dpdt_9 (.coil(IE0), .com(dpdt_9_com), .NO(I0[0]), .com_2(dpdt_9_com_2), .NO_2(I0[1]));  // open: NC, NC_2
  buf buffer_17 (buffer_1_out, dpdt_9_com);
  buf buffer_18 (buffer_2_out, dpdt_9_com_2);
  DPDT dpdt_10 (.coil(IE0), .com(dpdt_10_com), .NO(I0[2]), .com_2(dpdt_10_com_2), .NO_2(I0[3]));  // open: NC, NC_2
  buf buffer_19 (buffer_3_out, dpdt_10_com);
  buf buffer_20 (buffer_4_out, dpdt_10_com_2);
  buf buffer_21 (buffer_5_out, dpdt_11_com);
  DPDT dpdt_11 (.coil(IE0), .com(dpdt_11_com), .NO(I0[4]), .com_2(dpdt_11_com_2), .NO_2(I0[5]));  // open: NC, NC_2
  buf buffer_22 (buffer_6_out, dpdt_11_com_2);
  DPDT dpdt_12 (.coil(IE0), .com(dpdt_12_com), .NO(I0[6]), .com_2(dpdt_12_com_2), .NO_2(I0[7]));  // open: NC, NC_2
  buf buffer_23 (buffer_7_out, dpdt_12_com);
  buf buffer_24 (buffer_8_out, dpdt_12_com_2);
  DPDT dpdt_13 (.coil(IE0), .com(dpdt_13_com), .NO(I0[8]), .com_2(dpdt_13_com_2), .NO_2(I0[9]));  // open: NC, NC_2
  buf buffer_25 (buffer_9_out, dpdt_13_com);
  buf buffer_26 (buffer_10_out, dpdt_13_com_2);
  buf buffer_27 (buffer_11_out, dpdt_14_com);
  DPDT dpdt_14 (.coil(IE0), .com(dpdt_14_com), .NO(I0[10]), .com_2(dpdt_14_com_2), .NO_2(I0[11]));  // open: NC, NC_2
  buf buffer_28 (buffer_12_out, dpdt_14_com_2);
  DPDT dpdt_15 (.coil(IE0), .com(dpdt_15_com), .NO(I0[12]), .com_2(dpdt_15_com_2), .NO_2(I0[13]));  // open: NC, NC_2
  buf buffer_29 (buffer_13_out, dpdt_15_com);
  buf buffer_30 (buffer_14_out, dpdt_15_com_2);
  DPDT dpdt_16 (.coil(IE0), .com(dpdt_16_com), .NO(I0[14]), .com_2(dpdt_16_com_2), .NO_2(I0[15]));  // open: NC, NC_2
  buf buffer_31 (buffer_15_out, dpdt_16_com);
  buf buffer_32 (buffer_16_out, dpdt_16_com_2);
  DPDTh dpdth_1 (.coil(buffer_2_out), .NO(Hold), .NO_2(OE), .com(R[1]), .com_2(A[1]));  // open: NC, NC_2
  DPDTh dpdth_2 (.coil(buffer_4_out), .NO(Hold), .NO_2(OE), .com(R[3]), .com_2(A[3]));  // open: NC, NC_2
  DPDTh dpdth_3 (.coil(buffer_6_out), .NO(Hold), .NO_2(OE), .com(R[5]), .com_2(A[5]));  // open: NC, NC_2
  DPDTh dpdth_4 (.coil(buffer_8_out), .NO(Hold), .NO_2(OE), .com(R[7]), .com_2(A[7]));  // open: NC, NC_2
  DPDTh dpdth_5 (.coil(buffer_10_out), .NO(Hold), .NO_2(OE), .com(R[9]), .com_2(A[9]));  // open: NC, NC_2
  DPDTh dpdth_6 (.coil(buffer_12_out), .NO(Hold), .NO_2(OE), .com(R[11]), .com_2(A[11]));  // open: NC, NC_2
  DPDTh dpdth_7 (.coil(buffer_14_out), .NO(Hold), .NO_2(OE), .com(R[13]), .com_2(A[13]));  // open: NC, NC_2
  DPDTh dpdth_8 (.coil(buffer_16_out), .NO(Hold), .NO_2(OE), .com(R[15]), .com_2(A[15]));  // open: NC, NC_2
  DPDTh dpdth_9 (.coil(buffer_1_out), .NO(Hold), .NO_2(OE), .com(R[0]), .com_2(A[0]));  // open: NC, NC_2
  DPDTh dpdth_10 (.coil(buffer_3_out), .NO(Hold), .NO_2(OE), .com(R[2]), .com_2(A[2]));  // open: NC, NC_2
  DPDTh dpdth_11 (.coil(buffer_5_out), .NO(Hold), .NO_2(OE), .com(R[4]), .com_2(A[4]));  // open: NC, NC_2
  DPDTh dpdth_12 (.coil(buffer_7_out), .NO(Hold), .NO_2(OE), .com(R[6]), .com_2(A[6]));  // open: NC, NC_2
  DPDTh dpdth_13 (.coil(buffer_9_out), .NO(Hold), .NO_2(OE), .com(R[8]), .com_2(A[8]));  // open: NC, NC_2
  DPDTh dpdth_14 (.coil(buffer_11_out), .NO(Hold), .NO_2(OE), .com(R[10]), .com_2(A[10]));  // open: NC, NC_2
  DPDTh dpdth_15 (.coil(buffer_13_out), .NO(Hold), .NO_2(OE), .com(R[12]), .com_2(A[12]));  // open: NC, NC_2
  DPDTh dpdth_16 (.coil(buffer_15_out), .NO(Hold), .NO_2(OE), .com(R[14]), .com_2(A[14]));  // open: NC, NC_2

  // Notes on the sheet:
  //   buffer_1 drives only 1 and floats otherwise
  //   buffer_2 drives only 1 and floats otherwise
  //   buffer_3 drives only 1 and floats otherwise
  //   buffer_4 drives only 1 and floats otherwise
  //   buffer_5 drives only 1 and floats otherwise
  //   buffer_6 drives only 1 and floats otherwise
  //   buffer_7 drives only 1 and floats otherwise
  //   buffer_8 drives only 1 and floats otherwise
  //   buffer_9 drives only 1 and floats otherwise
  //   buffer_10 drives only 1 and floats otherwise
  //   buffer_11 drives only 1 and floats otherwise
  //   buffer_12 drives only 1 and floats otherwise
  //   buffer_13 drives only 1 and floats otherwise
  //   buffer_14 drives only 1 and floats otherwise
  //   buffer_15 drives only 1 and floats otherwise
  //   buffer_16 drives only 1 and floats otherwise
  //   buffer_17 drives only 1 and floats otherwise
  //   buffer_18 drives only 1 and floats otherwise
  //   buffer_19 drives only 1 and floats otherwise
  //   buffer_20 drives only 1 and floats otherwise
  //   buffer_21 drives only 1 and floats otherwise
  //   buffer_22 drives only 1 and floats otherwise
  //   buffer_23 drives only 1 and floats otherwise
  //   buffer_24 drives only 1 and floats otherwise
  //   buffer_25 drives only 1 and floats otherwise
  //   buffer_26 drives only 1 and floats otherwise
  //   buffer_27 drives only 1 and floats otherwise
  //   buffer_28 drives only 1 and floats otherwise
  //   buffer_29 drives only 1 and floats otherwise
  //   buffer_30 drives only 1 and floats otherwise
  //   buffer_31 drives only 1 and floats otherwise
  //   buffer_32 drives only 1 and floats otherwise
endmodule

// ALU-CTRL
module ALUController (
  input  Ld_A,
  input  Ld_B,
  input  And,
  input  Or,
  input  Xor,
  input  Add,
  input  Sub,
  input  Rsb,
  output [7:0] out_9
);

  buf buffer_1 (out_9[7], Add);
  buf buffer_2 (out_9[6], Rsb);
  buf buffer_3 (out_9[5], Sub);
  buf buffer_4 (out_9[3], Ld_A);
  buf buffer_5 (out_9[2], Ld_B);
  buf buffer_6 (out_9[3], Ld_B);
  buf buffer_7 (out_9[3], And);
  buf buffer_8 (out_9[2], Or);
  buf buffer_9 (out_9[3], Or);
  buf buffer_10 (out_9[2], Xor);
  buf buffer_11 (out_9[2], Add);
  buf buffer_12 (out_9[3], Sub);
  buf buffer_13 (out_9[3], Rsb);
  buf buffer_14 (out_9[1], Ld_A);
  buf buffer_15 (out_9[1], Or);
  buf buffer_16 (out_9[1], Xor);
  buf buffer_17 (out_9[1], Add);
  buf buffer_18 (out_9[0], Sub);
  buf buffer_19 (out_9[0], Rsb);

  // Notes on the sheet:
  //   buffer_1 drives only 1 and floats otherwise
  //   buffer_2 drives only 1 and floats otherwise
  //   buffer_3 drives only 1 and floats otherwise
  //   buffer_4 drives only 1 and floats otherwise
  //   buffer_5 drives only 1 and floats otherwise
  //   buffer_6 drives only 1 and floats otherwise
  //   buffer_7 drives only 1 and floats otherwise
  //   buffer_8 drives only 1 and floats otherwise
  //   buffer_9 drives only 1 and floats otherwise
  //   buffer_10 drives only 1 and floats otherwise
  //   buffer_11 drives only 1 and floats otherwise
  //   buffer_12 drives only 1 and floats otherwise
  //   buffer_13 drives only 1 and floats otherwise
  //   buffer_14 drives only 1 and floats otherwise
  //   buffer_15 drives only 1 and floats otherwise
  //   buffer_16 drives only 1 and floats otherwise
  //   buffer_17 drives only 1 and floats otherwise
  //   buffer_18 drives only 1 and floats otherwise
  //   buffer_19 drives only 1 and floats otherwise
endmodule

// ALU
module ALU16Bit (
  input  LdA,
  input  LdB,
  input  And,
  input  Or,
  input  Xor,
  input  Add,
  input  Sub,
  input  Rsb,
  input  SelT,
  input  SelF,
  input  WiT,
  input  WiF,
  input  A_D6_plus,
  input  A_D6_minus,
  input  A_C1,
  input  A_C,
  input  NT,
  input  CIn,
  input  NZIn,
  input  [15:0] A,
  input  [15:0] B,
  input  Csh,
  input  SH,
  input  [7:0] CC_8,
  output NW,
  output Cout,
  output [15:0] O,
  output NZ,
  output NT_2
);

  wire alubase4bit_1_cout, alubase4bit_2_cout, alubase4bit_3_cout, alubase4bit_4_cx, buffer_2_out,
       buffer_3_out, buffer_27_out, dpdt_1_com, dpdt_1_com_2, dpdt_2_com, dpdtr_1_nc, dpdtr_1_nc_2,
       dpdtr_1_no, dpdtr_1_no_2, dpdtr_2_nc, dpdtr_2_no_2;
  wire [7:0] alucontroller_1_out_9;

  buf buffer_1 (CC_8[2], SH);
  DPDTr dpdtr_1 (
    .coil(NT), .com(SelT), .com_2(SelF), .NC(dpdtr_1_nc), .NO(dpdtr_1_no), .NC_2(dpdtr_1_nc_2),
    .NO_2(dpdtr_1_no_2));
  DPDTr dpdtr_2 (.coil(NT), .com(WiT), .com_2(WiF), .NC(dpdtr_2_nc), .NO_2(dpdtr_2_no_2));  // open: NO, NC_2
  DPDT dpdt_1 (.coil(A_C), .com(dpdt_1_com), .NO(CIn), .com_2(dpdt_1_com_2), .NO_2(NZIn));  // open: NC, NC_2
  DPDT dpdt_2 (.coil(A_C1), .NC(dpdt_1_com), .com(dpdt_2_com), .NO(1'b1));  // open: NC_2, com_2, NO_2
  buf buffer_2 (buffer_2_out, LdA);
  buf buffer_3 (buffer_3_out, LdB);
  buf buffer_4 (buffer_2_out, dpdtr_1_no);
  buf buffer_5 (buffer_3_out, dpdtr_1_nc);
  buf buffer_6 (buffer_3_out, dpdtr_1_no_2);
  buf buffer_7 (buffer_2_out, dpdtr_1_nc_2);
  buf buffer_8 (NW, dpdtr_2_nc);
  buf buffer_9 (NW, dpdtr_2_no_2);
  ALUController alucontroller_1 (
    .And(And), .Or(Or), .Xor(Xor), .Add(Add), .Sub(Sub), .out_9(alucontroller_1_out_9), .Rsb(Rsb),
    .Ld_A(buffer_2_out), .Ld_B(buffer_3_out));
  buf buffer_10 (NZ, dpdt_1_com_2);
  ALUBase4bit alubase4bit_1 (
    .Op(alucontroller_1_out_9), .A(A[3:0]), .B(B[3:0]), .Cin(dpdt_2_com), .minus_6(A_D6_minus), .Q(O[3:0]),
    .Cout(alubase4bit_1_cout), .plus_6(A_D6_plus));  // open: Cx
  buf buffer_11 (NZ, O[6]);
  buf buffer_12 (NZ, O[2]);
  buf buffer_13 (NZ, O[0]);
  buf buffer_14 (NZ, O[4]);
  buf buffer_15 (NZ, O[1]);
  buf buffer_16 (NZ, O[3]);
  buf buffer_17 (NZ, O[5]);
  buf buffer_18 (NZ, O[10]);
  buf buffer_19 (NZ, O[12]);
  buf buffer_20 (NZ, O[14]);
  buf buffer_21 (NZ, O[8]);
  buf buffer_22 (NZ, O[9]);
  buf buffer_23 (NZ, O[11]);
  buf buffer_24 (NZ, O[7]);
  buf buffer_25 (NZ, O[13]);
  ALUBase4bit alubase4bit_2 (
    .Op(alucontroller_1_out_9), .A(A[7:4]), .B(B[7:4]), .Cin(alubase4bit_1_cout), .minus_6(A_D6_minus),
    .Q(O[7:4]), .Cout(alubase4bit_2_cout), .plus_6(A_D6_plus));  // open: Cx
  buf buffer_26 (NZ, O[15]);
  buf buffer_27 (buffer_27_out, Csh);
  buf buffer_28 (buffer_27_out, Cout);
  ALUBase4bit alubase4bit_3 (
    .Op(alucontroller_1_out_9), .A(A[11:8]), .B(B[11:8]), .Cin(alubase4bit_2_cout), .minus_6(A_D6_minus),
    .Q(O[11:8]), .Cout(alubase4bit_3_cout), .plus_6(A_D6_plus));  // open: Cx
  ALUBase4bit alubase4bit_4 (
    .Op(alucontroller_1_out_9), .A(A[15:12]), .B(B[15:12]), .Cin(alubase4bit_3_cout), .minus_6(A_D6_minus),
    .Q(O[15:12]), .Cout(Cout), .Cx(alubase4bit_4_cx), .plus_6(A_D6_plus));
  AluFlags aluflags_1 (.NT(NT_2), .Cx(alubase4bit_4_cx), .C(buffer_27_out), .CC_8(CC_8), .nZ(NZ), .S(O[15]));

  // Notes on the sheet:
  //   buffer_1 drives only 1 and floats otherwise
  //   buffer_2 drives only 1 and floats otherwise
  //   buffer_3 drives only 1 and floats otherwise
  //   buffer_4 drives only 1 and floats otherwise
  //   buffer_5 drives only 1 and floats otherwise
  //   buffer_6 drives only 1 and floats otherwise
  //   buffer_7 drives only 1 and floats otherwise
  //   buffer_8 drives only 1 and floats otherwise
  //   buffer_9 drives only 1 and floats otherwise
  //   buffer_10 drives only 1 and floats otherwise
  //   buffer_11 drives only 1 and floats otherwise
  //   buffer_12 drives only 1 and floats otherwise
  //   buffer_13 drives only 1 and floats otherwise
  //   buffer_14 drives only 1 and floats otherwise
  //   buffer_15 drives only 1 and floats otherwise
  //   buffer_16 drives only 1 and floats otherwise
  //   buffer_17 drives only 1 and floats otherwise
  //   buffer_18 drives only 1 and floats otherwise
  //   buffer_19 drives only 1 and floats otherwise
  //   buffer_20 drives only 1 and floats otherwise
  //   buffer_21 drives only 1 and floats otherwise
  //   buffer_22 drives only 1 and floats otherwise
  //   buffer_23 drives only 1 and floats otherwise
  //   buffer_24 drives only 1 and floats otherwise
  //   buffer_25 drives only 1 and floats otherwise
  //   buffer_26 drives only 1 and floats otherwise
  //   buffer_27 drives only 1 and floats otherwise
  //   buffer_28 drives only 1 and floats otherwise
endmodule

// ALU4
module ALUBase4bit (
  input  [7:0] Op,
  input  minus_6,
  input  plus_6,
  input  [3:0] A,
  input  [3:0] B,
  input  Cin,
  output Cout,
  output Cx,
  output [3:0] Q
);

  wire alubase1bit_1_cout, alubase1bit_2_cout, alusub6_1_c, alusub6_1_nc;
  wire [3:0] aluadd6_1_q, alubase1bit_1_q;

  AluAdd6 aluadd6_1 (.I(B), .EN(plus_6), .Q(aluadd6_1_q));
  ALUBase1bit alubase1bit_1 (
    .A(A[0]), .B(aluadd6_1_q[0]), .Cin(Cin), .Q(alubase1bit_1_q[0]), .Cout(alubase1bit_1_cout), .GS1(Op[5]),
    .GS2(Op[6]), .GS3(Op[7]), .PS0(Op[0]), .PS1(Op[1]), .PS2(Op[2]), .PS3(Op[3]), .GS0(Op[4]));
  ALUBase1bit alubase1bit_2 (
    .A(A[1]), .B(aluadd6_1_q[1]), .Cin(alubase1bit_1_cout), .Q(alubase1bit_1_q[1]),
    .Cout(alubase1bit_2_cout), .GS1(Op[5]), .GS2(Op[6]), .GS3(Op[7]), .PS0(Op[0]), .PS1(Op[1]), .PS2(Op[2]),
    .PS3(Op[3]), .GS0(Op[4]));
  ALUBase1bit alubase1bit_3 (
    .A(A[2]), .B(aluadd6_1_q[2]), .Cin(alubase1bit_2_cout), .Q(alubase1bit_1_q[2]), .Cout(Cx), .GS1(Op[5]),
    .GS2(Op[6]), .GS3(Op[7]), .PS0(Op[0]), .PS1(Op[1]), .PS2(Op[2]), .PS3(Op[3]), .GS0(Op[4]));
  ALUBase1bit alubase1bit_4 (
    .A(A[3]), .B(aluadd6_1_q[3]), .Cin(Cx), .Q(alubase1bit_1_q[3]), .Cout(Cout), .GS1(Op[5]), .GS2(Op[6]),
    .GS3(Op[7]), .PS0(Op[0]), .PS1(Op[1]), .PS2(Op[2]), .PS3(Op[3]), .GS0(Op[4]));
  AluSub6 alusub6_1 (.I(alubase1bit_1_q), .EN(minus_6), .Q(Q), .Cin(Cout), .C(alusub6_1_c), .nC(alusub6_1_nc));
endmodule

// ALU-1
module ALUBase1bit (
  input  A,
  input  GS3,
  input  PS3,
  input  GS2,
  input  PS2,
  input  GS1,
  input  PS1,
  input  GS0,
  input  PS0,
  input  B,
  input  Cin,
  output Cout,
  output Q
);

  wire dpdt_1_com, dpdt_1_com_2, dpdt_2_com, dpdt_2_com_2, dpdt_3_com, dpdt_3_com_2, dpdtr_1_nc, dpdtr_1_no;

  DPDT dpdt_1 (.coil(A), .NC(GS2), .com(dpdt_1_com), .NO(GS3), .NC_2(GS0), .com_2(dpdt_1_com_2), .NO_2(GS1));
  DPDT dpdt_2 (.coil(A), .NC(PS2), .com(dpdt_2_com), .NO(PS3), .NC_2(PS0), .com_2(dpdt_2_com_2), .NO_2(PS1));
  DPDT dpdt_3 (
    .coil(B), .NC(dpdt_2_com_2), .com(dpdt_3_com), .NO(dpdt_2_com), .NC_2(dpdt_1_com_2),
    .com_2(dpdt_3_com_2), .NO_2(dpdt_1_com));
  DPDTr dpdtr_1 (.coil(Cin), .com(1'b1), .NC(dpdtr_1_nc), .NO(dpdtr_1_no));  // open: com_2, NC_2, NO_2
  DPDT dpdt_4 (
    .coil(dpdt_3_com), .NC(dpdt_3_com_2), .com(Cout), .NO(Cin), .NC_2(dpdtr_1_no), .com_2(Q),
    .NO_2(dpdtr_1_nc));

  // Notes on the sheet:
  //    GS.PS
  //   0000.0000 Q=0x00
  //   0000.1111 Q=0xff
  //   0000.1010 Q=A
  //   0000.1100 Q=B
  //   0000.0101 Q=/A
  //   0000.0011 Q=/B
  //   0000.1110 Q= A| B
  //   0000.1101 Q=/A| B
  //   0000.1011 Q= A|/B
  //   0000.0111 Q=/A|/B
  //   0000.1000 Q= A& B
  //   0000.0100 Q=/A& B
  //   0000.0010 Q= A&/B
  //   0000.0001 Q=/A&/B
  //   0000.0110 Q=  A^B
  //   0000.1001 Q=/(A^B)
  //    0100.1001 Q=/A+B=B-A 
  //   1000.0110 Q=A+B
  //   0010.1001 Q=A+/B=A-B
  //   1010.0000 Q=A<<1 //shift left
  //   1100.0000 Q=B<<1 //shift left
  //   1010.0101 Q=A+$FF=A-1
  //   1100.0011 Q=B+$FF=B-1
endmodule

module AluAdd6 (
  input  [3:0] I,
  input  EN,
  output [3:0] Q
);

  wire dpdtb_1_com_2, dpdtb_1_nc_2, dpdtb_1_no_2, dpdtr_1_nc_2, dpdtr_1_no, dpdtr_1_no_2, dpdtr_2_nc,
       dpdtr_2_nc_2;

  DPDTr dpdtr_1 (
    .coil(I[2]), .com(EN), .com_2(EN), .NO(dpdtr_1_no), .NC_2(dpdtr_1_nc_2), .NO_2(dpdtr_1_no_2));  // open: NC
  DPDTr dpdtr_2 (.coil(EN), .com(I[1]), .com_2(I[2]), .NC(dpdtr_2_nc), .NC_2(dpdtr_2_nc_2));  // open: NO, NO_2
  DPDTb dpdtb_1 (
    .coil(I[1]), .com(EN), .NC(dpdtr_1_nc_2), .NO(dpdtr_1_no_2), .NC_2(dpdtb_1_nc_2), .NO_2(dpdtb_1_no_2),
    .com_2(dpdtb_1_com_2));
  buf buffer_1 (Q[3], I[3]);
  buf buffer_2 (Q[3], dpdtr_1_no);
  buf buffer_3 (Q[3], dpdtb_1_no_2);
  buf buffer_4 (Q[1], dpdtb_1_nc_2);
  buf buffer_5 (Q[1], dpdtr_2_nc);
  buf buffer_6 (Q[2], dpdtb_1_com_2);
  buf buffer_7 (Q[2], dpdtr_2_nc_2);

  assign Q[0] = I[0];

  // Notes on the sheet:
  //   buffer_1 drives only 1 and floats otherwise
  //   buffer_2 drives only 1 and floats otherwise
  //   buffer_3 drives only 1 and floats otherwise
  //   buffer_4 drives only 1 and floats otherwise
  //   buffer_5 drives only 1 and floats otherwise
  //   buffer_6 drives only 1 and floats otherwise
  //   buffer_7 drives only 1 and floats otherwise
endmodule

// -6
module AluSub6 (
  input  [3:0] I,
  input  Cin,
  input  EN,
  output [3:0] Q,
  output C,
  output nC
);

  wire dpdtb_1_com_2, dpdtb_1_nc_2, dpdtb_1_no_2, dpdtr_1_nc, dpdtr_2_no, dpdtr_3_nc_2, dpdtr_3_no,
       dpdtr_3_no_2, dpdtr_4_nc, dpdtr_4_nc_2, dpdtr_5_nc;

  DPDTr dpdtr_1 (.coil(Cin), .com(EN), .com_2(1'b1), .NC(dpdtr_1_nc), .NC_2(nC), .NO_2(C));  // open: NO
  DPDTr dpdtr_2 (.coil(I[3]), .com(dpdtb_1_no_2), .NO(dpdtr_2_no));  // open: com_2, NC, NC_2, NO_2
  DPDTr dpdtr_3 (
    .coil(I[2]), .com(dpdtr_2_no), .com_2(dpdtr_1_nc), .NO(dpdtr_3_no), .NC_2(dpdtr_3_nc_2),
    .NO_2(dpdtr_3_no_2));  // open: NC
  DPDTr dpdtr_4 (.coil(dpdtr_1_nc), .com(I[1]), .com_2(I[2]), .NC(dpdtr_4_nc), .NC_2(dpdtr_4_nc_2));  // open: NO, NO_2
  DPDTr dpdtr_5 (.coil(dpdtr_1_nc), .com(I[3]), .NC(dpdtr_5_nc));  // open: com_2, NO, NC_2, NO_2
  buf buffer_1 (Q[3], dpdtr_3_no);
  DPDTb dpdtb_1 (
    .coil(I[1]), .com(dpdtr_1_nc), .NC(dpdtr_3_no_2), .NO(dpdtr_3_nc_2), .NC_2(dpdtb_1_nc_2),
    .NO_2(dpdtb_1_no_2), .com_2(dpdtb_1_com_2));
  buf buffer_2 (Q[3], dpdtr_5_nc);
  buf buffer_3 (Q[1], dpdtb_1_nc_2);
  buf buffer_4 (Q[1], dpdtr_4_nc);
  buf buffer_5 (Q[2], dpdtb_1_com_2);
  buf buffer_6 (Q[2], dpdtr_4_nc_2);

  assign Q[0] = I[0];

  // Notes on the sheet:
  //   buffer_1 drives only 1 and floats otherwise
  //   buffer_2 drives only 1 and floats otherwise
  //   buffer_3 drives only 1 and floats otherwise
  //   buffer_4 drives only 1 and floats otherwise
  //   buffer_5 drives only 1 and floats otherwise
  //   buffer_6 drives only 1 and floats otherwise
endmodule

// INC
module INCrementer (
  input  [15:0] I0,
  input  Hold,
  input  IE,
  input  OE,
  output COut,
  output [15:0] R,
  output [15:0] B
);

  wire buffer_1_out, buffer_2_out, buffer_3_out, buffer_4_out, buffer_5_out, buffer_6_out, buffer_7_out,
       buffer_8_out, buffer_9_out, buffer_10_out, buffer_11_out, buffer_12_out, buffer_13_out, buffer_14_out,
       buffer_15_out, buffer_16_out, dpdt_1_com, dpdt_1_com_2, dpdt_2_com, dpdt_2_com_2, dpdt_3_com,
       dpdt_3_com_2, dpdt_4_com, dpdt_4_com_2, dpdt_5_com, dpdt_5_com_2, dpdt_6_com, dpdt_6_com_2,
       dpdt_7_com, dpdt_7_com_2, dpdt_8_com, dpdt_8_com_2, incbase1_1_cout, incbase1_1_q, incbase1_2_cout,
       incbase1_2_q, incbase1_3_cout, incbase1_3_q, incbase1_4_cout, incbase1_4_q, incbase1_5_cout,
       incbase1_5_q, incbase1_6_cout, incbase1_6_q, incbase1_7_cout, incbase1_7_q, incbase1_8_cout,
       incbase1_8_q, incbase1_9_cout, incbase1_9_q, incbase1_10_cout, incbase1_10_q, incbase1_11_cout,
       incbase1_11_q, incbase1_12_cout, incbase1_12_q, incbase1_13_cout, incbase1_13_q, incbase1_14_cout,
       incbase1_14_q, incbase1_15_cout, incbase1_15_q, incbase1_16_q;

  INCBase1 incbase1_1 (.I(I0[0]), .Cin(1'b1), .Q(incbase1_1_q), .Cout(incbase1_1_cout));
  INCBase1 incbase1_2 (.I(I0[1]), .Cin(incbase1_1_cout), .Q(incbase1_2_q), .Cout(incbase1_2_cout));
  INCBase1 incbase1_3 (.I(I0[2]), .Cin(incbase1_2_cout), .Q(incbase1_3_q), .Cout(incbase1_3_cout));
  INCBase1 incbase1_4 (.I(I0[3]), .Cin(incbase1_3_cout), .Q(incbase1_4_q), .Cout(incbase1_4_cout));
  INCBase1 incbase1_5 (.I(I0[4]), .Cin(incbase1_4_cout), .Q(incbase1_5_q), .Cout(incbase1_5_cout));
  INCBase1 incbase1_6 (.I(I0[5]), .Cin(incbase1_5_cout), .Q(incbase1_6_q), .Cout(incbase1_6_cout));
  INCBase1 incbase1_7 (.I(I0[6]), .Cin(incbase1_6_cout), .Q(incbase1_7_q), .Cout(incbase1_7_cout));
  INCBase1 incbase1_8 (.I(I0[7]), .Cin(incbase1_7_cout), .Q(incbase1_8_q), .Cout(incbase1_8_cout));
  INCBase1 incbase1_9 (.I(I0[8]), .Cin(incbase1_8_cout), .Q(incbase1_9_q), .Cout(incbase1_9_cout));
  INCBase1 incbase1_10 (.I(I0[9]), .Cin(incbase1_9_cout), .Q(incbase1_10_q), .Cout(incbase1_10_cout));
  INCBase1 incbase1_11 (.I(I0[10]), .Cin(incbase1_10_cout), .Q(incbase1_11_q), .Cout(incbase1_11_cout));
  INCBase1 incbase1_12 (.I(I0[11]), .Cin(incbase1_11_cout), .Q(incbase1_12_q), .Cout(incbase1_12_cout));
  INCBase1 incbase1_13 (.I(I0[12]), .Cin(incbase1_12_cout), .Q(incbase1_13_q), .Cout(incbase1_13_cout));
  INCBase1 incbase1_14 (.I(I0[13]), .Cin(incbase1_13_cout), .Q(incbase1_14_q), .Cout(incbase1_14_cout));
  INCBase1 incbase1_15 (.I(I0[14]), .Cin(incbase1_14_cout), .Q(incbase1_15_q), .Cout(incbase1_15_cout));
  INCBase1 incbase1_16 (.I(I0[15]), .Cin(incbase1_15_cout), .Q(incbase1_16_q), .Cout(COut));
  DPDT dpdt_1 (
    .coil(IE), .com(dpdt_1_com), .NO(incbase1_1_q), .com_2(dpdt_1_com_2), .NO_2(incbase1_2_q));  // open: NC, NC_2
  DPDT dpdt_2 (
    .coil(IE), .com(dpdt_2_com), .NO(incbase1_3_q), .com_2(dpdt_2_com_2), .NO_2(incbase1_4_q));  // open: NC, NC_2
  DPDT dpdt_3 (
    .coil(IE), .com(dpdt_3_com), .NO(incbase1_5_q), .com_2(dpdt_3_com_2), .NO_2(incbase1_6_q));  // open: NC, NC_2
  DPDT dpdt_4 (
    .coil(IE), .com(dpdt_4_com), .NO(incbase1_7_q), .com_2(dpdt_4_com_2), .NO_2(incbase1_8_q));  // open: NC, NC_2
  DPDT dpdt_5 (
    .coil(IE), .com(dpdt_5_com), .NO(incbase1_9_q), .com_2(dpdt_5_com_2), .NO_2(incbase1_10_q));  // open: NC, NC_2
  DPDT dpdt_6 (
    .coil(IE), .com(dpdt_6_com), .NO(incbase1_11_q), .com_2(dpdt_6_com_2), .NO_2(incbase1_12_q));  // open: NC, NC_2
  DPDT dpdt_7 (
    .coil(IE), .com(dpdt_7_com), .NO(incbase1_13_q), .com_2(dpdt_7_com_2), .NO_2(incbase1_14_q));  // open: NC, NC_2
  DPDT dpdt_8 (
    .coil(IE), .com(dpdt_8_com), .NO(incbase1_15_q), .com_2(dpdt_8_com_2), .NO_2(incbase1_16_q));  // open: NC, NC_2
  buf buffer_1 (buffer_1_out, dpdt_1_com);
  buf buffer_2 (buffer_2_out, dpdt_1_com_2);
  buf buffer_3 (buffer_3_out, dpdt_2_com);
  buf buffer_4 (buffer_4_out, dpdt_2_com_2);
  buf buffer_5 (buffer_5_out, dpdt_3_com);
  buf buffer_6 (buffer_6_out, dpdt_3_com_2);
  buf buffer_7 (buffer_7_out, dpdt_4_com);
  buf buffer_8 (buffer_8_out, dpdt_4_com_2);
  buf buffer_9 (buffer_9_out, dpdt_5_com);
  buf buffer_10 (buffer_10_out, dpdt_5_com_2);
  buf buffer_11 (buffer_11_out, dpdt_6_com);
  buf buffer_12 (buffer_12_out, dpdt_6_com_2);
  buf buffer_13 (buffer_13_out, dpdt_7_com);
  buf buffer_14 (buffer_14_out, dpdt_7_com_2);
  buf buffer_15 (buffer_15_out, dpdt_8_com);
  buf buffer_16 (buffer_16_out, dpdt_8_com_2);
  DPDTh dpdth_1 (.coil(buffer_2_out), .NO(Hold), .NO_2(OE), .com(R[1]), .com_2(B[1]));  // open: NC, NC_2
  DPDTh dpdth_2 (.coil(buffer_4_out), .NO(Hold), .NO_2(OE), .com(R[3]), .com_2(B[3]));  // open: NC, NC_2
  DPDTh dpdth_3 (.coil(buffer_6_out), .NO(Hold), .NO_2(OE), .com(R[5]), .com_2(B[5]));  // open: NC, NC_2
  DPDTh dpdth_4 (.coil(buffer_8_out), .NO(Hold), .NO_2(OE), .com(R[7]), .com_2(B[7]));  // open: NC, NC_2
  DPDTh dpdth_5 (.coil(buffer_10_out), .NO(Hold), .NO_2(OE), .com(R[9]), .com_2(B[9]));  // open: NC, NC_2
  DPDTh dpdth_6 (.coil(buffer_12_out), .NO(Hold), .NO_2(OE), .com(R[11]), .com_2(B[11]));  // open: NC, NC_2
  DPDTh dpdth_7 (.coil(buffer_14_out), .NO(Hold), .NO_2(OE), .com(R[13]), .com_2(B[13]));  // open: NC, NC_2
  DPDTh dpdth_8 (.coil(buffer_16_out), .NO(Hold), .NO_2(OE), .com(R[15]), .com_2(B[15]));  // open: NC, NC_2
  DPDTh dpdth_9 (.coil(buffer_1_out), .NO(Hold), .NO_2(OE), .com(R[0]), .com_2(B[0]));  // open: NC, NC_2
  DPDTh dpdth_10 (.coil(buffer_3_out), .NO(Hold), .NO_2(OE), .com(R[2]), .com_2(B[2]));  // open: NC, NC_2
  DPDTh dpdth_11 (.coil(buffer_5_out), .NO(Hold), .NO_2(OE), .com(R[4]), .com_2(B[4]));  // open: NC, NC_2
  DPDTh dpdth_12 (.coil(buffer_7_out), .NO(Hold), .NO_2(OE), .com(R[6]), .com_2(B[6]));  // open: NC, NC_2
  DPDTh dpdth_13 (.coil(buffer_9_out), .NO(Hold), .NO_2(OE), .com(R[8]), .com_2(B[8]));  // open: NC, NC_2
  DPDTh dpdth_14 (.coil(buffer_11_out), .NO(Hold), .NO_2(OE), .com(R[10]), .com_2(B[10]));  // open: NC, NC_2
  DPDTh dpdth_15 (.coil(buffer_13_out), .NO(Hold), .NO_2(OE), .com(R[12]), .com_2(B[12]));  // open: NC, NC_2
  DPDTh dpdth_16 (.coil(buffer_15_out), .NO(Hold), .NO_2(OE), .com(R[14]), .com_2(B[14]));  // open: NC, NC_2

  // Notes on the sheet:
  //   buffer_1 drives only 1 and floats otherwise
  //   buffer_2 drives only 1 and floats otherwise
  //   buffer_3 drives only 1 and floats otherwise
  //   buffer_4 drives only 1 and floats otherwise
  //   buffer_5 drives only 1 and floats otherwise
  //   buffer_6 drives only 1 and floats otherwise
  //   buffer_7 drives only 1 and floats otherwise
  //   buffer_8 drives only 1 and floats otherwise
  //   buffer_9 drives only 1 and floats otherwise
  //   buffer_10 drives only 1 and floats otherwise
  //   buffer_11 drives only 1 and floats otherwise
  //   buffer_12 drives only 1 and floats otherwise
  //   buffer_13 drives only 1 and floats otherwise
  //   buffer_14 drives only 1 and floats otherwise
  //   buffer_15 drives only 1 and floats otherwise
  //   buffer_16 drives only 1 and floats otherwise
endmodule

module INCBase1 (
  input  I,
  input  Cin,
  output Q,
  output Cout
);

  wire dpdtr_1_nc, dpdtr_1_no;

  DPDTr dpdtr_1 (.coil(Cin), .com(1'b1), .NC(dpdtr_1_nc), .NO(dpdtr_1_no));  // open: com_2, NC_2, NO_2
  DPDT dpdt_1 (.coil(I), .com(Cout), .NO(Cin), .NC_2(dpdtr_1_no), .com_2(Q), .NO_2(dpdtr_1_nc));  // open: NC
endmodule

// INPUT SEL
module InputSelect (
  input  [15:0] I0,
  input  [15:0] I1,
  input  EN0,
  input  EN1,
  output [15:0] A
);

  wire dpdt_1_com, dpdt_1_com_2, dpdt_2_com, dpdt_2_com_2, dpdt_3_com, dpdt_3_com_2, dpdt_4_com,
       dpdt_4_com_2, dpdt_5_com, dpdt_5_com_2, dpdt_6_com, dpdt_6_com_2, dpdt_7_com, dpdt_7_com_2,
       dpdt_8_com, dpdt_8_com_2, dpdt_9_com, dpdt_9_com_2, dpdt_10_com, dpdt_10_com_2, dpdt_11_com,
       dpdt_11_com_2, dpdt_12_com, dpdt_12_com_2, dpdt_13_com, dpdt_13_com_2, dpdt_14_com, dpdt_14_com_2,
       dpdt_15_com, dpdt_15_com_2, dpdt_16_com, dpdt_16_com_2;

  DPDT dpdt_1 (.coil(EN1), .com(dpdt_1_com), .NO(I1[0]), .com_2(dpdt_1_com_2), .NO_2(I1[1]));  // open: NC, NC_2
  DPDT dpdt_2 (.coil(EN1), .com(dpdt_2_com), .NO(I1[2]), .com_2(dpdt_2_com_2), .NO_2(I1[3]));  // open: NC, NC_2
  DPDT dpdt_3 (.coil(EN1), .com(dpdt_3_com), .NO(I1[4]), .com_2(dpdt_3_com_2), .NO_2(I1[5]));  // open: NC, NC_2
  DPDT dpdt_4 (.coil(EN1), .com(dpdt_4_com), .NO(I1[6]), .com_2(dpdt_4_com_2), .NO_2(I1[7]));  // open: NC, NC_2
  DPDT dpdt_5 (.coil(EN1), .com(dpdt_5_com), .NO(I1[8]), .com_2(dpdt_5_com_2), .NO_2(I1[9]));  // open: NC, NC_2
  DPDT dpdt_6 (.coil(EN1), .com(dpdt_6_com), .NO(I1[10]), .com_2(dpdt_6_com_2), .NO_2(I1[11]));  // open: NC, NC_2
  DPDT dpdt_7 (.coil(EN1), .com(dpdt_7_com), .NO(I1[12]), .com_2(dpdt_7_com_2), .NO_2(I1[13]));  // open: NC, NC_2
  DPDT dpdt_8 (.coil(EN1), .com(dpdt_8_com), .NO(I1[14]), .com_2(dpdt_8_com_2), .NO_2(I1[15]));  // open: NC, NC_2
  DPDT dpdt_9 (.coil(EN0), .com(dpdt_9_com), .NO(I0[0]), .com_2(dpdt_9_com_2), .NO_2(I0[1]));  // open: NC, NC_2
  DPDT dpdt_10 (.coil(EN0), .com(dpdt_10_com), .NO(I0[2]), .com_2(dpdt_10_com_2), .NO_2(I0[3]));  // open: NC, NC_2
  DPDT dpdt_11 (.coil(EN0), .com(dpdt_11_com), .NO(I0[4]), .com_2(dpdt_11_com_2), .NO_2(I0[5]));  // open: NC, NC_2
  DPDT dpdt_12 (.coil(EN0), .com(dpdt_12_com), .NO(I0[6]), .com_2(dpdt_12_com_2), .NO_2(I0[7]));  // open: NC, NC_2
  DPDT dpdt_13 (.coil(EN0), .com(dpdt_13_com), .NO(I0[8]), .com_2(dpdt_13_com_2), .NO_2(I0[9]));  // open: NC, NC_2
  DPDT dpdt_14 (.coil(EN0), .com(dpdt_14_com), .NO(I0[10]), .com_2(dpdt_14_com_2), .NO_2(I0[11]));  // open: NC, NC_2
  DPDT dpdt_15 (.coil(EN0), .com(dpdt_15_com), .NO(I0[12]), .com_2(dpdt_15_com_2), .NO_2(I0[13]));  // open: NC, NC_2
  DPDT dpdt_16 (.coil(EN0), .com(dpdt_16_com), .NO(I0[14]), .com_2(dpdt_16_com_2), .NO_2(I0[15]));  // open: NC, NC_2
  buf buffer_1 (A[0], dpdt_9_com);
  buf buffer_2 (A[1], dpdt_9_com_2);
  buf buffer_3 (A[0], dpdt_1_com);
  buf buffer_4 (A[1], dpdt_1_com_2);
  buf buffer_5 (A[2], dpdt_10_com);
  buf buffer_6 (A[3], dpdt_10_com_2);
  buf buffer_7 (A[2], dpdt_2_com);
  buf buffer_8 (A[3], dpdt_2_com_2);
  buf buffer_9 (A[4], dpdt_11_com);
  buf buffer_10 (A[5], dpdt_11_com_2);
  buf buffer_11 (A[4], dpdt_3_com);
  buf buffer_12 (A[5], dpdt_3_com_2);
  buf buffer_13 (A[6], dpdt_12_com);
  buf buffer_14 (A[7], dpdt_12_com_2);
  buf buffer_15 (A[6], dpdt_4_com);
  buf buffer_16 (A[7], dpdt_4_com_2);
  buf buffer_17 (A[8], dpdt_13_com);
  buf buffer_18 (A[9], dpdt_13_com_2);
  buf buffer_19 (A[8], dpdt_5_com);
  buf buffer_20 (A[9], dpdt_5_com_2);
  buf buffer_21 (A[10], dpdt_14_com);
  buf buffer_22 (A[11], dpdt_14_com_2);
  buf buffer_23 (A[10], dpdt_6_com);
  buf buffer_24 (A[11], dpdt_6_com_2);
  buf buffer_25 (A[12], dpdt_15_com);
  buf buffer_26 (A[13], dpdt_15_com_2);
  buf buffer_27 (A[12], dpdt_7_com);
  buf buffer_28 (A[13], dpdt_7_com_2);
  buf buffer_29 (A[14], dpdt_16_com);
  buf buffer_30 (A[15], dpdt_16_com_2);
  buf buffer_31 (A[14], dpdt_8_com);
  buf buffer_32 (A[15], dpdt_8_com_2);

  // Notes on the sheet:
  //   buffer_1 drives only 1 and floats otherwise
  //   buffer_2 drives only 1 and floats otherwise
  //   buffer_3 drives only 1 and floats otherwise
  //   buffer_4 drives only 1 and floats otherwise
  //   buffer_5 drives only 1 and floats otherwise
  //   buffer_6 drives only 1 and floats otherwise
  //   buffer_7 drives only 1 and floats otherwise
  //   buffer_8 drives only 1 and floats otherwise
  //   buffer_9 drives only 1 and floats otherwise
  //   buffer_10 drives only 1 and floats otherwise
  //   buffer_11 drives only 1 and floats otherwise
  //   buffer_12 drives only 1 and floats otherwise
  //   buffer_13 drives only 1 and floats otherwise
  //   buffer_14 drives only 1 and floats otherwise
  //   buffer_15 drives only 1 and floats otherwise
  //   buffer_16 drives only 1 and floats otherwise
  //   buffer_17 drives only 1 and floats otherwise
  //   buffer_18 drives only 1 and floats otherwise
  //   buffer_19 drives only 1 and floats otherwise
  //   buffer_20 drives only 1 and floats otherwise
  //   buffer_21 drives only 1 and floats otherwise
  //   buffer_22 drives only 1 and floats otherwise
  //   buffer_23 drives only 1 and floats otherwise
  //   buffer_24 drives only 1 and floats otherwise
  //   buffer_25 drives only 1 and floats otherwise
  //   buffer_26 drives only 1 and floats otherwise
  //   buffer_27 drives only 1 and floats otherwise
  //   buffer_28 drives only 1 and floats otherwise
  //   buffer_29 drives only 1 and floats otherwise
  //   buffer_30 drives only 1 and floats otherwise
  //   buffer_31 drives only 1 and floats otherwise
  //   buffer_32 drives only 1 and floats otherwise
endmodule

// INPUT SW
module InputSwitch (
  input  [15:0] I1,
  input  [15:0] I0,
  input  S1,
  output [15:0] O
);

  DPDT dpdt_1 (.coil(S1), .NC(I0[0]), .com(O[0]), .NO(I1[0]), .NC_2(I0[1]), .com_2(O[1]), .NO_2(I1[1]));
  DPDT dpdt_2 (.coil(S1), .NC(I0[2]), .com(O[2]), .NO(I1[2]), .NC_2(I0[3]), .com_2(O[3]), .NO_2(I1[3]));
  DPDT dpdt_3 (.coil(S1), .NC(I0[4]), .com(O[4]), .NO(I1[4]), .NC_2(I0[5]), .com_2(O[5]), .NO_2(I1[5]));
  DPDT dpdt_4 (.coil(S1), .NC(I0[6]), .com(O[6]), .NO(I1[6]), .NC_2(I0[7]), .com_2(O[7]), .NO_2(I1[7]));
  DPDT dpdt_5 (.coil(S1), .NC(I0[8]), .com(O[8]), .NO(I1[8]), .NC_2(I0[9]), .com_2(O[9]), .NO_2(I1[9]));
  DPDT dpdt_6 (.coil(S1), .NC(I0[10]), .com(O[10]), .NO(I1[10]), .NC_2(I0[11]), .com_2(O[11]), .NO_2(I1[11]));
  DPDT dpdt_7 (.coil(S1), .NC(I0[12]), .com(O[12]), .NO(I1[12]), .NC_2(I0[13]), .com_2(O[13]), .NO_2(I1[13]));
  DPDT dpdt_8 (.coil(S1), .NC(I0[14]), .com(O[14]), .NO(I1[14]), .NC_2(I0[15]), .com_2(O[15]), .NO_2(I1[15]));
endmodule

// BUS SEL
module BusSelect (
  input  [15:0] I1,
  input  SA,
  input  SB,
  output [15:0] A,
  output [15:0] B
);

  DPDT dpdt_1 (.coil(SB), .com(B[0]), .NO(I1[0]), .com_2(B[1]), .NO_2(I1[1]));  // open: NC, NC_2
  DPDT dpdt_2 (.coil(SB), .com(B[2]), .NO(I1[2]), .com_2(B[3]), .NO_2(I1[3]));  // open: NC, NC_2
  DPDT dpdt_3 (.coil(SB), .com(B[4]), .NO(I1[4]), .com_2(B[5]), .NO_2(I1[5]));  // open: NC, NC_2
  DPDT dpdt_4 (.coil(SB), .com(B[6]), .NO(I1[6]), .com_2(B[7]), .NO_2(I1[7]));  // open: NC, NC_2
  DPDT dpdt_5 (.coil(SB), .com(B[8]), .NO(I1[8]), .com_2(B[9]), .NO_2(I1[9]));  // open: NC, NC_2
  DPDT dpdt_6 (.coil(SB), .com(B[10]), .NO(I1[10]), .com_2(B[11]), .NO_2(I1[11]));  // open: NC, NC_2
  DPDT dpdt_7 (.coil(SB), .com(B[12]), .NO(I1[12]), .com_2(B[13]), .NO_2(I1[13]));  // open: NC, NC_2
  DPDT dpdt_8 (.coil(SB), .com(B[14]), .NO(I1[14]), .com_2(B[15]), .NO_2(I1[15]));  // open: NC, NC_2
  DPDT dpdt_9 (.coil(SA), .com(A[0]), .NO(I1[0]), .com_2(A[1]), .NO_2(I1[1]));  // open: NC, NC_2
  DPDT dpdt_10 (.coil(SA), .com(A[2]), .NO(I1[2]), .com_2(A[3]), .NO_2(I1[3]));  // open: NC, NC_2
  DPDT dpdt_11 (.coil(SA), .com(A[4]), .NO(I1[4]), .com_2(A[5]), .NO_2(I1[5]));  // open: NC, NC_2
  DPDT dpdt_12 (.coil(SA), .com(A[6]), .NO(I1[6]), .com_2(A[7]), .NO_2(I1[7]));  // open: NC, NC_2
  DPDT dpdt_13 (.coil(SA), .com(A[8]), .NO(I1[8]), .com_2(A[9]), .NO_2(I1[9]));  // open: NC, NC_2
  DPDT dpdt_14 (.coil(SA), .com(A[10]), .NO(I1[10]), .com_2(A[11]), .NO_2(I1[11]));  // open: NC, NC_2
  DPDT dpdt_15 (.coil(SA), .com(A[12]), .NO(I1[12]), .com_2(A[13]), .NO_2(I1[13]));  // open: NC, NC_2
  DPDT dpdt_16 (.coil(SA), .com(A[14]), .NO(I1[14]), .com_2(A[15]), .NO_2(I1[15]));  // open: NC, NC_2
endmodule

// TRANS
module Transceiver (
  input  [15:0] I0,
  input  [15:0] I1,
  input  S0,
  input  S1,
  output [15:0] O0,
  output [15:0] O1
);

  DPDT dpdt_1 (.coil(S1), .com(O1[0]), .NO(I1[0]), .com_2(O1[1]), .NO_2(I1[1]));  // open: NC, NC_2
  DPDT dpdt_2 (.coil(S1), .com(O1[2]), .NO(I1[2]), .com_2(O1[3]), .NO_2(I1[3]));  // open: NC, NC_2
  DPDT dpdt_3 (.coil(S1), .com(O1[4]), .NO(I1[4]), .com_2(O1[5]), .NO_2(I1[5]));  // open: NC, NC_2
  DPDT dpdt_4 (.coil(S1), .com(O1[6]), .NO(I1[6]), .com_2(O1[7]), .NO_2(I1[7]));  // open: NC, NC_2
  DPDT dpdt_5 (.coil(S1), .com(O1[8]), .NO(I1[8]), .com_2(O1[9]), .NO_2(I1[9]));  // open: NC, NC_2
  DPDT dpdt_6 (.coil(S1), .com(O1[10]), .NO(I1[10]), .com_2(O1[11]), .NO_2(I1[11]));  // open: NC, NC_2
  DPDT dpdt_7 (.coil(S1), .com(O1[12]), .NO(I1[12]), .com_2(O1[13]), .NO_2(I1[13]));  // open: NC, NC_2
  DPDT dpdt_8 (.coil(S1), .com(O1[14]), .NO(I1[14]), .com_2(O1[15]), .NO_2(I1[15]));  // open: NC, NC_2
  DPDT dpdt_9 (.coil(S0), .com(O0[0]), .NO(I0[0]), .com_2(O0[1]), .NO_2(I0[1]));  // open: NC, NC_2
  DPDT dpdt_10 (.coil(S0), .com(O0[2]), .NO(I0[2]), .com_2(O0[3]), .NO_2(I0[3]));  // open: NC, NC_2
  DPDT dpdt_11 (.coil(S0), .com(O0[4]), .NO(I0[4]), .com_2(O0[5]), .NO_2(I0[5]));  // open: NC, NC_2
  DPDT dpdt_12 (.coil(S0), .com(O0[6]), .NO(I0[6]), .com_2(O0[7]), .NO_2(I0[7]));  // open: NC, NC_2
  DPDT dpdt_13 (.coil(S0), .com(O0[8]), .NO(I0[8]), .com_2(O0[9]), .NO_2(I0[9]));  // open: NC, NC_2
  DPDT dpdt_14 (.coil(S0), .com(O0[10]), .NO(I0[10]), .com_2(O0[11]), .NO_2(I0[11]));  // open: NC, NC_2
  DPDT dpdt_15 (.coil(S0), .com(O0[12]), .NO(I0[12]), .com_2(O0[13]), .NO_2(I0[13]));  // open: NC, NC_2
  DPDT dpdt_16 (.coil(S0), .com(O0[14]), .NO(I0[14]), .com_2(O0[15]), .NO_2(I0[15]));  // open: NC, NC_2
endmodule

// INST SPLIT
module Decoder (
  input  [15:0] I,
  output [1:0] Ty,
  output [2:0] Op,
  output [2:0] Ri,
  output [1:0] FN,
  output St,
  output [2:0] Rj,
  output [2:0] Rk,
  output [4:0] imm5,
  output [10:0] pfix11
);


  assign FN = I[7:6];
  assign imm5 = I[4:0];
  assign Op = I[13:11];
  assign pfix11 = I[10:0];
  assign Ri = I[10:8];
  assign Rj = I[5:3];
  assign Rk = I[2:0];
  assign St = I[5];
  assign Ty = I[15:14];
endmodule

// INSTDECODER
module InstDecoder (
  input  [2:0] Op,
  input  [1:0] Ty,
  input  [1:0] Fn_Ak,
  input  St,
  input  PH1,
  input  PH2,
  input  [2:0] Ri_CC,
  input  [2:0] Rk,
  input  [2:0] Rj,
  input  CLR1,
  input  CLR2,
  output SB_R7,
  output SB_R6,
  output SB_R5,
  output SB_R4,
  output [7:0] A_CC,
  output SB_R3,
  output SB_R2,
  output SB_R1,
  output SB_R0,
  output IE_R7,
  output IE_R6,
  output IE_R5,
  output IE_R4,
  output IE_R3,
  output IE_R2,
  output IE_R1,
  output IE_R0,
  output IE_D,
  output SA_R7,
  output WE_M,
  output SA_R6,
  output SA_R5,
  output SA_R4,
  output SA_R3,
  output S_BUS,
  output SA_R2,
  output S_IMM,
  output SA_R1,
  output SA_R0,
  output S_D,
  output S_P,
  output IE_MAR,
  output OE_M,
  output IE_LK,
  output A_WIT,
  output A_WIF,
  output A_C,
  output A_C1,
  output A_D6_plus,
  output A_D6_minus,
  output A_ZERO,
  output A_LDA,
  output A_LDB,
  output A_SELT,
  output A_SELF,
  output A_ADD,
  output A_SUB,
  output A_RSB,
  output A_AND,
  output A_OR,
  output A_XOR,
  output A_SR1,
  output A_SR4,
  output A_SL1,
  output A_SL4,
  output A_ROT1,
  output A_ROT4,
  output HLT,
  output IE_PFR,
  output WI_SR,
  output LPDM
);

  wire A_WISR, adc, add, adf, adt, \and , buffer_1_out, buffer_3_out, buffer_4_out, buffer_12_out,
       buffer_13_out, buffer_14_out, buffer_15_out, buffer_16_out, buffer_18_out, buffer_20_out,
       buffer_23_out, buffer_25_out, buffer_27_out, buffer_97_out, buffer_100_out, buffer_106_out,
       CLR_2_nc_2, CLR_nc_2, cmp, cpc, dac, dad, dpdth_5_com, dpdtr_1_nc, dpdtr_1_no, dpdtr_2_nc,
       dpdtr_2_nc_2, dpdtr_2_no, dpdtr_2_no_2, dpdtr_3_nc, dpdtr_3_no, dpdtr_4_nc, dpdtr_4_no, dpdtr_5_no,
       dpdtr_6_nc, dpdtr_6_nc_2, dpdtr_6_no, dpdtr_6_no_2, dpdtr_7_nc, dpdtr_7_nc_2, dpdtr_7_no,
       dpdtr_7_no_2, dpdtr_8_nc, dpdtr_8_nc_2, dpdtr_8_no, dpdtr_8_no_2, dpdtr_9_nc, dpdtr_9_nc_2,
       dpdtr_9_no, dpdtr_9_no_2, dpdtr_10_no, dpdtr_10_no_2, dpdtr_11_nc, dpdtr_12_nc, dpdtr_12_nc_2,
       dpdtr_12_no, dpdtr_12_no_2, dpdtr_21_nc, dpdtr_21_nc_2, dpdtr_21_no, dpdtr_21_no_2, dpdtr_22_no,
       dpdtr_22_no_2, dpdtr_24_nc, dpdtr_24_nc_2, dpdtr_24_no, dpdtr_25_nc, dpdtr_25_nc_2, dpdtr_25_no,
       dpdtr_25_no_2, dpdtr_26_nc, dpdtr_26_nc_2, dpdtr_26_no, dpdtr_26_no_2, dpdtr_27_nc, dpdtr_27_nc_2,
       dpdtr_27_no, dpdtr_27_no_2, dpdtr_28_nc, dpdtr_28_nc_2, dpdtr_28_no, dpdtr_28_no_2, dpdtr_29_nc,
       dpdtr_29_nc_2, dpdtr_29_no, dpdtr_29_no_2, dpdtr_30_nc, dpdtr_30_nc_2, dpdtr_30_no, dpdtr_30_no_2,
       dpdtr_32_nc, dpdtr_36_nc, dpdtr_40_nc, dpdtr_40_no, dpdtr_41_nc, dpdtr_41_nc_2, dpdtr_41_no,
       dpdtr_41_no_2, dpdtr_42_nc, dpdtr_42_no, dpdtr_45_nc_2, dpdtr_45_no, dsc, DST_Ri, hlt_t, lp, lp1, lp2,
       mov, mvl, next_no, nPH1_Ex, nPH2_Ex, nTy_00_2_no, nTy_00_2_no_2, op_000, op_001, op_011, \or , pfx,
       PH1CC, PH1TypeI, PH1TypeMLd, PH1TypeMSt, PH1TypeR, PH1TypeZPLd, PH1TypeZPSt, PH2Ldp1, PH2Ldp2, PH2Mem,
       PH2Reg, rl1, rl4, rmov, rr1, rr4, rsb, sbc, sbf, sbt, sef, sel, set, sl1, sl4, sr1, sr4, SRC_CC,
       SRC_Ri, SRC_Rj, SRC_Rk, SRC_Rkm, St_3_nc_2, sub, Ty_0_nc_2, Ty_0_no_2, Ty_1_2_nc, Ty_1_2_no, Ty_1_nc,
       Ty_1_no, undriven, undriven_2, undriven_3, undriven_4, undriven_5, \xor ;

  buf buffer_1 (buffer_1_out, CLR1);
  buf buffer_2 (IE_LK, mvl);
  buf buffer_3 (buffer_3_out, pfx);
  DPDTr dpdtr_1 (.coil(Ri_CC[2]), .com(SRC_CC), .NC(dpdtr_1_nc), .NO(dpdtr_1_no));  // open: com_2, NC_2, NO_2
  DPDTr dpdtr_2 (
    .coil(Ri_CC[2]), .com(DST_Ri), .com_2(SRC_Ri), .NC(dpdtr_2_nc), .NO(dpdtr_2_no), .NC_2(dpdtr_2_nc_2),
    .NO_2(dpdtr_2_no_2));
  DPDTr dpdtr_3 (.coil(Rj[2]), .com(SRC_Rj), .NC(dpdtr_3_nc), .NO(dpdtr_3_no));  // open: com_2, NC_2, NO_2
  buf buffer_4 (buffer_4_out, Ty[0]);
  buf buffer_5 (buffer_4_out, Ty[1]);
  DPDTr dpdtr_4 (.coil(Fn_Ak[1]), .com(PH1), .NC(dpdtr_4_nc), .NO(dpdtr_4_no));  // open: com_2, NC_2, NO_2
  buf buffer_6 (A_WIT, sbf);
  buf buffer_7 (A_WIT, hlt_t);
  buf buffer_8 (A_WIT, cpc);
  buf buffer_9 (A_WIT, adf);
  buf buffer_10 (A_WIT, pfx);
  buf buffer_11 (A_WIT, cmp);
  DPDTr CLR (.coil(buffer_1_out), .com_2(1'b1), .NC_2(CLR_nc_2));  // open: com, NC, NO, NO_2
  buf buffer_12 (buffer_12_out, pfx);
  buf buffer_13 (buffer_13_out, A_WISR);
  buf buffer_14 (buffer_14_out, lp1);
  buf buffer_15 (buffer_15_out, lp2);
  buf buffer_16 (buffer_16_out, Ty[0]);
  buf buffer_17 (buffer_16_out, Ty[1]);
  buf buffer_18 (buffer_18_out, Fn_Ak[0]);
  buf buffer_19 (buffer_18_out, Fn_Ak[1]);
  buf buffer_20 (buffer_20_out, Op[0]);
  buf buffer_21 (buffer_20_out, Op[1]);
  buf buffer_22 (buffer_20_out, Op[2]);
  DPDTr Ty_1 (.coil(Ty[1]), .com(nPH1_Ex), .NC(Ty_1_nc), .NO(Ty_1_no));  // open: com_2, NC_2, NO_2
  buf buffer_23 (buffer_23_out, Op[0]);
  buf buffer_24 (buffer_23_out, Op[2]);
  DPDTr dpdtr_5 (.coil(Op[1]), .com(nPH1_Ex), .NO(dpdtr_5_no));  // open: com_2, NC, NC_2, NO_2
  DPDTr Ty_1_2 (.coil(Ty[1]), .com(nPH2_Ex), .NC(Ty_1_2_nc), .NO(Ty_1_2_no));  // open: com_2, NC_2, NO_2
  DPDTr dpdtr_6 (
    .coil(Ri_CC[1]), .com(dpdtr_1_no), .com_2(dpdtr_1_nc), .NC(dpdtr_6_nc), .NO(dpdtr_6_no),
    .NC_2(dpdtr_6_nc_2), .NO_2(dpdtr_6_no_2));
  DPDTr dpdtr_7 (
    .coil(Ri_CC[1]), .com(dpdtr_2_no), .com_2(dpdtr_2_nc), .NC(dpdtr_7_nc), .NO(dpdtr_7_no),
    .NC_2(dpdtr_7_nc_2), .NO_2(dpdtr_7_no_2));
  DPDTr dpdtr_8 (
    .coil(Ri_CC[1]), .com(dpdtr_2_no_2), .com_2(dpdtr_2_nc_2), .NC(dpdtr_8_nc), .NO(dpdtr_8_no),
    .NC_2(dpdtr_8_nc_2), .NO_2(dpdtr_8_no_2));
  DPDTr dpdtr_9 (
    .coil(Rj[1]), .com(dpdtr_3_no), .com_2(dpdtr_3_nc), .NC(dpdtr_9_nc), .NO(dpdtr_9_no),
    .NC_2(dpdtr_9_nc_2), .NO_2(dpdtr_9_no_2));
  buf buffer_25 (buffer_25_out, Ty[0]);
  buf buffer_26 (buffer_25_out, Ty[1]);
  buf buffer_27 (buffer_27_out, Ty[0]);
  buf buffer_28 (buffer_27_out, Ty[1]);
  buf buffer_29 (buffer_27_out, Fn_Ak[0]);
  buf buffer_30 (buffer_27_out, Fn_Ak[1]);
  buf buffer_31 (A_WISR, sbf);
  buf buffer_32 (A_WISR, mvl);
  buf buffer_33 (A_WISR, sel);
  buf buffer_34 (A_WIF, hlt_t);
  buf buffer_35 (A_WISR, hlt_t);
  buf buffer_36 (A_WISR, sbt);
  buf buffer_37 (A_WIF, sbt);
  buf buffer_38 (A_WISR, sef);
  buf buffer_39 (A_WIF, cpc);
  buf buffer_40 (A_WISR, adf);
  buf buffer_41 (A_WISR, set);
  buf buffer_42 (A_WISR, pfx);
  buf buffer_43 (A_WIF, pfx);
  buf buffer_44 (A_WISR, adt);
  buf buffer_45 (A_WIF, adt);
  buf buffer_46 (A_WIF, cmp);
  buf buffer_47 (A_WISR, rmov);
  buf buffer_48 (A_WISR, mov);
  buf buffer_49 (A_WISR, lp);
  DPDTr dpdtr_10 (
    .coil(buffer_20_out), .com(PH1), .com_2(PH2), .NO(dpdtr_10_no), .NO_2(dpdtr_10_no_2));  // open: NC, NC_2
  DPDTr Ty_0 (
    .coil(Ty[0]), .com(Ty_1_no), .com_2(Ty_1_nc), .NC(PH1TypeR), .NO(PH1TypeI), .NC_2(Ty_0_nc_2),
    .NO_2(Ty_0_no_2));
  DPDTr dpdtr_11 (.coil(buffer_23_out), .com(dpdtr_5_no), .NC(dpdtr_11_nc));  // open: com_2, NO, NC_2, NO_2
  buf buffer_50 (SRC_CC, PH1CC);
  buf buffer_51 (SRC_Ri, PH1TypeI);
  buf buffer_52 (S_IMM, PH1TypeI);
  buf buffer_53 (SRC_Rj, PH1TypeR);
  buf buffer_54 (SRC_Rk, PH1TypeR);
  buf buffer_55 (S_BUS, PH1TypeR);
  buf buffer_56 (SRC_Ri, PH1TypeZPSt);
  buf buffer_57 (S_D, PH1TypeZPSt);
  buf buffer_58 (IE_MAR, PH1TypeZPSt);
  buf buffer_59 (OE_M, PH1TypeZPSt);
  buf buffer_60 (SRC_Ri, PH1TypeZPLd);
  buf buffer_61 (S_D, PH1TypeZPLd);
  buf buffer_62 (IE_MAR, PH1TypeZPLd);
  buf buffer_63 (OE_M, PH1TypeZPLd);
  buf buffer_64 (SRC_Ri, PH1TypeMSt);
  buf buffer_65 (S_D, PH1TypeMSt);
  buf buffer_66 (SRC_Rkm, PH1TypeMSt);
  buf buffer_67 (IE_MAR, PH1TypeMSt);
  buf buffer_68 (OE_M, PH1TypeMSt);
  buf buffer_69 (SRC_Ri, PH1TypeMLd);
  buf buffer_70 (S_D, PH1TypeMLd);
  buf buffer_71 (SRC_Rkm, PH1TypeMLd);
  buf buffer_72 (IE_MAR, PH1TypeMLd);
  buf buffer_73 (OE_M, PH1TypeMLd);
  DPDTr dpdtr_12 (
    .coil(buffer_4_out), .com(dpdtr_4_no), .com_2(dpdtr_4_nc), .NC(dpdtr_12_nc), .NO(dpdtr_12_no),
    .NC_2(dpdtr_12_nc_2), .NO_2(dpdtr_12_no_2));
  buf buffer_74 (dpdtr_12_no_2, dpdtr_12_nc);
  buf buffer_75 (dpdtr_12_no_2, dpdtr_12_nc_2);
  DPDTr nTy_00 (.coil(buffer_25_out), .com(op_000), .com_2(op_001), .NC(pfx), .NO(sr1), .NC_2(hlt_t), .NO_2(sl1));
  DPDTr next (.coil(buffer_27_out), .com(op_011), .NC(lp), .NO(next_no));  // open: com_2, NC_2, NO_2
  buf buffer_76 (A_C, dsc);
  buf buffer_77 (A_C, dac);
  buf buffer_78 (A_C, sbc);
  buf buffer_79 (A_C, adc);
  buf buffer_80 (A_C, cpc);
  buf buffer_81 (A_C1, rsb);
  buf buffer_82 (A_C1, sub);
  buf buffer_83 (A_C1, cmp);
  DPDTh dpdth_1 (.coil(buffer_12_out), .NO(CLR_nc_2), .NO_2(PH2), .com_2(IE_PFR));  // open: NC, NC_2, com
  DPDTh dpdth_2 (.coil(buffer_13_out), .NO(CLR_nc_2), .NO_2(1'b1), .com_2(WI_SR));  // open: NC, NC_2, com
  DPDTh dpdth_3 (.coil(buffer_14_out), .NO(CLR_nc_2), .NO_2(PH2), .com_2(PH2Ldp1));  // open: NC, NC_2, com
  DPDTh dpdth_4 (.coil(buffer_15_out), .NO(CLR_nc_2), .NO_2(PH2), .com_2(PH2Ldp2));  // open: NC, NC_2, com
  DPDTr dpdtr_13 (
    .coil(Ri_CC[0]), .com(dpdtr_6_no), .com_2(dpdtr_6_nc), .NC(A_CC[6]), .NO(A_CC[7]), .NC_2(A_CC[4]),
    .NO_2(A_CC[5]));
  DPDTr dpdtr_14 (
    .coil(Ri_CC[0]), .com(dpdtr_6_no_2), .com_2(dpdtr_6_nc_2), .NC(A_CC[2]), .NO(A_CC[3]), .NC_2(A_CC[0]),
    .NO_2(A_CC[1]));
  DPDTr dpdtr_15 (
    .coil(Ri_CC[0]), .com(dpdtr_7_no), .com_2(dpdtr_7_nc), .NC(IE_R6), .NO(IE_R7), .NC_2(IE_R4), .NO_2(IE_R5));
  DPDTr dpdtr_16 (
    .coil(Ri_CC[0]), .com(dpdtr_7_no_2), .com_2(dpdtr_7_nc_2), .NC(IE_R2), .NO(IE_R3), .NC_2(IE_R0),
    .NO_2(IE_R1));
  DPDTr dpdtr_17 (
    .coil(Ri_CC[0]), .com(dpdtr_8_no), .com_2(dpdtr_8_nc), .NC(SA_R6), .NO(SA_R7), .NC_2(SA_R4), .NO_2(SA_R5));
  DPDTr dpdtr_18 (
    .coil(Ri_CC[0]), .com(dpdtr_8_no_2), .com_2(dpdtr_8_nc_2), .NC(SA_R2), .NO(SA_R3), .NC_2(SA_R0),
    .NO_2(SA_R1));
  DPDTr dpdtr_19 (
    .coil(Rj[0]), .com(dpdtr_9_no), .com_2(dpdtr_9_nc), .NC(SA_R6), .NO(SA_R7), .NC_2(SA_R4), .NO_2(SA_R5));
  DPDTr dpdtr_20 (
    .coil(Rj[0]), .com(dpdtr_9_no_2), .com_2(dpdtr_9_nc_2), .NC(SA_R2), .NO(SA_R3), .NC_2(SA_R0), .NO_2(SA_R1));
  DPDTr dpdtr_21 (
    .coil(Fn_Ak[0]), .com(dpdtr_12_no), .com_2(dpdtr_12_no_2), .NC(dpdtr_21_nc), .NO(dpdtr_21_no),
    .NC_2(dpdtr_21_nc_2), .NO_2(dpdtr_21_no_2));
  DPDTr u_St (.coil(St), .com(next_no), .NC(mov), .NO(rmov));  // open: com_2, NC_2, NO_2
  buf buffer_84 (A_D6_plus, dac);
  buf buffer_85 (A_D6_plus, dad);
  DPDTr nTy_00_2 (
    .coil(buffer_16_out), .com(PH1), .com_2(PH2), .NO(nTy_00_2_no), .NO_2(nTy_00_2_no_2));  // open: NC, NC_2
  buf buffer_86 (nPH2_Ex, nTy_00_2_no_2);
  DPDTr dpdtr_22 (
    .coil(buffer_18_out), .com(dpdtr_10_no), .com_2(dpdtr_10_no_2), .NO(dpdtr_22_no), .NO_2(dpdtr_22_no_2));  // open: NC, NC_2
  buf buffer_87 (nPH2_Ex, dpdtr_22_no_2);
  DPDTr St_2 (
    .coil(St), .com(Ty_0_no_2), .com_2(Ty_0_nc_2), .NC(PH1TypeZPLd), .NO(PH1TypeZPSt), .NC_2(PH1TypeMLd),
    .NO_2(PH1TypeMSt));
  DPDTr dpdtr_23 (.coil(Fn_Ak[0]), .com(dpdtr_11_nc), .NC(PH1CC));  // open: com_2, NO, NC_2, NO_2
  DPDTr St_3 (.coil(St), .com_2(Ty_1_2_nc), .NC_2(St_3_nc_2), .NO_2(PH2Mem));  // open: com, NC, NO
  buf buffer_88 (PH2Reg, St_3_nc_2);
  buf buffer_89 (PH2Reg, Ty_1_2_no);
  buf buffer_90 (A_D6_minus, dsc);
  buf buffer_91 (A_D6_minus, dac);
  buf buffer_92 (A_ZERO, sef);
  buf buffer_93 (A_D6_minus, dad);
  buf buffer_94 (A_ZERO, set);
  buf buffer_95 (nPH1_Ex, nTy_00_2_no);
  buf buffer_96 (nPH1_Ex, dpdtr_22_no);
  buf buffer_97 (buffer_97_out, dpdtr_24_nc);
  DPDTr dpdtr_24 (
    .coil(buffer_4_out), .com(dpdtr_21_no_2), .com_2(dpdtr_21_nc_2), .NC(dpdtr_24_nc), .NO(dpdtr_24_no),
    .NC_2(dpdtr_24_nc_2), .NO_2(buffer_97_out));
  buf buffer_98 (buffer_97_out, dpdtr_24_nc_2);
  buf buffer_99 (A_LDA, rmov);
  buf buffer_100 (buffer_100_out, CLR2);
  DPDTr dpdtr_25 (
    .coil(Op[2]), .com(dpdtr_21_no), .com_2(dpdtr_21_nc), .NC(dpdtr_25_nc), .NO(dpdtr_25_no),
    .NC_2(dpdtr_25_nc_2), .NO_2(dpdtr_25_no_2));
  DPDTr dpdtr_26 (
    .coil(Op[2]), .com(dpdtr_24_no), .com_2(buffer_97_out), .NC(dpdtr_26_nc), .NO(dpdtr_26_no),
    .NC_2(dpdtr_26_nc_2), .NO_2(dpdtr_26_no_2));
  buf buffer_101 (A_LDB, mvl);
  buf buffer_102 (A_SELT, sel);
  buf buffer_103 (A_SELT, set);
  buf buffer_104 (A_LDB, mov);
  buf buffer_105 (A_LDB, lp);
  DPDTr CLR_2 (.coil(buffer_100_out), .com_2(1'b1), .NC_2(CLR_2_nc_2));  // open: com, NC, NO, NO_2
  buf buffer_106 (buffer_106_out, PH2Ldp1);
  DPDTr dpdtr_27 (
    .coil(Op[1]), .com(dpdtr_25_no), .com_2(dpdtr_25_nc), .NC(dpdtr_27_nc), .NO(dpdtr_27_no),
    .NC_2(dpdtr_27_nc_2), .NO_2(dpdtr_27_no_2));
  DPDTr dpdtr_28 (
    .coil(Op[1]), .com(dpdtr_25_no_2), .com_2(dpdtr_25_nc_2), .NC(dpdtr_28_nc), .NO(dpdtr_28_no),
    .NC_2(dpdtr_28_nc_2), .NO_2(dpdtr_28_no_2));
  DPDTr dpdtr_29 (
    .coil(Op[1]), .com(dpdtr_26_no), .com_2(dpdtr_26_nc), .NC(dpdtr_29_nc), .NO(dpdtr_29_no),
    .NC_2(dpdtr_29_nc_2), .NO_2(dpdtr_29_no_2));
  DPDTr dpdtr_30 (
    .coil(Op[1]), .com(dpdtr_26_no_2), .com_2(dpdtr_26_nc_2), .NC(dpdtr_30_nc), .NO(dpdtr_30_no),
    .NC_2(dpdtr_30_nc_2), .NO_2(dpdtr_30_no_2));
  buf buffer_107 (A_ADD, dac);
  buf buffer_108 (A_ADD, adc);
  buf buffer_109 (A_SELF, sef);
  buf buffer_110 (A_ADD, adf);
  buf buffer_111 (A_ADD, dad);
  buf buffer_112 (A_ADD, adt);
  buf buffer_113 (A_ADD, add);
  buf buffer_114 (A_SUB, sbf);
  buf buffer_115 (A_SUB, sbt);
  buf buffer_116 (A_SUB, sbc);
  buf buffer_117 (A_SUB, sub);
  buf buffer_118 (A_SUB, cmp);
  DPDTh dpdth_5 (.coil(buffer_106_out), .NO(CLR_2_nc_2), .com(dpdth_5_com));  // open: NC, NC_2, NO_2, com_2
  buf buffer_119 (DST_Ri, PH2Reg);
  buf buffer_120 (IE_D, PH2Mem);
  buf buffer_121 (WE_M, PH2Mem);
  buf buffer_122 (SRC_Rk, lp1);
  buf buffer_123 (S_BUS, lp1);
  buf buffer_124 (IE_R7, PH2Ldp1);
  buf buffer_125 (S_P, lp2);
  buf buffer_126 (S_BUS, lp2);
  buf buffer_127 (DST_Ri, PH2Ldp2);
  DPDTr dpdtr_31 (.coil(Op[0]), .com(dpdtr_27_no), .com_2(dpdtr_27_nc), .NC(mvl), .NO(sbf), .NC_2(dac), .NO_2(dsc));
  DPDTr dpdtr_32 (
    .coil(Op[0]), .com(dpdtr_27_no_2), .com_2(dpdtr_27_nc_2), .NC(dpdtr_32_nc), .NO(sel), .NC_2(rr4),
    .NO_2(rl4));
  DPDTr dpdtr_33 (.coil(Op[0]), .com(dpdtr_28_no), .com_2(dpdtr_28_nc), .NC(\xor ), .NO(sbt), .NC_2(adc), .NO_2(sbc));
  DPDTr dpdtr_34 (.coil(Op[0]), .com(dpdtr_28_no_2), .com_2(dpdtr_28_nc_2), .NC(cpc), .NO(sef), .NC_2(sr4), .NO_2(sl4));
  DPDTr dpdtr_35 (.coil(Op[0]), .com(dpdtr_29_no), .com_2(dpdtr_29_nc), .NC(\or ), .NO(adf), .NC_2(dad), .NO_2(rsb));
  DPDTr dpdtr_36 (
    .coil(Op[0]), .com(dpdtr_29_no_2), .com_2(dpdtr_29_nc_2), .NC(dpdtr_36_nc), .NO(set), .NC_2(rr1),
    .NO_2(rl1));
  DPDTr dpdtr_37 (.coil(Op[0]), .com(dpdtr_30_no), .com_2(dpdtr_30_nc), .NC(\and ), .NO(adt), .NC_2(add), .NO_2(sub));
  DPDTr dpdtr_38 (
    .coil(Op[0]), .com(dpdtr_30_no_2), .com_2(dpdtr_30_nc_2), .NC(cmp), .NO(op_011), .NC_2(op_000),
    .NO_2(op_001));
  buf buffer_128 (A_RSB, dsc);
  buf buffer_129 (A_RSB, rsb);
  buf buffer_130 (A_AND, \and );
  DPDTr dpdtr_39 (.coil(dpdth_5_com), .com(lp), .com_2(1'b1), .NC(lp1), .NO(lp2), .NO_2(LPDM));  // open: NC_2
  DPDTr dpdtr_40 (.coil(Rk[2]), .com(SRC_Rk), .NC(dpdtr_40_nc), .NO(dpdtr_40_no));  // open: com_2, NC_2, NO_2
  // Buffer buffer_131 has open pins: in=undriven, out=open
  // Buffer buffer_132 has open pins: in=undriven_2, out=open
  buf buffer_133 (A_OR, \or );
  // Buffer buffer_134 has open pins: in=undriven_3, out=open
  // Buffer buffer_135 has open pins: in=undriven_4, out=open
  buf buffer_136 (A_XOR, \xor );
  buf buffer_137 (A_SR1, rr1);
  buf buffer_138 (A_SR1, sr1);
  DPDTr dpdtr_41 (
    .coil(Rk[1]), .com(dpdtr_40_no), .com_2(dpdtr_40_nc), .NC(dpdtr_41_nc), .NO(dpdtr_41_no),
    .NC_2(dpdtr_41_nc_2), .NO_2(dpdtr_41_no_2));
  DPDTr dpdtr_42 (.coil(Fn_Ak[1]), .com(SRC_Rkm), .NC(dpdtr_42_nc), .NO(dpdtr_42_no));  // open: com_2, NC_2, NO_2
  // Buffer buffer_139 has open pins: in=undriven_5, out=open
  buf buffer_140 (A_SR4, rr4);
  buf buffer_141 (A_SR4, sr4);
  buf buffer_142 (A_SL1, rl1);
  buf buffer_143 (A_SL1, sl1);
  DPDTr dpdtr_43 (
    .coil(Rk[0]), .com(dpdtr_41_no), .com_2(dpdtr_41_nc), .NC(SB_R6), .NO(SB_R7), .NC_2(SB_R4), .NO_2(SB_R5));
  DPDTr dpdtr_44 (
    .coil(Rk[0]), .com(dpdtr_41_no_2), .com_2(dpdtr_41_nc_2), .NC(SB_R2), .NO(SB_R3), .NC_2(SB_R0),
    .NO_2(SB_R1));
  DPDTr dpdtr_45 (
    .coil(Fn_Ak[0]), .com(dpdtr_42_no), .com_2(dpdtr_42_nc), .NC(SB_R5), .NO(dpdtr_45_no),
    .NC_2(dpdtr_45_nc_2), .NO_2(SB_R4));
  buf buffer_144 (A_SL4, rl4);
  buf buffer_145 (A_SL4, sl4);
  buf buffer_146 (A_ROT4, rl4);
  buf buffer_147 (A_ROT4, rr4);
  buf buffer_148 (A_ROT1, rl1);
  buf buffer_149 (A_ROT1, rr1);
  buf buffer_150 (HLT, hlt_t);

  // Other names for the same wires on the sheet: DST_D = IE_D; DST_MAR = IE_MAR; DST_PC = IE_R7; Fn[1:0] = Fn_Ak;
  //   PH1Ldp1 = lp1; PH1Ldp2 = lp2; MEM_OE = OE_M; MEM_WE = WE_M; Oper[2:0] = Op; SRC_BUS = S_BUS; SRC_D = S_D;
  //   SRC_IMM = S_IMM; SRC_P = S_P; Type[1:0] = Ty

  // Notes on the sheet:
  //   buffer_1 drives only 1 and floats otherwise
  //   buffer_2 drives only 1 and floats otherwise
  //   buffer_3 drives only 1 and floats otherwise
  //   buffer_4 drives only 1 and floats otherwise
  //   buffer_5 drives only 1 and floats otherwise
  //   buffer_6 drives only 1 and floats otherwise
  //   buffer_7 drives only 1 and floats otherwise
  //   buffer_8 drives only 1 and floats otherwise
  //   buffer_9 drives only 1 and floats otherwise
  //   buffer_10 drives only 1 and floats otherwise
  //   buffer_11 drives only 1 and floats otherwise
  //   buffer_12 drives only 1 and floats otherwise
  //   buffer_13 drives only 1 and floats otherwise
  //   buffer_14 drives only 1 and floats otherwise
  //   buffer_15 drives only 1 and floats otherwise
  //   buffer_16 drives only 1 and floats otherwise
  //   buffer_17 drives only 1 and floats otherwise
  //   buffer_18 drives only 1 and floats otherwise
  //   buffer_19 drives only 1 and floats otherwise
  //   buffer_20 drives only 1 and floats otherwise
  //   buffer_21 drives only 1 and floats otherwise
  //   buffer_22 drives only 1 and floats otherwise
  //   buffer_23 drives only 1 and floats otherwise
  //   buffer_24 drives only 1 and floats otherwise
  //   buffer_25 drives only 1 and floats otherwise
  //   buffer_26 drives only 1 and floats otherwise
  //   buffer_27 drives only 1 and floats otherwise
  //   buffer_28 drives only 1 and floats otherwise
  //   buffer_29 drives only 1 and floats otherwise
  //   buffer_30 drives only 1 and floats otherwise
  //   buffer_31 drives only 1 and floats otherwise
  //   buffer_32 drives only 1 and floats otherwise
  //   buffer_33 drives only 1 and floats otherwise
  //   buffer_34 drives only 1 and floats otherwise
  //   buffer_35 drives only 1 and floats otherwise
  //   buffer_36 drives only 1 and floats otherwise
  //   buffer_37 drives only 1 and floats otherwise
  //   buffer_38 drives only 1 and floats otherwise
  //   buffer_39 drives only 1 and floats otherwise
  //   buffer_40 drives only 1 and floats otherwise
  //   buffer_41 drives only 1 and floats otherwise
  //   buffer_42 drives only 1 and floats otherwise
  //   buffer_43 drives only 1 and floats otherwise
  //   buffer_44 drives only 1 and floats otherwise
  //   buffer_45 drives only 1 and floats otherwise
  //   buffer_46 drives only 1 and floats otherwise
  //   buffer_47 drives only 1 and floats otherwise
  //   buffer_48 drives only 1 and floats otherwise
  //   buffer_49 drives only 1 and floats otherwise
  //   buffer_50 drives only 1 and floats otherwise
  //   buffer_51 drives only 1 and floats otherwise
  //   buffer_52 drives only 1 and floats otherwise
  //   buffer_53 drives only 1 and floats otherwise
  //   buffer_54 drives only 1 and floats otherwise
  //   buffer_55 drives only 1 and floats otherwise
  //   buffer_56 drives only 1 and floats otherwise
  //   buffer_57 drives only 1 and floats otherwise
  //   buffer_58 drives only 1 and floats otherwise
  //   buffer_59 drives only 1 and floats otherwise
  //   buffer_60 drives only 1 and floats otherwise
  //   buffer_61 drives only 1 and floats otherwise
  //   buffer_62 drives only 1 and floats otherwise
  //   buffer_63 drives only 1 and floats otherwise
  //   buffer_64 drives only 1 and floats otherwise
  //   buffer_65 drives only 1 and floats otherwise
  //   buffer_66 drives only 1 and floats otherwise
  //   buffer_67 drives only 1 and floats otherwise
  //   buffer_68 drives only 1 and floats otherwise
  //   buffer_69 drives only 1 and floats otherwise
  //   buffer_70 drives only 1 and floats otherwise
  //   buffer_71 drives only 1 and floats otherwise
  //   buffer_72 drives only 1 and floats otherwise
  //   buffer_73 drives only 1 and floats otherwise
  //   buffer_74 drives only 1 and floats otherwise
  //   buffer_75 drives only 1 and floats otherwise
  //   buffer_76 drives only 1 and floats otherwise
  //   buffer_77 drives only 1 and floats otherwise
  //   buffer_78 drives only 1 and floats otherwise
  //   buffer_79 drives only 1 and floats otherwise
  //   buffer_80 drives only 1 and floats otherwise
  //   buffer_81 drives only 1 and floats otherwise
  //   buffer_82 drives only 1 and floats otherwise
  //   buffer_83 drives only 1 and floats otherwise
  //   buffer_84 drives only 1 and floats otherwise
  //   buffer_85 drives only 1 and floats otherwise
  //   buffer_86 drives only 1 and floats otherwise
  //   buffer_87 drives only 1 and floats otherwise
  //   buffer_88 drives only 1 and floats otherwise
  //   buffer_89 drives only 1 and floats otherwise
  //   buffer_90 drives only 1 and floats otherwise
  //   buffer_91 drives only 1 and floats otherwise
  //   buffer_92 drives only 1 and floats otherwise
  //   buffer_93 drives only 1 and floats otherwise
  //   buffer_94 drives only 1 and floats otherwise
  //   buffer_95 drives only 1 and floats otherwise
  //   buffer_96 drives only 1 and floats otherwise
  //   buffer_97 drives only 1 and floats otherwise
  //   buffer_98 drives only 1 and floats otherwise
  //   buffer_99 drives only 1 and floats otherwise
  //   buffer_100 drives only 1 and floats otherwise
  //   buffer_101 drives only 1 and floats otherwise
  //   buffer_102 drives only 1 and floats otherwise
  //   buffer_103 drives only 1 and floats otherwise
  //   buffer_104 drives only 1 and floats otherwise
  //   buffer_105 drives only 1 and floats otherwise
  //   buffer_106 drives only 1 and floats otherwise
  //   buffer_107 drives only 1 and floats otherwise
  //   buffer_108 drives only 1 and floats otherwise
  //   buffer_109 drives only 1 and floats otherwise
  //   buffer_110 drives only 1 and floats otherwise
  //   buffer_111 drives only 1 and floats otherwise
  //   buffer_112 drives only 1 and floats otherwise
  //   buffer_113 drives only 1 and floats otherwise
  //   buffer_114 drives only 1 and floats otherwise
  //   buffer_115 drives only 1 and floats otherwise
  //   buffer_116 drives only 1 and floats otherwise
  //   buffer_117 drives only 1 and floats otherwise
  //   buffer_118 drives only 1 and floats otherwise
  //   buffer_119 drives only 1 and floats otherwise
  //   buffer_120 drives only 1 and floats otherwise
  //   buffer_121 drives only 1 and floats otherwise
  //   buffer_122 drives only 1 and floats otherwise
  //   buffer_123 drives only 1 and floats otherwise
  //   buffer_124 drives only 1 and floats otherwise
  //   buffer_125 drives only 1 and floats otherwise
  //   buffer_126 drives only 1 and floats otherwise
  //   buffer_127 drives only 1 and floats otherwise
  //   buffer_128 drives only 1 and floats otherwise
  //   buffer_129 drives only 1 and floats otherwise
  //   buffer_130 drives only 1 and floats otherwise
  //   buffer_131 drives only 1 and floats otherwise
  //   buffer_132 drives only 1 and floats otherwise
  //   buffer_133 drives only 1 and floats otherwise
  //   buffer_134 drives only 1 and floats otherwise
  //   buffer_135 drives only 1 and floats otherwise
  //   buffer_136 drives only 1 and floats otherwise
  //   buffer_137 drives only 1 and floats otherwise
  //   buffer_138 drives only 1 and floats otherwise
  //   buffer_139 drives only 1 and floats otherwise
  //   buffer_140 drives only 1 and floats otherwise
  //   buffer_141 drives only 1 and floats otherwise
  //   buffer_142 drives only 1 and floats otherwise
  //   buffer_143 drives only 1 and floats otherwise
  //   buffer_144 drives only 1 and floats otherwise
  //   buffer_145 drives only 1 and floats otherwise
  //   buffer_146 drives only 1 and floats otherwise
  //   buffer_147 drives only 1 and floats otherwise
  //   buffer_148 drives only 1 and floats otherwise
  //   buffer_149 drives only 1 and floats otherwise
  //   buffer_150 drives only 1 and floats otherwise
endmodule

// FLAGS
module AluFlags (
  input  [7:0] CC_8,
  input  S,
  input  nZ,
  input  Cx,
  input  C,
  output NT
);

  wire buffer_1_out, buffer_2_out, buffer_4_out, buffer_6_out, buffer_8_out, buffer_10_out, buffer_12_out,
       buffer_19_out, buffer_20_out, dpdt_2_com, dpdt_2_com_2, dpdtr_1_nc, dpdtr_1_nc_2, dpdtr_1_no,
       dpdtr_1_no_2, dpdtr_2_nc, dpdtr_2_nc_2, dpdtr_2_no, dpdtr_2_no_2, dpdtr_3_nc_2, dpdtr_3_no,
       dpdtr_4_nc, dpdtr_4_no_2;

  // Probe on CC_8[0]
  // Probe on CC_8[1]
  // Probe on CC_8[2]
  // Probe on CC_8[3]
  // Probe on CC_8[4]
  // Probe on CC_8[5]
  // Probe on CC_8[6]
  // Probe on CC_8[7]
  buf buffer_1 (buffer_1_out, CC_8[0]);
  buf buffer_2 (buffer_2_out, CC_8[0]);
  buf buffer_3 (buffer_1_out, CC_8[1]);
  buf buffer_4 (buffer_4_out, CC_8[1]);
  buf buffer_5 (buffer_1_out, CC_8[2]);
  buf buffer_6 (buffer_6_out, CC_8[2]);
  buf buffer_7 (buffer_1_out, CC_8[3]);
  buf buffer_8 (buffer_8_out, CC_8[3]);
  buf buffer_9 (buffer_1_out, CC_8[4]);
  buf buffer_10 (buffer_10_out, CC_8[4]);
  buf buffer_11 (buffer_1_out, CC_8[5]);
  buf buffer_12 (buffer_12_out, CC_8[5]);
  buf buffer_13 (buffer_1_out, CC_8[6]);
  buf buffer_14 (buffer_4_out, CC_8[6]);
  buf buffer_15 (buffer_6_out, CC_8[6]);
  buf buffer_16 (buffer_1_out, CC_8[7]);
  buf buffer_17 (buffer_4_out, CC_8[7]);
  buf buffer_18 (buffer_10_out, CC_8[7]);
  DPDT dpdt_1 (.coil(buffer_1_out), .NC(1'b1), .com(buffer_2_out));  // open: NO, NC_2, com_2, NO_2
  // Probe on buffer_2_out
  // Probe on buffer_4_out
  // Probe on buffer_6_out
  // Probe on buffer_8_out
  // Probe on buffer_10_out
  // Probe on buffer_12_out
  DPDTr dpdtr_1 (
    .coil(S), .com(buffer_10_out), .com_2(buffer_12_out), .NC(dpdtr_1_nc), .NO(dpdtr_1_no),
    .NC_2(dpdtr_1_nc_2), .NO_2(dpdtr_1_no_2));
  buf buffer_19 (buffer_19_out, dpdtr_1_no);
  buf buffer_20 (buffer_20_out, dpdtr_1_nc);
  buf buffer_21 (buffer_20_out, dpdtr_1_no_2);
  buf buffer_22 (buffer_19_out, dpdtr_1_nc_2);
  DPDTr dpdtr_2 (
    .coil(Cx), .com(buffer_20_out), .com_2(buffer_19_out), .NC(dpdtr_2_nc), .NO(dpdtr_2_no),
    .NC_2(dpdtr_2_nc_2), .NO_2(dpdtr_2_no_2));
  DPDTr dpdtr_3 (
    .coil(nZ), .com(buffer_2_out), .com_2(buffer_4_out), .NO(dpdtr_3_no), .NC_2(dpdtr_3_nc_2));  // open: NC, NO_2
  DPDTr dpdtr_4 (
    .coil(C), .com(buffer_6_out), .com_2(buffer_8_out), .NC(dpdtr_4_nc), .NO_2(dpdtr_4_no_2));  // open: NO, NC_2
  DPDT dpdt_2 (
    .coil(C), .NC(dpdtr_2_no), .com(dpdt_2_com), .NO(dpdtr_2_nc), .NC_2(dpdtr_2_nc_2), .com_2(dpdt_2_com_2),
    .NO_2(dpdtr_2_no_2));
  buf buffer_23 (NT, dpdtr_3_no);
  buf buffer_24 (NT, dpdtr_3_nc_2);
  buf buffer_25 (NT, dpdtr_4_nc);
  buf buffer_26 (NT, dpdtr_4_no_2);
  buf buffer_27 (NT, dpdt_2_com);
  buf buffer_28 (NT, dpdt_2_com_2);

  // Notes on the sheet:
  //   buffer_1 drives only 1 and floats otherwise
  //   buffer_2 drives only 1 and floats otherwise
  //   buffer_3 drives only 1 and floats otherwise
  //   buffer_4 drives only 1 and floats otherwise
  //   buffer_5 drives only 1 and floats otherwise
  //   buffer_6 drives only 1 and floats otherwise
  //   buffer_7 drives only 1 and floats otherwise
  //   buffer_8 drives only 1 and floats otherwise
  //   buffer_9 drives only 1 and floats otherwise
  //   buffer_10 drives only 1 and floats otherwise
  //   buffer_11 drives only 1 and floats otherwise
  //   buffer_12 drives only 1 and floats otherwise
  //   buffer_13 drives only 1 and floats otherwise
  //   buffer_14 drives only 1 and floats otherwise
  //   buffer_15 drives only 1 and floats otherwise
  //   buffer_16 drives only 1 and floats otherwise
  //   buffer_17 drives only 1 and floats otherwise
  //   buffer_18 drives only 1 and floats otherwise
  //   buffer_19 drives only 1 and floats otherwise
  //   buffer_20 drives only 1 and floats otherwise
  //   buffer_21 drives only 1 and floats otherwise
  //   buffer_22 drives only 1 and floats otherwise
  //   V
  //   /V
  //   buffer_23 drives only 1 and floats otherwise
  //   buffer_24 drives only 1 and floats otherwise
  //   buffer_25 drives only 1 and floats otherwise
  //   buffer_26 drives only 1 and floats otherwise
  //   buffer_27 drives only 1 and floats otherwise
  //   buffer_28 drives only 1 and floats otherwise
endmodule

// EA16
module ADD16 (
  input  [15:0] B,
  input  [15:0] Imm,
  output [15:0] Q
);

  wire addbase4bit_1_cout, addbase4bit_2_cout, addbase4bit_3_cout;

  ADDBase4bit addbase4bit_1 (.A(B[3:0]), .B(Imm[3:0]), .Q(Q[3:0]), .Cout(addbase4bit_1_cout));  // open: Cin
  ADDBase4bit addbase4bit_2 (.A(B[7:4]), .B(Imm[7:4]), .Q(Q[7:4]), .Cin(addbase4bit_1_cout), .Cout(addbase4bit_2_cout));
  ADDBase4bit addbase4bit_3 (
    .A(B[11:8]), .B(Imm[11:8]), .Q(Q[11:8]), .Cin(addbase4bit_2_cout), .Cout(addbase4bit_3_cout));
  ADDBase4bit addbase4bit_4 (.A(B[15:12]), .B(Imm[15:12]), .Q(Q[15:12]), .Cin(addbase4bit_3_cout));  // open: Cout
endmodule

// ADD1
module ADDBase1bit (
  input  B,
  input  A,
  input  Cin,
  output Cout,
  output Q
);

  wire dpdt_1_com, dpdt_1_com_2, dpdtr_1_nc, dpdtr_1_no, dpdtr_1_no_2, dpdtr_2_nc, dpdtr_2_no;

  DPDTr dpdtr_1 (
    .coil(A), .com(1'b1), .com_2(1'b1), .NC(dpdtr_1_nc), .NO(dpdtr_1_no), .NO_2(dpdtr_1_no_2));  // open: NC_2
  DPDT dpdt_1 (
    .coil(B), .NC(dpdtr_1_no), .com(dpdt_1_com), .NO(dpdtr_1_nc), .com_2(dpdt_1_com_2), .NO_2(dpdtr_1_no_2));  // open: NC_2
  DPDTr dpdtr_2 (.coil(Cin), .com(1'b1), .NC(dpdtr_2_nc), .NO(dpdtr_2_no));  // open: com_2, NC_2, NO_2
  DPDT dpdt_2 (
    .coil(dpdt_1_com), .NC(dpdt_1_com_2), .com(Cout), .NO(Cin), .NC_2(dpdtr_2_no), .com_2(Q),
    .NO_2(dpdtr_2_nc));
endmodule

// ADD4
module ADDBase4bit (
  input  [3:0] A,
  input  [3:0] B,
  input  Cin,
  output Cout,
  output [3:0] Q
);

  wire addbase1bit_1_cout, addbase1bit_2_cout, addbase1bit_3_cout;

  ADDBase1bit addbase1bit_1 (.B(B[0]), .A(A[0]), .Cin(Cin), .Cout(addbase1bit_1_cout), .Q(Q[0]));
  ADDBase1bit addbase1bit_2 (.B(B[1]), .A(A[1]), .Cin(addbase1bit_1_cout), .Cout(addbase1bit_2_cout), .Q(Q[1]));
  ADDBase1bit addbase1bit_3 (.B(B[2]), .A(A[2]), .Cin(addbase1bit_2_cout), .Cout(addbase1bit_3_cout), .Q(Q[2]));
  ADDBase1bit addbase1bit_4 (.B(B[3]), .A(A[3]), .Cin(addbase1bit_3_cout), .Cout(Cout), .Q(Q[3]));
endmodule
module SHIFT (
  input  SHR4,
  input  SHL4,
  input  SHR1,
  input  SHL1,
  input  ZERO,
  input  ROT4,
  input  ROT1,
  input  [15:0] K,
  input  [15:0] A,
  output Sh,
  output [15:0] O,
  output Csh
);

  wire buffer_1_out, dpdt_17_com_2, dpdt_18_com, dpdt_35_com, dpdt_35_com_2, dpdt_36_com, dpdt_36_com_2,
       dpdt_37_com, dpdt_37_com_2, dpdt_38_com, dpdt_38_com_2;

  buf buffer_1 (buffer_1_out, SHL4);
  buf buffer_2 (buffer_1_out, ZERO);
  buf buffer_3 (buffer_1_out, SHL1);
  buf buffer_4 (buffer_1_out, SHR1);
  buf buffer_5 (Sh, SHL1);
  buf buffer_6 (buffer_1_out, SHR4);
  buf buffer_7 (Sh, SHR1);
  buf buffer_8 (Sh, SHR4);
  buf buffer_9 (Sh, SHL4);
  DPDT dpdt_1 (.coil(buffer_1_out), .NC(A[0]), .com(O[0]), .NC_2(A[1]), .com_2(O[1]));  // open: NO, NO_2
  DPDT dpdt_2 (.coil(buffer_1_out), .NC(A[2]), .com(O[2]), .NC_2(A[3]), .com_2(O[3]));  // open: NO, NO_2
  DPDT dpdt_3 (.coil(buffer_1_out), .NC(A[4]), .com(O[4]), .NC_2(A[5]), .com_2(O[5]));  // open: NO, NO_2
  DPDT dpdt_4 (.coil(buffer_1_out), .NC(A[6]), .com(O[6]), .NC_2(A[7]), .com_2(O[7]));  // open: NO, NO_2
  DPDT dpdt_5 (.coil(buffer_1_out), .NC(A[8]), .com(O[8]), .NC_2(A[9]), .com_2(O[9]));  // open: NO, NO_2
  DPDT dpdt_6 (.coil(buffer_1_out), .NC(A[10]), .com(O[10]), .NC_2(A[11]), .com_2(O[11]));  // open: NO, NO_2
  DPDT dpdt_7 (.coil(buffer_1_out), .NC(A[12]), .com(O[12]), .NC_2(A[13]), .com_2(O[13]));  // open: NO, NO_2
  DPDT dpdt_8 (.coil(buffer_1_out), .NC(A[14]), .com(O[14]), .NC_2(A[15]), .com_2(O[15]));  // open: NO, NO_2
  DPDT dpdt_9 (.coil(ROT1), .com_2(O[0]), .NO_2(K[15]));  // open: NC, com, NO, NC_2
  DPDT dpdt_10 (.coil(SHL1), .com(O[1]), .NO(A[0]), .com_2(O[2]), .NO_2(A[1]));  // open: NC, NC_2
  DPDT dpdt_11 (.coil(SHL1), .com(O[3]), .NO(A[2]), .com_2(O[4]), .NO_2(A[3]));  // open: NC, NC_2
  DPDT dpdt_12 (.coil(SHL1), .com(O[5]), .NO(A[4]), .com_2(O[6]), .NO_2(A[5]));  // open: NC, NC_2
  DPDT dpdt_13 (.coil(SHL1), .com(O[7]), .NO(A[6]), .com_2(O[8]), .NO_2(A[7]));  // open: NC, NC_2
  DPDT dpdt_14 (.coil(SHL1), .com(O[9]), .NO(A[8]), .com_2(O[10]), .NO_2(A[9]));  // open: NC, NC_2
  DPDT dpdt_15 (.coil(SHL1), .com(O[11]), .NO(A[10]), .com_2(O[12]), .NO_2(A[11]));  // open: NC, NC_2
  DPDT dpdt_16 (.coil(SHL1), .com(O[13]), .NO(A[12]), .com_2(O[14]), .NO_2(A[13]));  // open: NC, NC_2
  DPDT dpdt_17 (.coil(SHL1), .com(O[15]), .NO(A[14]), .com_2(dpdt_17_com_2), .NO_2(A[15]));  // open: NC, NC_2
  DPDT dpdt_18 (.coil(SHR1), .com(dpdt_18_com), .NO(A[0]), .com_2(O[0]), .NO_2(A[1]));  // open: NC, NC_2
  DPDT dpdt_19 (.coil(SHR1), .com(O[1]), .NO(A[2]), .com_2(O[2]), .NO_2(A[3]));  // open: NC, NC_2
  DPDT dpdt_20 (.coil(SHR1), .com(O[3]), .NO(A[4]), .com_2(O[4]), .NO_2(A[5]));  // open: NC, NC_2
  DPDT dpdt_21 (.coil(SHR1), .com(O[5]), .NO(A[6]), .com_2(O[6]), .NO_2(A[7]));  // open: NC, NC_2
  DPDT dpdt_22 (.coil(SHR1), .com(O[7]), .NO(A[8]), .com_2(O[8]), .NO_2(A[9]));  // open: NC, NC_2
  DPDT dpdt_23 (.coil(SHR1), .com(O[9]), .NO(A[10]), .com_2(O[10]), .NO_2(A[11]));  // open: NC, NC_2
  DPDT dpdt_24 (.coil(SHR1), .com(O[11]), .NO(A[12]), .com_2(O[12]), .NO_2(A[13]));  // open: NC, NC_2
  DPDT dpdt_25 (.coil(SHR1), .com(O[13]), .NO(A[14]), .com_2(O[14]), .NO_2(A[15]));  // open: NC, NC_2
  DPDT dpdt_26 (.coil(ROT1), .com(O[15]), .NO(K[0]));  // open: NC, NC_2, com_2, NO_2
  buf buffer_10 (Csh, dpdt_18_com);
  buf buffer_11 (Csh, dpdt_17_com_2);
  DPDT dpdt_27 (.coil(ZERO), .com(O[0]), .NO(K[12]), .com_2(O[1]), .NO_2(K[13]));  // open: NC, NC_2
  DPDT dpdt_28 (.coil(ZERO), .com(O[2]), .NO(K[14]), .com_2(O[3]), .NO_2(K[15]));  // open: NC, NC_2
  DPDT dpdt_29 (.coil(SHL4), .com(O[4]), .NO(A[0]), .com_2(O[5]), .NO_2(A[1]));  // open: NC, NC_2
  DPDT dpdt_30 (.coil(SHL4), .com(O[6]), .NO(A[2]), .com_2(O[7]), .NO_2(A[3]));  // open: NC, NC_2
  DPDT dpdt_31 (.coil(SHL4), .com(O[8]), .NO(A[4]), .com_2(O[9]), .NO_2(A[5]));  // open: NC, NC_2
  DPDT dpdt_32 (.coil(SHL4), .com(O[10]), .NO(A[6]), .com_2(O[11]), .NO_2(A[7]));  // open: NC, NC_2
  DPDT dpdt_33 (.coil(SHL4), .com(O[12]), .NO(A[8]), .com_2(O[13]), .NO_2(A[9]));  // open: NC, NC_2
  DPDT dpdt_34 (.coil(SHL4), .com(O[14]), .NO(A[10]), .com_2(O[15]), .NO_2(A[11]));  // open: NC, NC_2
  DPDT dpdt_35 (.coil(SHL4), .com(dpdt_35_com), .NO(A[12]), .com_2(dpdt_35_com_2), .NO_2(A[13]));  // open: NC, NC_2
  DPDT dpdt_36 (.coil(SHL4), .com(dpdt_36_com), .NO(A[14]), .com_2(dpdt_36_com_2), .NO_2(A[15]));  // open: NC, NC_2
  DPDT dpdt_37 (.coil(SHR4), .com(dpdt_37_com), .NO(A[0]), .com_2(dpdt_37_com_2), .NO_2(A[1]));  // open: NC, NC_2
  DPDT dpdt_38 (.coil(SHR4), .com(dpdt_38_com), .NO(A[2]), .com_2(dpdt_38_com_2), .NO_2(A[3]));  // open: NC, NC_2
  DPDT dpdt_39 (.coil(SHR4), .com(O[0]), .NO(A[4]), .com_2(O[1]), .NO_2(A[5]));  // open: NC, NC_2
  DPDT dpdt_40 (.coil(SHR4), .com(O[2]), .NO(A[6]), .com_2(O[3]), .NO_2(A[7]));  // open: NC, NC_2
  DPDT dpdt_41 (.coil(SHR4), .com(O[4]), .NO(A[8]), .com_2(O[5]), .NO_2(A[9]));  // open: NC, NC_2
  DPDT dpdt_42 (.coil(SHR4), .com(O[6]), .NO(A[10]), .com_2(O[7]), .NO_2(A[11]));  // open: NC, NC_2
  DPDT dpdt_43 (.coil(SHR4), .com(O[8]), .NO(A[12]), .com_2(O[9]), .NO_2(A[13]));  // open: NC, NC_2
  DPDT dpdt_44 (.coil(SHR4), .com(O[10]), .NO(A[14]), .com_2(O[11]), .NO_2(A[15]));  // open: NC, NC_2
  DPDT dpdt_45 (.coil(ROT4), .com(O[12]), .NO(K[0]), .com_2(O[13]), .NO_2(K[1]));  // open: NC, NC_2
  DPDT dpdt_46 (.coil(ROT4), .com(O[14]), .NO(K[2]), .com_2(O[15]), .NO_2(K[3]));  // open: NC, NC_2
  buf buffer_12 (Csh, dpdt_37_com);
  buf buffer_13 (Csh, dpdt_37_com_2);
  buf buffer_14 (Csh, dpdt_38_com);
  buf buffer_15 (Csh, dpdt_38_com_2);
  buf buffer_16 (Csh, dpdt_35_com);
  buf buffer_17 (Csh, dpdt_35_com_2);
  buf buffer_18 (Csh, dpdt_36_com);
  buf buffer_19 (Csh, dpdt_36_com_2);

  // Notes on the sheet:
  //   buffer_1 drives only 1 and floats otherwise
  //   buffer_2 drives only 1 and floats otherwise
  //   buffer_3 drives only 1 and floats otherwise
  //   buffer_4 drives only 1 and floats otherwise
  //   buffer_5 drives only 1 and floats otherwise
  //   buffer_6 drives only 1 and floats otherwise
  //   buffer_7 drives only 1 and floats otherwise
  //   buffer_8 drives only 1 and floats otherwise
  //   buffer_9 drives only 1 and floats otherwise
  //   buffer_10 drives only 1 and floats otherwise
  //   buffer_11 drives only 1 and floats otherwise
  //   buffer_12 drives only 1 and floats otherwise
  //   buffer_13 drives only 1 and floats otherwise
  //   buffer_14 drives only 1 and floats otherwise
  //   buffer_15 drives only 1 and floats otherwise
  //   buffer_16 drives only 1 and floats otherwise
  //   buffer_17 drives only 1 and floats otherwise
  //   buffer_18 drives only 1 and floats otherwise
  //   buffer_19 drives only 1 and floats otherwise
endmodule

// 0/1
module Buffer1 (
  input  in_1,
  output out_2
);

  wire buffer_1_out;

  buf buffer_1 (buffer_1_out, in_1);
  Pull_Resistor pull_resistor_1 (.node(buffer_1_out));
  buf buffer_2 (out_2, buffer_1_out);

  // Notes on the sheet:
  //   buffer_1 drives only 1 and floats otherwise
endmodule

// 0/1
module Buffer16 (
  input  [15:0] in_1,
  output [15:0] out_2
);

  wire buffer_1_out, buffer_2_out, buffer_3_out, buffer_4_out, buffer_5_out, buffer_6_out, buffer_7_out,
       buffer_8_out, buffer_9_out, buffer_10_out, buffer_11_out, buffer_12_out, buffer_13_out, buffer_14_out,
       buffer_15_out, buffer_16_out;

  buf buffer_1 (buffer_1_out, in_1[0]);
  buf buffer_2 (buffer_2_out, in_1[2]);
  buf buffer_3 (buffer_3_out, in_1[4]);
  buf buffer_4 (buffer_4_out, in_1[6]);
  buf buffer_5 (buffer_5_out, in_1[8]);
  buf buffer_6 (buffer_6_out, in_1[10]);
  buf buffer_7 (buffer_7_out, in_1[12]);
  buf buffer_8 (buffer_8_out, in_1[14]);
  buf buffer_9 (buffer_9_out, in_1[1]);
  buf buffer_10 (buffer_10_out, in_1[3]);
  buf buffer_11 (buffer_11_out, in_1[5]);
  buf buffer_12 (buffer_12_out, in_1[7]);
  buf buffer_13 (buffer_13_out, in_1[9]);
  buf buffer_14 (buffer_14_out, in_1[11]);
  buf buffer_15 (buffer_15_out, in_1[13]);
  buf buffer_16 (buffer_16_out, in_1[15]);
  Pull_Resistor pull_resistor_1 (.node(buffer_3_out));
  Pull_Resistor pull_resistor_2 (.node(buffer_11_out));
  Pull_Resistor pull_resistor_3 (.node(buffer_10_out));
  Pull_Resistor pull_resistor_4 (.node(buffer_2_out));
  Pull_Resistor pull_resistor_5 (.node(buffer_1_out));
  Pull_Resistor pull_resistor_6 (.node(buffer_9_out));
  Pull_Resistor pull_resistor_7 (.node(buffer_12_out));
  Pull_Resistor pull_resistor_8 (.node(buffer_4_out));
  Pull_Resistor pull_resistor_9 (.node(buffer_5_out));
  Pull_Resistor pull_resistor_10 (.node(buffer_6_out));
  Pull_Resistor pull_resistor_11 (.node(buffer_14_out));
  Pull_Resistor pull_resistor_12 (.node(buffer_15_out));
  Pull_Resistor pull_resistor_13 (.node(buffer_7_out));
  Pull_Resistor pull_resistor_14 (.node(buffer_13_out));
  buf buffer_17 (out_2[0], buffer_1_out);
  buf buffer_18 (out_2[2], buffer_2_out);
  buf buffer_19 (out_2[4], buffer_3_out);
  buf buffer_20 (out_2[6], buffer_4_out);
  buf buffer_21 (out_2[8], buffer_5_out);
  buf buffer_22 (out_2[10], buffer_6_out);
  buf buffer_23 (out_2[12], buffer_7_out);
  buf buffer_24 (out_2[14], buffer_8_out);
  Pull_Resistor pull_resistor_15 (.node(buffer_8_out));
  Pull_Resistor pull_resistor_16 (.node(buffer_16_out));
  buf buffer_25 (out_2[1], buffer_9_out);
  buf buffer_26 (out_2[3], buffer_10_out);
  buf buffer_27 (out_2[5], buffer_11_out);
  buf buffer_28 (out_2[7], buffer_12_out);
  buf buffer_29 (out_2[9], buffer_13_out);
  buf buffer_30 (out_2[11], buffer_14_out);
  buf buffer_31 (out_2[13], buffer_15_out);
  buf buffer_32 (out_2[15], buffer_16_out);

  // Notes on the sheet:
  //   buffer_1 drives only 1 and floats otherwise
  //   buffer_2 drives only 1 and floats otherwise
  //   buffer_3 drives only 1 and floats otherwise
  //   buffer_4 drives only 1 and floats otherwise
  //   buffer_5 drives only 1 and floats otherwise
  //   buffer_6 drives only 1 and floats otherwise
  //   buffer_7 drives only 1 and floats otherwise
  //   buffer_8 drives only 1 and floats otherwise
  //   buffer_9 drives only 1 and floats otherwise
  //   buffer_10 drives only 1 and floats otherwise
  //   buffer_11 drives only 1 and floats otherwise
  //   buffer_12 drives only 1 and floats otherwise
  //   buffer_13 drives only 1 and floats otherwise
  //   buffer_14 drives only 1 and floats otherwise
  //   buffer_15 drives only 1 and floats otherwise
  //   buffer_16 drives only 1 and floats otherwise
endmodule
